// Logisim project cpu21-riscv.circ as structural Verilog: 18 circuits, main circuit ◇单周期+多级中断
// 单周期硬布线控制器
module \单周期硬布线控制器  (
  input  [4:0] OP,
  input  [4:0] Funct,
  input  IR,
  output [3:0] ALU_OP,
  output uret,
  output MemToReg,
  output ecall,
  output MemWrite,
  output ALU_SRC,
  output RegWrite,
  output S_type,
  output Beq,
  output Bne,
  output Jalr,
  output JAL,
  output Bge,
  output sb,
  output ALT,
  output IRD,
  output RsUsed,
  output LUI,
  output BLT,
  output IRE,
  output RtUsed
);

  wire \控制信号自动生成_1_ecall ;

  \运算控制器自动生成  \u_运算控制器自动生成_1  (
    .OP2(OP[0]), .OP3(OP[1]), .OP4(OP[2]), .OP5(OP[3]), .OP6(OP[4]), .F12(Funct[0]), .F13(Funct[1]),
    .F14(Funct[2]), .F25(Funct[3]), .F30(Funct[4]), .S0(ALU_OP[0]), .S1(ALU_OP[1]), .S2(ALU_OP[2]),
    .S3(ALU_OP[3]));
  \控制信号自动生成  \u_控制信号自动生成_1  (
    .OP2(OP[0]), .OP3(OP[1]), .MemToReg(MemToReg), .OP4(OP[2]), .OP5(OP[3]), .OP6(OP[4]), .F12(Funct[0]),
    .MemWrite(MemWrite), .F13(Funct[1]), .F14(Funct[2]), .F25(Funct[3]), .F30(Funct[4]), .ALU_SRC(ALU_SRC),
    .RegWrite(RegWrite), .ecall(\控制信号自动生成_1_ecall ), .S_Type(S_type), .BEQ(Beq), .BNE(Bne), .JALR(Jalr),
    .JAL(JAL), .BGE(Bge), .SB(sb), .ALT(ALT), .RsUsed(RsUsed), .RtUsed(RtUsed), .IRE(IRE), .IRD(IRD),
    .LUI(LUI), .BLT(BLT));
  and and_1 (uret, IR, \控制信号自动生成_1_ecall );
  and and_2 (ecall, ~IR, \控制信号自动生成_1_ecall );  // AND_Gate

  // Other names for the same wires on the sheet: IR21 = IR; OP_CODE[4:0] = OP

  // Notes on the sheet:
  //   运算器控制器，根据指令生成运算器功能选择信号
  //   控制信号生成，产生数据通路需要的其他控制信号
endmodule

// 运算器控制器
module \运算控制器自动生成  (
  input  OP2,
  input  OP3,
  input  OP4,
  input  OP5,
  input  OP6,
  input  F12,
  input  F13,
  input  F14,
  input  F25,
  input  F30,
  output S0,
  output S1,
  output S2,
  output S3
);

  wire and_1_out, and_2_out, and_3_out, and_4_out, and_5_out, and_6_out, and_7_out, and_8_out, and_9_out,
       and_10_out, and_11_out, and_12_out, and_13_out, and_14_out, and_15_out, and_16_out, and_17_out,
       and_18_out, and_19_out, and_20_out, and_21_out, and_22_out, and_23_out, and_24_out, and_25_out,
       and_26_out, and_27_out, and_28_out, and_29_out, and_30_out, and_31_out, and_32_out, and_33_out,
       and_34_out, and_35_out, and_36_out, and_37_out, and_38_out, and_39_out, and_40_out, and_41_out,
       and_42_out, and_43_out, and_44_out, and_45_out, and_46_out, not_1_out, not_2_out, not_3_out,
       not_4_out, not_5_out, not_6_out, not_7_out, not_8_out, not_9_out, not_10_out, not_11_out, not_12_out,
       not_13_out, not_14_out, not_15_out, not_16_out, not_17_out, not_18_out, not_19_out, not_20_out,
       not_21_out, not_22_out, not_23_out, not_24_out, not_25_out, not_26_out, not_27_out, not_28_out,
       not_29_out, not_30_out, not_31_out, not_32_out, not_33_out, not_34_out, not_35_out, not_36_out,
       not_37_out, not_38_out, not_39_out, not_40_out, not_41_out, not_42_out, not_43_out, not_44_out,
       not_45_out, not_46_out, not_47_out, not_48_out, not_49_out, not_50_out, not_51_out, not_52_out,
       not_53_out, not_54_out, not_55_out, not_56_out, not_57_out, not_58_out, not_59_out, not_60_out,
       not_61_out, not_62_out, not_63_out, not_64_out, not_65_out, not_66_out, not_67_out, not_68_out,
       not_69_out, not_70_out, not_71_out, not_72_out, not_73_out, not_74_out, not_75_out, not_76_out,
       not_77_out, not_78_out, not_79_out, not_80_out, not_81_out, not_82_out, not_83_out, not_84_out,
       not_85_out, not_86_out, not_87_out, not_88_out, not_89_out, not_90_out, not_91_out, not_92_out,
       not_93_out, not_94_out, not_95_out, not_96_out, not_97_out, not_98_out, not_99_out, not_100_out,
       not_101_out, not_102_out, not_103_out, not_104_out, not_105_out, not_106_out, not_107_out,
       not_108_out, not_109_out, not_110_out, not_111_out, not_112_out, not_113_out, not_114_out,
       not_115_out, not_116_out, not_117_out, not_118_out, not_119_out, not_120_out, not_121_out,
       not_122_out, not_123_out, not_124_out, not_125_out, not_126_out, not_127_out, not_128_out,
       not_129_out, not_130_out, not_131_out, not_132_out, not_133_out, not_134_out, not_135_out,
       not_136_out, not_137_out, not_138_out, not_139_out, not_140_out, not_141_out, not_142_out,
       not_143_out, not_144_out, not_145_out, not_146_out, not_147_out, not_148_out, not_149_out,
       not_150_out, not_151_out, not_152_out, not_153_out, not_154_out, not_155_out, not_156_out,
       not_157_out, not_158_out, not_159_out, not_160_out, not_161_out, not_162_out, not_163_out,
       not_164_out, not_165_out, not_166_out, not_167_out, not_168_out, not_169_out, not_170_out,
       not_171_out, not_172_out, not_173_out, not_174_out, not_175_out, not_176_out, not_177_out,
       not_178_out, not_179_out, not_180_out, not_181_out, not_182_out, not_183_out, not_184_out,
       not_185_out, not_186_out, not_187_out, not_188_out, not_189_out, not_190_out, not_191_out,
       not_192_out, not_193_out, not_194_out, not_195_out, not_196_out, not_197_out, not_198_out,
       not_199_out, not_200_out, not_201_out, not_202_out, not_203_out, not_204_out, not_205_out,
       not_206_out, not_207_out, not_208_out, not_209_out, not_210_out, not_211_out, not_212_out,
       not_213_out, not_214_out, not_215_out, not_216_out, not_217_out, not_218_out, not_219_out,
       not_220_out, not_221_out, not_222_out, not_223_out, not_224_out, not_225_out, not_226_out,
       not_227_out, not_228_out, not_229_out, not_230_out, not_231_out, not_232_out, not_233_out,
       not_234_out, not_235_out, not_236_out, not_237_out, not_238_out, not_239_out, not_240_out,
       not_241_out, not_242_out, not_243_out, not_244_out, not_245_out, not_246_out, not_247_out,
       not_248_out, not_249_out, not_250_out, not_251_out, not_252_out, not_253_out, not_254_out,
       not_255_out, not_256_out, not_257_out, not_258_out, not_259_out, not_260_out, not_261_out,
       not_262_out, not_263_out, not_264_out, not_265_out, not_266_out, not_267_out, not_268_out,
       not_269_out, not_270_out, not_271_out, not_272_out, not_273_out;

  not not_1 (not_1_out, F30);
  not not_2 (not_2_out, F25);
  not not_3 (not_3_out, F14);
  not not_4 (not_4_out, F13);
  not not_5 (not_5_out, F12);
  not not_6 (not_6_out, OP6);
  not not_7 (not_7_out, OP3);
  not not_8 (not_8_out, OP2);
  not not_9 (not_9_out, F30);
  not not_10 (not_10_out, F25);
  not not_11 (not_11_out, OP6);
  not not_12 (not_12_out, OP3);
  not not_13 (not_13_out, OP2);
  not not_14 (not_14_out, F30);
  not not_15 (not_15_out, F25);
  not not_16 (not_16_out, F14);
  not not_17 (not_17_out, F12);
  not not_18 (not_18_out, OP6);
  not not_19 (not_19_out, OP3);
  not not_20 (not_20_out, OP2);
  not not_21 (not_21_out, F14);
  not not_22 (not_22_out, F13);
  not not_23 (not_23_out, F12);
  not not_24 (not_24_out, OP6);
  not not_25 (not_25_out, OP5);
  not not_26 (not_26_out, OP3);
  not not_27 (not_27_out, OP2);
  not not_28 (not_28_out, OP6);
  not not_29 (not_29_out, OP5);
  not not_30 (not_30_out, OP3);
  not not_31 (not_31_out, OP2);
  not not_32 (not_32_out, F13);
  not not_33 (not_33_out, F12);
  not not_34 (not_34_out, OP6);
  not not_35 (not_35_out, OP5);
  not not_36 (not_36_out, OP3);
  not not_37 (not_37_out, OP2);
  not not_38 (not_38_out, F14);
  not not_39 (not_39_out, F12);
  not not_40 (not_40_out, OP6);
  not not_41 (not_41_out, OP5);
  not not_42 (not_42_out, OP3);
  not not_43 (not_43_out, OP2);
  not not_44 (not_44_out, F25);
  not not_45 (not_45_out, F13);
  not not_46 (not_46_out, OP6);
  not not_47 (not_47_out, OP5);
  not not_48 (not_48_out, OP3);
  not not_49 (not_49_out, OP2);
  not not_50 (not_50_out, F14);
  not not_51 (not_51_out, F12);
  not not_52 (not_52_out, OP6);
  not not_53 (not_53_out, OP5);
  not not_54 (not_54_out, OP4);
  not not_55 (not_55_out, OP3);
  not not_56 (not_56_out, OP2);
  not not_57 (not_57_out, F14);
  not not_58 (not_58_out, F12);
  not not_59 (not_59_out, OP6);
  not not_60 (not_60_out, OP4);
  not not_61 (not_61_out, OP3);
  not not_62 (not_62_out, OP2);
  not not_63 (not_63_out, F14);
  not not_64 (not_64_out, F13);
  not not_65 (not_65_out, F12);
  not not_66 (not_66_out, OP6);
  not not_67 (not_67_out, OP4);
  not not_68 (not_68_out, OP3);
  not not_69 (not_69_out, OP2);
  not not_70 (not_70_out, F13);
  not not_71 (not_71_out, OP4);
  not not_72 (not_72_out, OP3);
  not not_73 (not_73_out, OP2);
  not not_74 (not_74_out, F30);
  not not_75 (not_75_out, F25);
  not not_76 (not_76_out, F13);
  not not_77 (not_77_out, F12);
  not not_78 (not_78_out, OP6);
  not not_79 (not_79_out, OP3);
  not not_80 (not_80_out, OP2);
  not not_81 (not_81_out, F13);
  not not_82 (not_82_out, F12);
  not not_83 (not_83_out, OP4);
  not not_84 (not_84_out, OP3);
  not not_85 (not_85_out, OP2);
  not not_86 (not_86_out, F30);
  not not_87 (not_87_out, F14);
  not not_88 (not_88_out, F13);
  not not_89 (not_89_out, F12);
  not not_90 (not_90_out, OP6);
  not not_91 (not_91_out, OP3);
  not not_92 (not_92_out, OP2);
  not not_93 (not_93_out, F25);
  not not_94 (not_94_out, F14);
  not not_95 (not_95_out, F13);
  not not_96 (not_96_out, F12);
  not not_97 (not_97_out, OP6);
  not not_98 (not_98_out, OP3);
  not not_99 (not_99_out, OP2);
  not not_100 (not_100_out, F30);
  not not_101 (not_101_out, F25);
  not not_102 (not_102_out, OP6);
  not not_103 (not_103_out, OP3);
  not not_104 (not_104_out, OP2);
  not not_105 (not_105_out, F30);
  not not_106 (not_106_out, F25);
  not not_107 (not_107_out, F14);
  not not_108 (not_108_out, F12);
  not not_109 (not_109_out, OP6);
  not not_110 (not_110_out, OP3);
  not not_111 (not_111_out, OP2);
  not not_112 (not_112_out, OP6);
  not not_113 (not_113_out, OP5);
  not not_114 (not_114_out, OP3);
  not not_115 (not_115_out, OP2);
  not not_116 (not_116_out, F14);
  not not_117 (not_117_out, F12);
  not not_118 (not_118_out, OP6);
  not not_119 (not_119_out, OP5);
  not not_120 (not_120_out, OP3);
  not not_121 (not_121_out, OP2);
  not not_122 (not_122_out, F30);
  not not_123 (not_123_out, F25);
  not not_124 (not_124_out, F13);
  not not_125 (not_125_out, OP6);
  not not_126 (not_126_out, OP5);
  not not_127 (not_127_out, OP3);
  not not_128 (not_128_out, OP2);
  not not_129 (not_129_out, F13);
  not not_130 (not_130_out, OP4);
  not not_131 (not_131_out, OP3);
  not not_132 (not_132_out, OP2);
  not not_133 (not_133_out, F30);
  not not_134 (not_134_out, F25);
  not not_135 (not_135_out, F13);
  not not_136 (not_136_out, OP6);
  not not_137 (not_137_out, OP3);
  not not_138 (not_138_out, OP2);
  not not_139 (not_139_out, F13);
  not not_140 (not_140_out, F12);
  not not_141 (not_141_out, OP4);
  not not_142 (not_142_out, OP3);
  not not_143 (not_143_out, OP2);
  not not_144 (not_144_out, F30);
  not not_145 (not_145_out, F14);
  not not_146 (not_146_out, F13);
  not not_147 (not_147_out, F12);
  not not_148 (not_148_out, OP6);
  not not_149 (not_149_out, OP3);
  not not_150 (not_150_out, OP2);
  not not_151 (not_151_out, F30);
  not not_152 (not_152_out, F25);
  not not_153 (not_153_out, F14);
  not not_154 (not_154_out, F13);
  not not_155 (not_155_out, F12);
  not not_156 (not_156_out, OP6);
  not not_157 (not_157_out, OP3);
  not not_158 (not_158_out, OP2);
  not not_159 (not_159_out, F25);
  not not_160 (not_160_out, F14);
  not not_161 (not_161_out, F13);
  not not_162 (not_162_out, F12);
  not not_163 (not_163_out, OP6);
  not not_164 (not_164_out, OP3);
  not not_165 (not_165_out, OP2);
  not not_166 (not_166_out, F30);
  not not_167 (not_167_out, F25);
  not not_168 (not_168_out, OP6);
  not not_169 (not_169_out, OP3);
  not not_170 (not_170_out, OP2);
  not not_171 (not_171_out, F30);
  not not_172 (not_172_out, F25);
  not not_173 (not_173_out, F14);
  not not_174 (not_174_out, OP6);
  not not_175 (not_175_out, OP3);
  not not_176 (not_176_out, OP2);
  not not_177 (not_177_out, F14);
  not not_178 (not_178_out, F13);
  not not_179 (not_179_out, F12);
  not not_180 (not_180_out, OP6);
  not not_181 (not_181_out, OP5);
  not not_182 (not_182_out, OP3);
  not not_183 (not_183_out, OP2);
  not not_184 (not_184_out, OP6);
  not not_185 (not_185_out, OP5);
  not not_186 (not_186_out, OP3);
  not not_187 (not_187_out, OP2);
  not not_188 (not_188_out, F14);
  not not_189 (not_189_out, F12);
  not not_190 (not_190_out, OP6);
  not not_191 (not_191_out, OP5);
  not not_192 (not_192_out, OP4);
  not not_193 (not_193_out, OP3);
  not not_194 (not_194_out, OP2);
  not not_195 (not_195_out, F14);
  not not_196 (not_196_out, F12);
  not not_197 (not_197_out, OP6);
  not not_198 (not_198_out, OP4);
  not not_199 (not_199_out, OP3);
  not not_200 (not_200_out, OP2);
  not not_201 (not_201_out, F30);
  not not_202 (not_202_out, F13);
  not not_203 (not_203_out, OP6);
  not not_204 (not_204_out, OP3);
  not not_205 (not_205_out, OP2);
  not not_206 (not_206_out, F30);
  not not_207 (not_207_out, OP6);
  not not_208 (not_208_out, OP3);
  not not_209 (not_209_out, OP2);
  not not_210 (not_210_out, F14);
  not not_211 (not_211_out, F13);
  not not_212 (not_212_out, F12);
  not not_213 (not_213_out, OP6);
  not not_214 (not_214_out, OP4);
  not not_215 (not_215_out, OP3);
  not not_216 (not_216_out, OP2);
  not not_217 (not_217_out, F30);
  not not_218 (not_218_out, F12);
  not not_219 (not_219_out, OP6);
  not not_220 (not_220_out, OP3);
  not not_221 (not_221_out, OP2);
  not not_222 (not_222_out, F30);
  not not_223 (not_223_out, F25);
  not not_224 (not_224_out, F12);
  not not_225 (not_225_out, OP6);
  not not_226 (not_226_out, OP3);
  not not_227 (not_227_out, OP2);
  not not_228 (not_228_out, F30);
  not not_229 (not_229_out, F25);
  not not_230 (not_230_out, F14);
  not not_231 (not_231_out, F12);
  not not_232 (not_232_out, OP6);
  not not_233 (not_233_out, OP3);
  not not_234 (not_234_out, OP2);
  not not_235 (not_235_out, F30);
  not not_236 (not_236_out, F25);
  not not_237 (not_237_out, F14);
  not not_238 (not_238_out, OP6);
  not not_239 (not_239_out, OP3);
  not not_240 (not_240_out, OP2);
  not not_241 (not_241_out, F12);
  not not_242 (not_242_out, OP6);
  not not_243 (not_243_out, OP5);
  not not_244 (not_244_out, OP3);
  not not_245 (not_245_out, OP2);
  not not_246 (not_246_out, F13);
  not not_247 (not_247_out, F12);
  not not_248 (not_248_out, OP6);
  not not_249 (not_249_out, OP5);
  not not_250 (not_250_out, OP3);
  not not_251 (not_251_out, OP2);
  not not_252 (not_252_out, F14);
  not not_253 (not_253_out, F12);
  not not_254 (not_254_out, OP6);
  not not_255 (not_255_out, OP5);
  not not_256 (not_256_out, OP3);
  not not_257 (not_257_out, OP2);
  not not_258 (not_258_out, F13);
  not not_259 (not_259_out, OP4);
  not not_260 (not_260_out, OP3);
  not not_261 (not_261_out, OP2);
  not not_262 (not_262_out, F30);
  not not_263 (not_263_out, F25);
  not not_264 (not_264_out, F13);
  not not_265 (not_265_out, F12);
  not not_266 (not_266_out, OP6);
  not not_267 (not_267_out, OP3);
  not not_268 (not_268_out, OP2);
  not not_269 (not_269_out, F13);
  not not_270 (not_270_out, F12);
  not not_271 (not_271_out, OP4);
  not not_272 (not_272_out, OP3);
  not not_273 (not_273_out, OP2);
  and and_1 (and_1_out, not_1_out, not_2_out, not_3_out, not_4_out, not_5_out, not_6_out, OP5, OP4, not_7_out, not_8_out);
  and and_2 (and_2_out, not_9_out, not_10_out, F14, F13, F12, not_11_out, OP5, OP4, not_12_out, not_13_out);
  and and_3 (and_3_out, not_14_out, not_15_out, not_16_out, F13, not_17_out, not_18_out, OP5, OP4, not_19_out, not_20_out);
  and and_4 (and_4_out, not_21_out, not_22_out, not_23_out, not_24_out, not_25_out, OP4, not_26_out, not_27_out);
  and and_5 (and_5_out, F14, F13, F12, not_28_out, not_29_out, OP4, not_30_out, not_31_out);
  and and_6 (and_6_out, F14, not_32_out, not_33_out, not_34_out, not_35_out, OP4, not_36_out, not_37_out);
  and and_7 (and_7_out, not_38_out, F13, not_39_out, not_40_out, not_41_out, OP4, not_42_out, not_43_out);
  and and_8 (and_8_out, F30, not_44_out, F14, not_45_out, F12, not_46_out, not_47_out, OP4, not_48_out, not_49_out);
  and and_9 (and_9_out, not_50_out, F13, not_51_out, not_52_out, not_53_out, not_54_out, not_55_out, not_56_out);
  and and_10 (and_10_out, not_57_out, F13, not_58_out, not_59_out, OP5, not_60_out, not_61_out, not_62_out);
  and and_11 (and_11_out, not_63_out, not_64_out, not_65_out, not_66_out, OP5, not_67_out, not_68_out, not_69_out);
  and and_12 (and_12_out, F14, not_70_out, F12, OP6, OP5, not_71_out, not_72_out, not_73_out);
  and and_13 (and_13_out, not_74_out, not_75_out, F14, not_76_out, not_77_out, not_78_out, OP5, OP4, not_79_out, not_80_out);
  and and_14 (and_14_out, F14, not_81_out, not_82_out, OP6, OP5, not_83_out, not_84_out, not_85_out);
  and and_15 (and_15_out, not_86_out, F25, not_87_out, not_88_out, not_89_out, not_90_out, OP5, OP4, not_91_out, not_92_out);
  and and_16 (and_16_out, F30, not_93_out, not_94_out, not_95_out, not_96_out, not_97_out, OP5, OP4, not_98_out, not_99_out);
  and and_17 (and_17_out, not_100_out, not_101_out, F14, F13, F12, not_102_out, OP5, OP4, not_103_out, not_104_out);
  and and_18 (and_18_out, not_105_out, not_106_out, not_107_out, F13, not_108_out, not_109_out, OP5, OP4, not_110_out, not_111_out);
  and and_19 (and_19_out, F14, F13, F12, not_112_out, not_113_out, OP4, not_114_out, not_115_out);
  and and_20 (and_20_out, not_116_out, F13, not_117_out, not_118_out, not_119_out, OP4, not_120_out, not_121_out);
  and and_21 (and_21_out, not_122_out, not_123_out, F14, not_124_out, F12, not_125_out, not_126_out, OP4, not_127_out, not_128_out);
  and and_22 (and_22_out, F14, not_129_out, F12, OP6, OP5, not_130_out, not_131_out, not_132_out);
  and and_23 (and_23_out, not_133_out, not_134_out, F14, not_135_out, F12, not_136_out, OP5, OP4, not_137_out, not_138_out);
  and and_24 (and_24_out, F14, not_139_out, not_140_out, OP6, OP5, not_141_out, not_142_out, not_143_out);
  and and_25 (and_25_out, not_144_out, F25, not_145_out, not_146_out, not_147_out, not_148_out, OP5, OP4, not_149_out, not_150_out);
  and and_26 (and_26_out, not_151_out, not_152_out, not_153_out, not_154_out, not_155_out, not_156_out, OP5, OP4, not_157_out, not_158_out);
  and and_27 (and_27_out, F30, not_159_out, not_160_out, not_161_out, not_162_out, not_163_out, OP5, OP4, not_164_out, not_165_out);
  and and_28 (and_28_out, not_166_out, not_167_out, F14, F13, F12, not_168_out, OP5, OP4, not_169_out, not_170_out);
  and and_29 (and_29_out, not_171_out, not_172_out, not_173_out, F13, F12, not_174_out, OP5, OP4, not_175_out, not_176_out);
  and and_30 (and_30_out, not_177_out, not_178_out, not_179_out, not_180_out, not_181_out, OP4, not_182_out, not_183_out);
  and and_31 (and_31_out, F14, F13, F12, not_184_out, not_185_out, OP4, not_186_out, not_187_out);
  and and_32 (and_32_out, not_188_out, F13, not_189_out, not_190_out, not_191_out, not_192_out, not_193_out, not_194_out);
  and and_33 (and_33_out, not_195_out, F13, not_196_out, not_197_out, OP5, not_198_out, not_199_out, not_200_out);
  and and_34 (and_34_out, not_201_out, F25, F14, not_202_out, F12, not_203_out, OP5, OP4, not_204_out, not_205_out);
  and and_35 (and_35_out, not_206_out, F25, F14, F13, F12, not_207_out, OP5, OP4, not_208_out, not_209_out);
  and and_36 (and_36_out, not_210_out, not_211_out, not_212_out, not_213_out, OP5, not_214_out, not_215_out, not_216_out);
  and and_37 (and_37_out, not_217_out, F25, F14, F13, not_218_out, not_219_out, OP5, OP4, not_220_out, not_221_out);
  and and_38 (and_38_out, not_222_out, not_223_out, F14, F13, not_224_out, not_225_out, OP5, OP4, not_226_out, not_227_out);
  and and_39 (and_39_out, not_228_out, not_229_out, not_230_out, F13, not_231_out, not_232_out, OP5, OP4, not_233_out, not_234_out);
  and and_40 (and_40_out, not_235_out, not_236_out, not_237_out, F13, F12, not_238_out, OP5, OP4, not_239_out, not_240_out);
  and and_41 (and_41_out, F14, F13, not_241_out, not_242_out, not_243_out, OP4, not_244_out, not_245_out);
  and and_42 (and_42_out, F14, not_246_out, not_247_out, not_248_out, not_249_out, OP4, not_250_out, not_251_out);
  and and_43 (and_43_out, not_252_out, F13, not_253_out, not_254_out, not_255_out, OP4, not_256_out, not_257_out);
  and and_44 (and_44_out, F14, not_258_out, F12, OP6, OP5, not_259_out, not_260_out, not_261_out);
  and and_45 (and_45_out, not_262_out, not_263_out, F14, not_264_out, not_265_out, not_266_out, OP5, OP4, not_267_out, not_268_out);
  and and_46 (and_46_out, F14, not_269_out, not_270_out, OP6, OP5, not_271_out, not_272_out, not_273_out);
  or or_1 (S0, and_1_out, and_2_out, and_3_out, and_4_out, and_5_out, and_6_out, and_7_out, and_8_out, and_9_out, and_10_out, and_11_out, and_12_out, and_13_out, and_14_out, and_15_out);
  or or_2 (S1, and_16_out, and_17_out, and_18_out, and_19_out, and_20_out, and_21_out, and_22_out, and_23_out, and_24_out, and_25_out);
  or or_3 (S2, and_26_out, and_27_out, and_28_out, and_29_out, and_30_out, and_31_out, and_32_out, and_33_out, and_34_out, and_35_out, and_36_out, and_37_out);
  or or_4 (S3, and_38_out, and_39_out, and_40_out, and_41_out, and_42_out, and_43_out, and_44_out, and_45_out, and_46_out);
endmodule

// 控制信号生成
module \控制信号自动生成  (
  input  OP2,
  input  OP3,
  input  OP4,
  input  OP5,
  input  OP6,
  input  F12,
  input  F13,
  input  F14,
  input  F25,
  input  F30,
  output MemToReg,
  output MemWrite,
  output ALU_SRC,
  output RegWrite,
  output ecall,
  output S_Type,
  output BEQ,
  output BNE,
  output JALR,
  output JAL,
  output BGE,
  output SB,
  output ALT,
  output RsUsed,
  output RtUsed,
  output IRE,
  output IRD,
  output LUI,
  output BLT
);

  wire and_3_out, and_4_out, and_5_out, and_6_out, and_7_out, and_8_out, and_9_out, and_10_out, and_11_out,
       and_12_out, and_13_out, and_14_out, and_15_out, and_16_out, and_17_out, and_18_out, and_19_out,
       and_20_out, and_21_out, and_22_out, and_23_out, and_24_out, and_25_out, and_26_out, and_27_out,
       and_28_out, and_29_out, and_30_out, and_31_out, and_32_out, and_33_out, and_34_out, and_35_out,
       and_45_out, and_46_out, and_47_out, and_48_out, and_49_out, and_50_out, and_51_out, and_52_out,
       and_53_out, and_54_out, and_55_out, and_56_out, and_57_out, and_58_out, and_59_out, and_60_out,
       and_61_out, and_62_out, and_63_out, and_64_out, and_65_out, and_66_out, and_67_out, and_68_out,
       and_69_out, and_70_out, and_71_out, and_72_out, and_73_out, and_74_out, and_75_out, and_76_out,
       and_77_out, and_78_out, and_79_out, and_80_out, and_81_out, and_82_out, and_83_out, and_84_out,
       and_85_out, and_86_out, and_87_out, and_88_out, and_89_out, and_90_out, and_91_out, and_92_out,
       and_93_out, and_94_out, not_1_out, not_2_out, not_3_out, not_4_out, not_5_out, not_6_out, not_7_out,
       not_8_out, not_9_out, not_10_out, not_11_out, not_12_out, not_13_out, not_14_out, not_15_out,
       not_16_out, not_17_out, not_18_out, not_19_out, not_20_out, not_21_out, not_22_out, not_23_out,
       not_24_out, not_25_out, not_26_out, not_27_out, not_28_out, not_29_out, not_30_out, not_31_out,
       not_32_out, not_33_out, not_34_out, not_35_out, not_36_out, not_37_out, not_38_out, not_39_out,
       not_40_out, not_41_out, not_42_out, not_43_out, not_44_out, not_45_out, not_46_out, not_47_out,
       not_48_out, not_49_out, not_50_out, not_51_out, not_52_out, not_53_out, not_54_out, not_55_out,
       not_56_out, not_57_out, not_58_out, not_59_out, not_60_out, not_61_out, not_62_out, not_63_out,
       not_64_out, not_65_out, not_66_out, not_67_out, not_68_out, not_69_out, not_70_out, not_71_out,
       not_72_out, not_73_out, not_74_out, not_75_out, not_76_out, not_77_out, not_78_out, not_79_out,
       not_80_out, not_81_out, not_82_out, not_83_out, not_84_out, not_85_out, not_86_out, not_87_out,
       not_88_out, not_89_out, not_90_out, not_91_out, not_92_out, not_93_out, not_94_out, not_95_out,
       not_96_out, not_97_out, not_98_out, not_99_out, not_100_out, not_101_out, not_102_out, not_103_out,
       not_104_out, not_105_out, not_106_out, not_107_out, not_108_out, not_109_out, not_110_out,
       not_111_out, not_112_out, not_113_out, not_114_out, not_115_out, not_116_out, not_117_out,
       not_118_out, not_119_out, not_120_out, not_121_out, not_122_out, not_123_out, not_124_out,
       not_125_out, not_126_out, not_127_out, not_128_out, not_129_out, not_130_out, not_131_out,
       not_132_out, not_133_out, not_134_out, not_135_out, not_136_out, not_137_out, not_138_out,
       not_139_out, not_140_out, not_141_out, not_142_out, not_143_out, not_144_out, not_145_out,
       not_146_out, not_147_out, not_148_out, not_149_out, not_150_out, not_151_out, not_152_out,
       not_153_out, not_154_out, not_155_out, not_156_out, not_157_out, not_158_out, not_159_out,
       not_160_out, not_161_out, not_162_out, not_163_out, not_164_out, not_165_out, not_166_out,
       not_167_out, not_168_out, not_169_out, not_170_out, not_171_out, not_172_out, not_173_out,
       not_174_out, not_175_out, not_176_out, not_177_out, not_178_out, not_179_out, not_180_out,
       not_181_out, not_182_out, not_183_out, not_184_out, not_185_out, not_186_out, not_187_out,
       not_188_out, not_189_out, not_190_out, not_191_out, not_192_out, not_193_out, not_194_out,
       not_195_out, not_196_out, not_197_out, not_198_out, not_199_out, not_200_out, not_201_out,
       not_202_out, not_203_out, not_204_out, not_205_out, not_206_out, not_207_out, not_208_out,
       not_209_out, not_210_out, not_211_out, not_212_out, not_213_out, not_214_out, not_215_out,
       not_216_out, not_217_out, not_218_out, not_219_out, not_220_out, not_221_out, not_222_out,
       not_223_out, not_224_out, not_225_out, not_226_out, not_227_out, not_228_out, not_229_out,
       not_230_out, not_231_out, not_232_out, not_233_out, not_234_out, not_235_out, not_236_out,
       not_237_out, not_238_out, not_239_out, not_240_out, not_241_out, not_242_out, not_243_out,
       not_244_out, not_245_out, not_246_out, not_247_out, not_248_out, not_249_out, not_250_out,
       not_251_out, not_252_out, not_253_out, not_254_out, not_255_out, not_256_out, not_257_out,
       not_258_out, not_259_out, not_260_out, not_261_out, not_262_out, not_263_out, not_264_out,
       not_265_out, not_266_out, not_267_out, not_268_out, not_269_out, not_270_out, not_271_out,
       not_272_out, not_273_out, not_274_out, not_275_out, not_276_out, not_277_out, not_278_out,
       not_279_out, not_280_out, not_281_out, not_282_out, not_283_out, not_284_out, not_285_out,
       not_286_out, not_287_out, not_288_out, not_289_out, not_290_out, not_291_out, not_292_out,
       not_293_out, not_294_out, not_295_out, not_296_out, not_297_out, not_298_out, not_299_out,
       not_300_out, not_301_out, not_302_out, not_303_out, not_304_out, not_305_out, not_306_out,
       not_307_out, not_308_out, not_309_out, not_310_out, not_311_out, not_312_out, not_313_out,
       not_314_out, not_315_out, not_316_out, not_317_out, not_318_out, not_319_out, not_320_out,
       not_321_out, not_322_out, not_323_out, not_324_out, not_325_out, not_326_out, not_327_out,
       not_328_out, not_329_out, not_330_out, not_331_out, not_332_out, not_333_out, not_334_out,
       not_335_out, not_336_out, not_337_out, not_338_out, not_339_out, not_340_out, not_341_out,
       not_342_out, not_343_out, not_344_out, not_345_out, not_346_out, not_347_out, not_348_out,
       not_349_out, not_350_out, not_351_out, not_352_out, not_353_out, not_354_out, not_355_out,
       not_356_out, not_357_out, not_358_out, not_359_out, not_360_out, not_361_out, not_362_out,
       not_363_out, not_364_out, not_365_out, not_366_out, not_367_out, not_368_out, not_369_out,
       not_370_out, not_371_out, not_372_out, not_373_out, not_374_out, not_375_out, not_376_out,
       not_377_out, not_378_out, not_379_out, not_380_out, not_381_out, not_382_out, not_383_out,
       not_384_out, not_385_out, not_386_out, not_387_out, not_388_out, not_389_out, not_390_out,
       not_391_out, not_392_out, not_393_out, not_394_out, not_395_out, not_396_out, not_397_out,
       not_398_out, not_399_out, not_400_out, not_401_out, not_402_out, not_403_out, not_404_out,
       not_405_out, not_406_out, not_407_out, not_408_out, not_409_out, not_410_out, not_411_out,
       not_412_out, not_413_out, not_414_out, not_415_out, not_416_out, not_417_out, not_418_out,
       not_419_out, not_420_out, not_421_out, not_422_out, not_423_out, not_424_out, not_425_out,
       not_426_out, not_427_out, not_428_out, not_429_out, not_430_out, not_431_out, not_432_out,
       not_433_out, not_434_out, not_435_out, not_436_out, not_437_out, not_438_out, not_439_out,
       not_440_out, not_441_out, not_442_out, not_443_out, not_444_out, not_445_out, not_446_out,
       not_447_out, not_448_out, not_449_out, not_450_out, not_451_out, not_452_out, not_453_out,
       not_454_out, not_455_out, not_456_out, not_457_out, not_458_out, not_459_out, not_460_out,
       not_461_out, not_462_out, not_463_out, not_464_out, not_465_out, not_466_out, not_467_out,
       not_468_out, not_469_out, not_470_out, not_471_out, not_472_out, not_473_out, not_474_out,
       not_475_out, not_476_out, not_477_out, not_478_out, not_479_out, not_480_out, not_481_out,
       not_482_out, not_483_out, not_484_out, not_485_out, not_486_out, not_487_out, not_488_out,
       not_489_out, not_490_out, not_491_out, not_492_out, not_493_out, not_494_out, not_495_out,
       not_496_out, not_497_out, not_498_out, not_499_out, not_500_out, not_501_out, not_502_out,
       not_503_out, not_504_out, not_505_out, not_506_out, not_507_out, not_508_out, not_509_out,
       not_510_out, not_511_out, not_512_out, not_513_out, not_514_out, not_515_out, not_516_out,
       not_517_out, not_518_out, not_519_out, not_520_out, not_521_out, not_522_out, not_523_out,
       not_524_out, not_525_out, not_526_out, not_527_out, not_528_out, not_529_out, not_530_out,
       not_531_out, not_532_out, not_533_out, not_534_out, not_535_out, not_536_out, not_537_out,
       not_538_out, not_539_out, not_540_out, not_541_out, not_542_out, not_543_out, not_544_out,
       not_545_out, not_546_out, not_547_out, not_548_out, not_549_out, not_550_out, not_551_out;

  not not_1 (not_1_out, OP2);
  not not_2 (not_2_out, OP3);
  not not_3 (not_3_out, OP4);
  not not_4 (not_4_out, OP5);
  not not_5 (not_5_out, OP6);
  not not_6 (not_6_out, F12);
  not not_7 (not_7_out, F14);
  not not_8 (not_8_out, OP2);
  not not_9 (not_9_out, OP3);
  not not_10 (not_10_out, OP4);
  not not_11 (not_11_out, OP6);
  not not_12 (not_12_out, F12);
  not not_13 (not_13_out, F14);
  not not_14 (not_14_out, OP2);
  not not_15 (not_15_out, OP3);
  not not_16 (not_16_out, OP5);
  not not_17 (not_17_out, OP6);
  not not_18 (not_18_out, F12);
  not not_19 (not_19_out, F14);
  not not_20 (not_20_out, OP2);
  not not_21 (not_21_out, OP3);
  not not_22 (not_22_out, OP4);
  not not_23 (not_23_out, OP6);
  not not_24 (not_24_out, F12);
  not not_25 (not_25_out, F14);
  not not_26 (not_26_out, OP2);
  not not_27 (not_27_out, OP3);
  not not_28 (not_28_out, OP5);
  not not_29 (not_29_out, OP6);
  not not_30 (not_30_out, F12);
  not not_31 (not_31_out, OP2);
  not not_32 (not_32_out, OP3);
  not not_33 (not_33_out, OP5);
  not not_34 (not_34_out, OP6);
  not not_35 (not_35_out, F13);
  not not_36 (not_36_out, F14);
  not not_37 (not_37_out, OP2);
  not not_38 (not_38_out, OP3);
  not not_39 (not_39_out, OP5);
  not not_40 (not_40_out, OP6);
  not not_41 (not_41_out, F13);
  not not_42 (not_42_out, F25);
  not not_43 (not_43_out, OP2);
  not not_44 (not_44_out, OP3);
  not not_45 (not_45_out, OP5);
  not not_46 (not_46_out, OP6);
  not not_47 (not_47_out, OP3);
  not not_48 (not_48_out, OP4);
  not not_49 (not_49_out, F12);
  not not_50 (not_50_out, F13);
  not not_51 (not_51_out, F14);
  not not_52 (not_52_out, OP3);
  not not_53 (not_53_out, OP6);
  not not_54 (not_54_out, F30);
  not not_55 (not_55_out, F25);
  not not_56 (not_56_out, F14);
  not not_57 (not_57_out, F13);
  not not_58 (not_58_out, F12);
  not not_59 (not_59_out, OP6);
  not not_60 (not_60_out, OP3);
  not not_61 (not_61_out, OP2);
  not not_62 (not_62_out, F25);
  not not_63 (not_63_out, F14);
  not not_64 (not_64_out, F13);
  not not_65 (not_65_out, F12);
  not not_66 (not_66_out, OP6);
  not not_67 (not_67_out, OP3);
  not not_68 (not_68_out, OP2);
  not not_69 (not_69_out, F30);
  not not_70 (not_70_out, F25);
  not not_71 (not_71_out, OP6);
  not not_72 (not_72_out, OP3);
  not not_73 (not_73_out, OP2);
  not not_74 (not_74_out, F30);
  not not_75 (not_75_out, F25);
  not not_76 (not_76_out, F12);
  not not_77 (not_77_out, OP6);
  not not_78 (not_78_out, OP3);
  not not_79 (not_79_out, OP2);
  not not_80 (not_80_out, F30);
  not not_81 (not_81_out, F25);
  not not_82 (not_82_out, F14);
  not not_83 (not_83_out, F12);
  not not_84 (not_84_out, OP6);
  not not_85 (not_85_out, OP3);
  not not_86 (not_86_out, OP2);
  not not_87 (not_87_out, F30);
  not not_88 (not_88_out, F25);
  not not_89 (not_89_out, F14);
  not not_90 (not_90_out, OP6);
  not not_91 (not_91_out, OP3);
  not not_92 (not_92_out, OP2);
  not not_93 (not_93_out, F14);
  not not_94 (not_94_out, F13);
  not not_95 (not_95_out, F12);
  not not_96 (not_96_out, OP6);
  not not_97 (not_97_out, OP5);
  not not_98 (not_98_out, OP3);
  not not_99 (not_99_out, OP2);
  not not_100 (not_100_out, OP6);
  not not_101 (not_101_out, OP5);
  not not_102 (not_102_out, OP3);
  not not_103 (not_103_out, OP2);
  not not_104 (not_104_out, F12);
  not not_105 (not_105_out, OP6);
  not not_106 (not_106_out, OP5);
  not not_107 (not_107_out, OP3);
  not not_108 (not_108_out, OP2);
  not not_109 (not_109_out, F13);
  not not_110 (not_110_out, F12);
  not not_111 (not_111_out, OP6);
  not not_112 (not_112_out, OP5);
  not not_113 (not_113_out, OP3);
  not not_114 (not_114_out, OP2);
  not not_115 (not_115_out, F14);
  not not_116 (not_116_out, F12);
  not not_117 (not_117_out, OP6);
  not not_118 (not_118_out, OP5);
  not not_119 (not_119_out, OP3);
  not not_120 (not_120_out, OP2);
  not not_121 (not_121_out, F14);
  not not_122 (not_122_out, F13);
  not not_123 (not_123_out, OP6);
  not not_124 (not_124_out, OP5);
  not not_125 (not_125_out, OP3);
  not not_126 (not_126_out, OP2);
  not not_127 (not_127_out, F30);
  not not_128 (not_128_out, F25);
  not not_129 (not_129_out, F13);
  not not_130 (not_130_out, OP6);
  not not_131 (not_131_out, OP5);
  not not_132 (not_132_out, OP3);
  not not_133 (not_133_out, OP2);
  not not_134 (not_134_out, F25);
  not not_135 (not_135_out, F13);
  not not_136 (not_136_out, OP6);
  not not_137 (not_137_out, OP5);
  not not_138 (not_138_out, OP3);
  not not_139 (not_139_out, OP2);
  not not_140 (not_140_out, F14);
  not not_141 (not_141_out, F12);
  not not_142 (not_142_out, OP6);
  not not_143 (not_143_out, OP5);
  not not_144 (not_144_out, OP4);
  not not_145 (not_145_out, OP3);
  not not_146 (not_146_out, OP2);
  not not_147 (not_147_out, OP4);
  not not_148 (not_148_out, F14);
  not not_149 (not_149_out, F13);
  not not_150 (not_150_out, F12);
  not not_151 (not_151_out, OP4);
  not not_152 (not_152_out, OP3);
  not not_153 (not_153_out, F30);
  not not_154 (not_154_out, F13);
  not not_155 (not_155_out, OP6);
  not not_156 (not_156_out, OP3);
  not not_157 (not_157_out, OP2);
  not not_158 (not_158_out, F30);
  not not_159 (not_159_out, OP6);
  not not_160 (not_160_out, OP3);
  not not_161 (not_161_out, OP2);
  not not_162 (not_162_out, OP6);
  not not_163 (not_163_out, OP3);
  not not_164 (not_164_out, F30);
  not not_165 (not_165_out, F12);
  not not_166 (not_166_out, OP6);
  not not_167 (not_167_out, OP3);
  not not_168 (not_168_out, OP2);
  not not_169 (not_169_out, F30);
  not not_170 (not_170_out, F25);
  not not_171 (not_171_out, F13);
  not not_172 (not_172_out, F12);
  not not_173 (not_173_out, OP6);
  not not_174 (not_174_out, OP3);
  not not_175 (not_175_out, OP2);
  not not_176 (not_176_out, F30);
  not not_177 (not_177_out, F25);
  not not_178 (not_178_out, F13);
  not not_179 (not_179_out, OP6);
  not not_180 (not_180_out, OP3);
  not not_181 (not_181_out, OP2);
  not not_182 (not_182_out, F30);
  not not_183 (not_183_out, F25);
  not not_184 (not_184_out, F14);
  not not_185 (not_185_out, F13);
  not not_186 (not_186_out, OP6);
  not not_187 (not_187_out, OP3);
  not not_188 (not_188_out, OP2);
  not not_189 (not_189_out, F30);
  not not_190 (not_190_out, F14);
  not not_191 (not_191_out, F13);
  not not_192 (not_192_out, F12);
  not not_193 (not_193_out, OP6);
  not not_194 (not_194_out, OP3);
  not not_195 (not_195_out, OP2);
  not not_196 (not_196_out, OP2);
  not not_197 (not_197_out, OP3);
  not not_198 (not_198_out, F12);
  not not_199 (not_199_out, F13);
  not not_200 (not_200_out, F14);
  not not_201 (not_201_out, F25);
  not not_202 (not_202_out, F30);
  not not_203 (not_203_out, OP2);
  not not_204 (not_204_out, OP3);
  not not_205 (not_205_out, OP4);
  not not_206 (not_206_out, OP6);
  not not_207 (not_207_out, F12);
  not not_208 (not_208_out, F14);
  not not_209 (not_209_out, OP2);
  not not_210 (not_210_out, OP3);
  not not_211 (not_211_out, OP4);
  not not_212 (not_212_out, F12);
  not not_213 (not_213_out, F13);
  not not_214 (not_214_out, F14);
  not not_215 (not_215_out, OP2);
  not not_216 (not_216_out, OP3);
  not not_217 (not_217_out, OP4);
  not not_218 (not_218_out, F13);
  not not_219 (not_219_out, F14);
  not not_220 (not_220_out, OP3);
  not not_221 (not_221_out, OP4);
  not not_222 (not_222_out, F12);
  not not_223 (not_223_out, F13);
  not not_224 (not_224_out, F14);
  not not_225 (not_225_out, OP4);
  not not_226 (not_226_out, OP2);
  not not_227 (not_227_out, OP3);
  not not_228 (not_228_out, OP4);
  not not_229 (not_229_out, F13);
  not not_230 (not_230_out, OP2);
  not not_231 (not_231_out, OP3);
  not not_232 (not_232_out, OP4);
  not not_233 (not_233_out, OP6);
  not not_234 (not_234_out, F12);
  not not_235 (not_235_out, F13);
  not not_236 (not_236_out, F14);
  not not_237 (not_237_out, OP2);
  not not_238 (not_238_out, OP3);
  not not_239 (not_239_out, OP6);
  not not_240 (not_240_out, F30);
  not not_241 (not_241_out, F30);
  not not_242 (not_242_out, F25);
  not not_243 (not_243_out, F14);
  not not_244 (not_244_out, F13);
  not not_245 (not_245_out, F12);
  not not_246 (not_246_out, OP6);
  not not_247 (not_247_out, OP3);
  not not_248 (not_248_out, OP2);
  not not_249 (not_249_out, F25);
  not not_250 (not_250_out, F14);
  not not_251 (not_251_out, F13);
  not not_252 (not_252_out, F12);
  not not_253 (not_253_out, OP6);
  not not_254 (not_254_out, OP3);
  not not_255 (not_255_out, OP2);
  not not_256 (not_256_out, F30);
  not not_257 (not_257_out, F25);
  not not_258 (not_258_out, OP6);
  not not_259 (not_259_out, OP3);
  not not_260 (not_260_out, OP2);
  not not_261 (not_261_out, F30);
  not not_262 (not_262_out, F25);
  not not_263 (not_263_out, F12);
  not not_264 (not_264_out, OP6);
  not not_265 (not_265_out, OP3);
  not not_266 (not_266_out, OP2);
  not not_267 (not_267_out, F30);
  not not_268 (not_268_out, F25);
  not not_269 (not_269_out, F14);
  not not_270 (not_270_out, F12);
  not not_271 (not_271_out, OP6);
  not not_272 (not_272_out, OP3);
  not not_273 (not_273_out, OP2);
  not not_274 (not_274_out, F30);
  not not_275 (not_275_out, F25);
  not not_276 (not_276_out, F14);
  not not_277 (not_277_out, OP6);
  not not_278 (not_278_out, OP3);
  not not_279 (not_279_out, OP2);
  not not_280 (not_280_out, F14);
  not not_281 (not_281_out, F13);
  not not_282 (not_282_out, F12);
  not not_283 (not_283_out, OP6);
  not not_284 (not_284_out, OP5);
  not not_285 (not_285_out, OP3);
  not not_286 (not_286_out, OP2);
  not not_287 (not_287_out, OP6);
  not not_288 (not_288_out, OP5);
  not not_289 (not_289_out, OP3);
  not not_290 (not_290_out, OP2);
  not not_291 (not_291_out, F12);
  not not_292 (not_292_out, OP6);
  not not_293 (not_293_out, OP5);
  not not_294 (not_294_out, OP3);
  not not_295 (not_295_out, OP2);
  not not_296 (not_296_out, F13);
  not not_297 (not_297_out, F12);
  not not_298 (not_298_out, OP6);
  not not_299 (not_299_out, OP5);
  not not_300 (not_300_out, OP3);
  not not_301 (not_301_out, OP2);
  not not_302 (not_302_out, F14);
  not not_303 (not_303_out, F12);
  not not_304 (not_304_out, OP6);
  not not_305 (not_305_out, OP5);
  not not_306 (not_306_out, OP3);
  not not_307 (not_307_out, OP2);
  not not_308 (not_308_out, F14);
  not not_309 (not_309_out, F13);
  not not_310 (not_310_out, OP6);
  not not_311 (not_311_out, OP5);
  not not_312 (not_312_out, OP3);
  not not_313 (not_313_out, OP2);
  not not_314 (not_314_out, F30);
  not not_315 (not_315_out, F25);
  not not_316 (not_316_out, F13);
  not not_317 (not_317_out, OP6);
  not not_318 (not_318_out, OP5);
  not not_319 (not_319_out, OP3);
  not not_320 (not_320_out, OP2);
  not not_321 (not_321_out, F25);
  not not_322 (not_322_out, F13);
  not not_323 (not_323_out, OP6);
  not not_324 (not_324_out, OP5);
  not not_325 (not_325_out, OP3);
  not not_326 (not_326_out, OP2);
  not not_327 (not_327_out, F14);
  not not_328 (not_328_out, F12);
  not not_329 (not_329_out, OP6);
  not not_330 (not_330_out, OP5);
  not not_331 (not_331_out, OP4);
  not not_332 (not_332_out, OP3);
  not not_333 (not_333_out, OP2);
  not not_334 (not_334_out, F14);
  not not_335 (not_335_out, F12);
  not not_336 (not_336_out, OP6);
  not not_337 (not_337_out, OP4);
  not not_338 (not_338_out, OP3);
  not not_339 (not_339_out, OP2);
  not not_340 (not_340_out, F30);
  not not_341 (not_341_out, F25);
  not not_342 (not_342_out, F14);
  not not_343 (not_343_out, F13);
  not not_344 (not_344_out, F12);
  not not_345 (not_345_out, OP3);
  not not_346 (not_346_out, OP2);
  not not_347 (not_347_out, F14);
  not not_348 (not_348_out, F13);
  not not_349 (not_349_out, F12);
  not not_350 (not_350_out, OP4);
  not not_351 (not_351_out, OP3);
  not not_352 (not_352_out, OP2);
  not not_353 (not_353_out, F14);
  not not_354 (not_354_out, F13);
  not not_355 (not_355_out, OP4);
  not not_356 (not_356_out, OP3);
  not not_357 (not_357_out, OP2);
  not not_358 (not_358_out, F14);
  not not_359 (not_359_out, F13);
  not not_360 (not_360_out, F12);
  not not_361 (not_361_out, OP4);
  not not_362 (not_362_out, OP3);
  not not_363 (not_363_out, F30);
  not not_364 (not_364_out, F13);
  not not_365 (not_365_out, OP6);
  not not_366 (not_366_out, OP3);
  not not_367 (not_367_out, OP2);
  not not_368 (not_368_out, F30);
  not not_369 (not_369_out, OP6);
  not not_370 (not_370_out, OP3);
  not not_371 (not_371_out, OP2);
  not not_372 (not_372_out, F14);
  not not_373 (not_373_out, F13);
  not not_374 (not_374_out, F12);
  not not_375 (not_375_out, OP6);
  not not_376 (not_376_out, OP4);
  not not_377 (not_377_out, OP3);
  not not_378 (not_378_out, OP2);
  not not_379 (not_379_out, F13);
  not not_380 (not_380_out, OP4);
  not not_381 (not_381_out, OP3);
  not not_382 (not_382_out, OP2);
  not not_383 (not_383_out, F30);
  not not_384 (not_384_out, F12);
  not not_385 (not_385_out, OP6);
  not not_386 (not_386_out, OP3);
  not not_387 (not_387_out, OP2);
  not not_388 (not_388_out, F30);
  not not_389 (not_389_out, F25);
  not not_390 (not_390_out, F13);
  not not_391 (not_391_out, F12);
  not not_392 (not_392_out, OP6);
  not not_393 (not_393_out, OP3);
  not not_394 (not_394_out, OP2);
  not not_395 (not_395_out, F30);
  not not_396 (not_396_out, F25);
  not not_397 (not_397_out, F13);
  not not_398 (not_398_out, OP6);
  not not_399 (not_399_out, OP3);
  not not_400 (not_400_out, OP2);
  not not_401 (not_401_out, F13);
  not not_402 (not_402_out, F12);
  not not_403 (not_403_out, OP4);
  not not_404 (not_404_out, OP3);
  not not_405 (not_405_out, OP2);
  not not_406 (not_406_out, F30);
  not not_407 (not_407_out, F25);
  not not_408 (not_408_out, F14);
  not not_409 (not_409_out, F13);
  not not_410 (not_410_out, OP6);
  not not_411 (not_411_out, OP3);
  not not_412 (not_412_out, OP2);
  not not_413 (not_413_out, F30);
  not not_414 (not_414_out, F14);
  not not_415 (not_415_out, F13);
  not not_416 (not_416_out, F12);
  not not_417 (not_417_out, OP6);
  not not_418 (not_418_out, OP3);
  not not_419 (not_419_out, OP2);
  not not_420 (not_420_out, F30);
  not not_421 (not_421_out, F25);
  not not_422 (not_422_out, F14);
  not not_423 (not_423_out, F13);
  not not_424 (not_424_out, F12);
  not not_425 (not_425_out, OP6);
  not not_426 (not_426_out, OP3);
  not not_427 (not_427_out, OP2);
  not not_428 (not_428_out, F25);
  not not_429 (not_429_out, F14);
  not not_430 (not_430_out, F13);
  not not_431 (not_431_out, F12);
  not not_432 (not_432_out, OP6);
  not not_433 (not_433_out, OP3);
  not not_434 (not_434_out, OP2);
  not not_435 (not_435_out, F30);
  not not_436 (not_436_out, F25);
  not not_437 (not_437_out, OP6);
  not not_438 (not_438_out, OP3);
  not not_439 (not_439_out, OP2);
  not not_440 (not_440_out, F30);
  not not_441 (not_441_out, F25);
  not not_442 (not_442_out, F12);
  not not_443 (not_443_out, OP6);
  not not_444 (not_444_out, OP3);
  not not_445 (not_445_out, OP2);
  not not_446 (not_446_out, F30);
  not not_447 (not_447_out, F25);
  not not_448 (not_448_out, F14);
  not not_449 (not_449_out, F12);
  not not_450 (not_450_out, OP6);
  not not_451 (not_451_out, OP3);
  not not_452 (not_452_out, OP2);
  not not_453 (not_453_out, F30);
  not not_454 (not_454_out, F25);
  not not_455 (not_455_out, F14);
  not not_456 (not_456_out, OP6);
  not not_457 (not_457_out, OP3);
  not not_458 (not_458_out, OP2);
  not not_459 (not_459_out, F14);
  not not_460 (not_460_out, F12);
  not not_461 (not_461_out, OP6);
  not not_462 (not_462_out, OP4);
  not not_463 (not_463_out, OP3);
  not not_464 (not_464_out, OP2);
  not not_465 (not_465_out, F30);
  not not_466 (not_466_out, F25);
  not not_467 (not_467_out, F14);
  not not_468 (not_468_out, F13);
  not not_469 (not_469_out, F12);
  not not_470 (not_470_out, OP3);
  not not_471 (not_471_out, OP2);
  not not_472 (not_472_out, F14);
  not not_473 (not_473_out, F13);
  not not_474 (not_474_out, F12);
  not not_475 (not_475_out, OP4);
  not not_476 (not_476_out, OP3);
  not not_477 (not_477_out, OP2);
  not not_478 (not_478_out, F14);
  not not_479 (not_479_out, F13);
  not not_480 (not_480_out, OP4);
  not not_481 (not_481_out, OP3);
  not not_482 (not_482_out, OP2);
  not not_483 (not_483_out, F30);
  not not_484 (not_484_out, F13);
  not not_485 (not_485_out, OP6);
  not not_486 (not_486_out, OP3);
  not not_487 (not_487_out, OP2);
  not not_488 (not_488_out, F30);
  not not_489 (not_489_out, OP6);
  not not_490 (not_490_out, OP3);
  not not_491 (not_491_out, OP2);
  not not_492 (not_492_out, F14);
  not not_493 (not_493_out, F13);
  not not_494 (not_494_out, F12);
  not not_495 (not_495_out, OP6);
  not not_496 (not_496_out, OP4);
  not not_497 (not_497_out, OP3);
  not not_498 (not_498_out, OP2);
  not not_499 (not_499_out, F13);
  not not_500 (not_500_out, OP4);
  not not_501 (not_501_out, OP3);
  not not_502 (not_502_out, OP2);
  not not_503 (not_503_out, F30);
  not not_504 (not_504_out, F12);
  not not_505 (not_505_out, OP6);
  not not_506 (not_506_out, OP3);
  not not_507 (not_507_out, OP2);
  not not_508 (not_508_out, F30);
  not not_509 (not_509_out, F25);
  not not_510 (not_510_out, F13);
  not not_511 (not_511_out, F12);
  not not_512 (not_512_out, OP6);
  not not_513 (not_513_out, OP3);
  not not_514 (not_514_out, OP2);
  not not_515 (not_515_out, F30);
  not not_516 (not_516_out, F25);
  not not_517 (not_517_out, F13);
  not not_518 (not_518_out, OP6);
  not not_519 (not_519_out, OP3);
  not not_520 (not_520_out, OP2);
  not not_521 (not_521_out, F13);
  not not_522 (not_522_out, F12);
  not not_523 (not_523_out, OP4);
  not not_524 (not_524_out, OP3);
  not not_525 (not_525_out, OP2);
  not not_526 (not_526_out, F30);
  not not_527 (not_527_out, F25);
  not not_528 (not_528_out, F14);
  not not_529 (not_529_out, F13);
  not not_530 (not_530_out, OP6);
  not not_531 (not_531_out, OP3);
  not not_532 (not_532_out, OP2);
  not not_533 (not_533_out, F30);
  not not_534 (not_534_out, F14);
  not not_535 (not_535_out, F13);
  not not_536 (not_536_out, F12);
  not not_537 (not_537_out, OP6);
  not not_538 (not_538_out, OP3);
  not not_539 (not_539_out, OP2);
  not not_540 (not_540_out, OP2);
  not not_541 (not_541_out, OP3);
  not not_542 (not_542_out, F12);
  not not_543 (not_543_out, OP2);
  not not_544 (not_544_out, OP3);
  not not_545 (not_545_out, OP3);
  not not_546 (not_546_out, OP6);
  not not_547 (not_547_out, OP2);
  not not_548 (not_548_out, OP3);
  not not_549 (not_549_out, OP4);
  not not_550 (not_550_out, F12);
  not not_551 (not_551_out, F13);
  and and_1 (MemToReg, not_1_out, not_2_out, not_3_out, not_4_out, not_5_out, not_6_out, F13, not_7_out);
  and and_2 (MemWrite, not_8_out, not_9_out, not_10_out, OP5, not_11_out, not_12_out, not_13_out);
  and and_3 (and_3_out, not_14_out, not_15_out, not_16_out, not_17_out, not_18_out, F13, not_19_out);
  and and_4 (and_4_out, not_20_out, not_21_out, not_22_out, OP5, not_23_out, not_24_out, not_25_out);
  and and_5 (and_5_out, not_26_out, not_27_out, OP4, not_28_out, not_29_out, not_30_out);
  and and_6 (and_6_out, not_31_out, not_32_out, OP4, not_33_out, not_34_out, not_35_out, not_36_out);
  and and_7 (and_7_out, not_37_out, not_38_out, OP4, not_39_out, not_40_out, not_41_out, not_42_out);
  and and_8 (and_8_out, not_43_out, not_44_out, OP4, not_45_out, not_46_out, F13, F14);
  and and_9 (and_9_out, OP2, not_47_out, not_48_out, OP5, OP6, not_49_out, not_50_out, not_51_out);
  and and_10 (and_10_out, OP2, not_52_out, OP4, OP5, not_53_out);
  and and_11 (and_11_out, not_54_out, not_55_out, not_56_out, not_57_out, not_58_out, not_59_out, OP5, OP4, not_60_out, not_61_out);
  and and_12 (and_12_out, F30, not_62_out, not_63_out, not_64_out, not_65_out, not_66_out, OP5, OP4, not_67_out, not_68_out);
  and and_13 (and_13_out, not_69_out, not_70_out, F14, F13, F12, not_71_out, OP5, OP4, not_72_out, not_73_out);
  and and_14 (and_14_out, not_74_out, not_75_out, F14, F13, not_76_out, not_77_out, OP5, OP4, not_78_out, not_79_out);
  and and_15 (and_15_out, not_80_out, not_81_out, not_82_out, F13, not_83_out, not_84_out, OP5, OP4, not_85_out, not_86_out);
  and and_16 (and_16_out, not_87_out, not_88_out, not_89_out, F13, F12, not_90_out, OP5, OP4, not_91_out, not_92_out);
  and and_17 (and_17_out, not_93_out, not_94_out, not_95_out, not_96_out, not_97_out, OP4, not_98_out, not_99_out);
  and and_18 (and_18_out, F14, F13, F12, not_100_out, not_101_out, OP4, not_102_out, not_103_out);
  and and_19 (and_19_out, F14, F13, not_104_out, not_105_out, not_106_out, OP4, not_107_out, not_108_out);
  and and_20 (and_20_out, F14, not_109_out, not_110_out, not_111_out, not_112_out, OP4, not_113_out, not_114_out);
  and and_21 (and_21_out, not_115_out, F13, not_116_out, not_117_out, not_118_out, OP4, not_119_out, not_120_out);
  and and_22 (and_22_out, not_121_out, not_122_out, F12, not_123_out, not_124_out, OP4, not_125_out, not_126_out);
  and and_23 (and_23_out, not_127_out, not_128_out, F14, not_129_out, F12, not_130_out, not_131_out, OP4, not_132_out, not_133_out);
  and and_24 (and_24_out, F30, not_134_out, F14, not_135_out, F12, not_136_out, not_137_out, OP4, not_138_out, not_139_out);
  and and_25 (and_25_out, not_140_out, F13, not_141_out, not_142_out, not_143_out, not_144_out, not_145_out, not_146_out);
  and and_26 (and_26_out, OP6, OP5, not_147_out, OP3, OP2);
  and and_27 (and_27_out, not_148_out, not_149_out, not_150_out, OP6, OP5, not_151_out, not_152_out, OP2);
  and and_28 (and_28_out, not_153_out, F25, F14, not_154_out, F12, not_155_out, OP5, OP4, not_156_out, not_157_out);
  and and_29 (and_29_out, not_158_out, F25, F14, F13, F12, not_159_out, OP5, OP4, not_160_out, not_161_out);
  and and_30 (and_30_out, not_162_out, OP5, OP4, not_163_out, OP2);
  and and_31 (and_31_out, not_164_out, F25, F14, F13, not_165_out, not_166_out, OP5, OP4, not_167_out, not_168_out);
  and and_32 (and_32_out, not_169_out, not_170_out, F14, not_171_out, not_172_out, not_173_out, OP5, OP4, not_174_out, not_175_out);
  and and_33 (and_33_out, not_176_out, not_177_out, F14, not_178_out, F12, not_179_out, OP5, OP4, not_180_out, not_181_out);
  and and_34 (and_34_out, not_182_out, not_183_out, not_184_out, not_185_out, F12, not_186_out, OP5, OP4, not_187_out, not_188_out);
  and and_35 (and_35_out, not_189_out, F25, not_190_out, not_191_out, not_192_out, not_193_out, OP5, OP4, not_194_out, not_195_out);
  and and_36 (ecall, not_196_out, not_197_out, OP4, OP5, OP6, not_198_out, not_199_out, not_200_out, not_201_out, not_202_out);
  and and_37 (S_Type, not_203_out, not_204_out, not_205_out, OP5, not_206_out, not_207_out, not_208_out);
  and and_38 (BEQ, not_209_out, not_210_out, not_211_out, OP5, OP6, not_212_out, not_213_out, not_214_out);
  and and_39 (BNE, not_215_out, not_216_out, not_217_out, OP5, OP6, F12, not_218_out, not_219_out);
  and and_40 (JALR, OP2, not_220_out, not_221_out, OP5, OP6, not_222_out, not_223_out, not_224_out);
  and and_41 (JAL, OP2, OP3, not_225_out, OP5, OP6);
  and and_42 (BGE, not_226_out, not_227_out, not_228_out, OP5, OP6, F12, not_229_out, F14);
  and and_43 (SB, not_230_out, not_231_out, not_232_out, OP5, not_233_out, not_234_out, not_235_out, not_236_out);
  and and_44 (ALT, not_237_out, not_238_out, OP4, OP5, not_239_out, F13, F14, F25, not_240_out);
  and and_45 (and_45_out, not_241_out, not_242_out, not_243_out, not_244_out, not_245_out, not_246_out, OP5, OP4, not_247_out, not_248_out);
  and and_46 (and_46_out, F30, not_249_out, not_250_out, not_251_out, not_252_out, not_253_out, OP5, OP4, not_254_out, not_255_out);
  and and_47 (and_47_out, not_256_out, not_257_out, F14, F13, F12, not_258_out, OP5, OP4, not_259_out, not_260_out);
  and and_48 (and_48_out, not_261_out, not_262_out, F14, F13, not_263_out, not_264_out, OP5, OP4, not_265_out, not_266_out);
  and and_49 (and_49_out, not_267_out, not_268_out, not_269_out, F13, not_270_out, not_271_out, OP5, OP4, not_272_out, not_273_out);
  and and_50 (and_50_out, not_274_out, not_275_out, not_276_out, F13, F12, not_277_out, OP5, OP4, not_278_out, not_279_out);
  and and_51 (and_51_out, not_280_out, not_281_out, not_282_out, not_283_out, not_284_out, OP4, not_285_out, not_286_out);
  and and_52 (and_52_out, F14, F13, F12, not_287_out, not_288_out, OP4, not_289_out, not_290_out);
  and and_53 (and_53_out, F14, F13, not_291_out, not_292_out, not_293_out, OP4, not_294_out, not_295_out);
  and and_54 (and_54_out, F14, not_296_out, not_297_out, not_298_out, not_299_out, OP4, not_300_out, not_301_out);
  and and_55 (and_55_out, not_302_out, F13, not_303_out, not_304_out, not_305_out, OP4, not_306_out, not_307_out);
  and and_56 (and_56_out, not_308_out, not_309_out, F12, not_310_out, not_311_out, OP4, not_312_out, not_313_out);
  and and_57 (and_57_out, not_314_out, not_315_out, F14, not_316_out, F12, not_317_out, not_318_out, OP4, not_319_out, not_320_out);
  and and_58 (and_58_out, F30, not_321_out, F14, not_322_out, F12, not_323_out, not_324_out, OP4, not_325_out, not_326_out);
  and and_59 (and_59_out, not_327_out, F13, not_328_out, not_329_out, not_330_out, not_331_out, not_332_out, not_333_out);
  and and_60 (and_60_out, not_334_out, F13, not_335_out, not_336_out, OP5, not_337_out, not_338_out, not_339_out);
  and and_61 (and_61_out, not_340_out, not_341_out, not_342_out, not_343_out, not_344_out, OP6, OP5, OP4, not_345_out, not_346_out);
  and and_62 (and_62_out, not_347_out, not_348_out, not_349_out, OP6, OP5, not_350_out, not_351_out, not_352_out);
  and and_63 (and_63_out, not_353_out, not_354_out, F12, OP6, OP5, not_355_out, not_356_out, not_357_out);
  and and_64 (and_64_out, not_358_out, not_359_out, not_360_out, OP6, OP5, not_361_out, not_362_out, OP2);
  and and_65 (and_65_out, not_363_out, F25, F14, not_364_out, F12, not_365_out, OP5, OP4, not_366_out, not_367_out);
  and and_66 (and_66_out, not_368_out, F25, F14, F13, F12, not_369_out, OP5, OP4, not_370_out, not_371_out);
  and and_67 (and_67_out, not_372_out, not_373_out, not_374_out, not_375_out, OP5, not_376_out, not_377_out, not_378_out);
  and and_68 (and_68_out, F14, not_379_out, F12, OP6, OP5, not_380_out, not_381_out, not_382_out);
  and and_69 (and_69_out, not_383_out, F25, F14, F13, not_384_out, not_385_out, OP5, OP4, not_386_out, not_387_out);
  and and_70 (and_70_out, not_388_out, not_389_out, F14, not_390_out, not_391_out, not_392_out, OP5, OP4, not_393_out, not_394_out);
  and and_71 (and_71_out, not_395_out, not_396_out, F14, not_397_out, F12, not_398_out, OP5, OP4, not_399_out, not_400_out);
  and and_72 (and_72_out, F14, not_401_out, not_402_out, OP6, OP5, not_403_out, not_404_out, not_405_out);
  and and_73 (and_73_out, not_406_out, not_407_out, not_408_out, not_409_out, F12, not_410_out, OP5, OP4, not_411_out, not_412_out);
  and and_74 (and_74_out, not_413_out, F25, not_414_out, not_415_out, not_416_out, not_417_out, OP5, OP4, not_418_out, not_419_out);
  and and_75 (and_75_out, not_420_out, not_421_out, not_422_out, not_423_out, not_424_out, not_425_out, OP5, OP4, not_426_out, not_427_out);
  and and_76 (and_76_out, F30, not_428_out, not_429_out, not_430_out, not_431_out, not_432_out, OP5, OP4, not_433_out, not_434_out);
  and and_77 (and_77_out, not_435_out, not_436_out, F14, F13, F12, not_437_out, OP5, OP4, not_438_out, not_439_out);
  and and_78 (and_78_out, not_440_out, not_441_out, F14, F13, not_442_out, not_443_out, OP5, OP4, not_444_out, not_445_out);
  and and_79 (and_79_out, not_446_out, not_447_out, not_448_out, F13, not_449_out, not_450_out, OP5, OP4, not_451_out, not_452_out);
  and and_80 (and_80_out, not_453_out, not_454_out, not_455_out, F13, F12, not_456_out, OP5, OP4, not_457_out, not_458_out);
  and and_81 (and_81_out, not_459_out, F13, not_460_out, not_461_out, OP5, not_462_out, not_463_out, not_464_out);
  and and_82 (and_82_out, not_465_out, not_466_out, not_467_out, not_468_out, not_469_out, OP6, OP5, OP4, not_470_out, not_471_out);
  and and_83 (and_83_out, not_472_out, not_473_out, not_474_out, OP6, OP5, not_475_out, not_476_out, not_477_out);
  and and_84 (and_84_out, not_478_out, not_479_out, F12, OP6, OP5, not_480_out, not_481_out, not_482_out);
  and and_85 (and_85_out, not_483_out, F25, F14, not_484_out, F12, not_485_out, OP5, OP4, not_486_out, not_487_out);
  and and_86 (and_86_out, not_488_out, F25, F14, F13, F12, not_489_out, OP5, OP4, not_490_out, not_491_out);
  and and_87 (and_87_out, not_492_out, not_493_out, not_494_out, not_495_out, OP5, not_496_out, not_497_out, not_498_out);
  and and_88 (and_88_out, F14, not_499_out, F12, OP6, OP5, not_500_out, not_501_out, not_502_out);
  and and_89 (and_89_out, not_503_out, F25, F14, F13, not_504_out, not_505_out, OP5, OP4, not_506_out, not_507_out);
  and and_90 (and_90_out, not_508_out, not_509_out, F14, not_510_out, not_511_out, not_512_out, OP5, OP4, not_513_out, not_514_out);
  and and_91 (and_91_out, not_515_out, not_516_out, F14, not_517_out, F12, not_518_out, OP5, OP4, not_519_out, not_520_out);
  and and_92 (and_92_out, F14, not_521_out, not_522_out, OP6, OP5, not_523_out, not_524_out, not_525_out);
  and and_93 (and_93_out, not_526_out, not_527_out, not_528_out, not_529_out, F12, not_530_out, OP5, OP4, not_531_out, not_532_out);
  and and_94 (and_94_out, not_533_out, F25, not_534_out, not_535_out, not_536_out, not_537_out, OP5, OP4, not_538_out, not_539_out);
  and and_95 (IRE, not_540_out, not_541_out, OP4, OP5, OP6, not_542_out, F13, F14);
  and and_96 (IRD, not_543_out, not_544_out, OP4, OP5, OP6, F12, F13, F14);
  and and_97 (LUI, OP2, not_545_out, OP4, OP5, not_546_out);
  and and_98 (BLT, not_547_out, not_548_out, not_549_out, OP5, OP6, not_550_out, not_551_out, F14);
  or or_1 (ALU_SRC, and_3_out, and_4_out, and_5_out, and_6_out, and_7_out, and_8_out, and_9_out, and_10_out);
  or or_2 (RtUsed, and_75_out, and_76_out, and_77_out, and_78_out, and_79_out, and_80_out, and_81_out, and_82_out, and_83_out, and_84_out, and_85_out, and_86_out, and_87_out, and_88_out, and_89_out, and_90_out, and_91_out, and_92_out, and_93_out, and_94_out);
  or or_3 (RegWrite, and_11_out, and_12_out, and_13_out, and_14_out, and_15_out, and_16_out, and_17_out, and_18_out, and_19_out, and_20_out, and_21_out, and_22_out, and_23_out, and_24_out, and_25_out, and_26_out, and_27_out, and_28_out, and_29_out, and_30_out, and_31_out, and_32_out, and_33_out, and_34_out, and_35_out);
  or or_4 (RsUsed, and_45_out, and_46_out, and_47_out, and_48_out, and_49_out, and_50_out, and_51_out, and_52_out, and_53_out, and_54_out, and_55_out, and_56_out, and_57_out, and_58_out, and_59_out, and_60_out, and_61_out, and_62_out, and_63_out, and_64_out, and_65_out, and_66_out, and_67_out, and_68_out, and_69_out, and_70_out, and_71_out, and_72_out, and_73_out, and_74_out);
endmodule

// ALU
module ALU (
  input  [31:0] X,
  input  [31:0] Y,
  input  [3:0] AluOP,
  output out_4,
  output Equal,
  output out_6,
  output [31:0] Result,
  output [31:0] Result_2
);

  wire [0:0] comparator_1_lt, comparator_2_lt;
  wire [31:0] adder_1_out, AND_out, divider_1_out, divider_1_rem, multiplier_1_cout, multiplier_1_out,
       NOR_out, OR_out, shifter_1_out, shifter_2_out, shifter_3_out, subtractor_1_out, XOR_out;

  assign AND_out = X & Y;  // AND_Gate AND, 32 bits wide
  assign OR_out = X | Y;  // OR_Gate OR, 32 bits wide
  Shifter #(.width(32), .shift("ll")) shifter_1 (.in(X), .\dist (Y[4:0]), .out(shifter_1_out));
  Shifter #(.width(32), .shift("ar")) shifter_2 (.in(X), .\dist (Y[4:0]), .out(shifter_2_out));
  Shifter #(.width(32), .shift("lr")) shifter_3 (.in(X), .\dist (Y[4:0]), .out(shifter_3_out));
  Multiplier #(.width(32)) multiplier_1 (.a(X), .b(Y), .out(multiplier_1_out), .cout(multiplier_1_cout));  // open: cin
  Divider #(.width(32)) divider_1 (.a(X), .b(Y), .out(divider_1_out), .rem(divider_1_rem));  // open: upper
  Adder #(.width(32)) adder_1 (.a(X), .b(Y), .out(adder_1_out));  // open: cin, cout
  Subtractor #(.width(32)) subtractor_1 (.a(X), .b(Y), .out(subtractor_1_out));  // open: bin, bout
  assign XOR_out = X ^ Y;  // XOR_Gate XOR, 32 bits wide
  assign NOR_out = ~(X | Y);  // NOR_Gate NOR, 32 bits wide
  Comparator #(.width(32), .mode("twosComplement")) comparator_1 (
    .a(X), .b(Y), .eq(Equal), .lt(comparator_1_lt[0]));  // open: gt
  Comparator #(.width(32), .mode("unsigned")) comparator_2 (.a(X), .b(Y), .lt(comparator_2_lt[0]));  // open: gt, eq
  Multiplexer #(.select(4), .width(32), .disabled("Z"), .enable("false")) multiplexer_1 (
    .in0(shifter_1_out), .in1(shifter_2_out), .in2(shifter_3_out), .in3(multiplier_1_out),
    .in4(divider_1_out), .in5(adder_1_out), .in6(subtractor_1_out), .in7(AND_out), .in8(OR_out),
    .in9(XOR_out), .in10(NOR_out), .in11({{31{1'b0}}, comparator_1_lt[0]}),
    .in12({{31{1'b0}}, comparator_2_lt[0]}), .in13({32{1'b0}}), .in14({32{1'b0}}), .in15({32{1'b0}}),
    .out(Result), .sel(AluOP));
  Multiplexer #(.select(4), .width(32), .disabled("Z"), .enable("false")) multiplexer_2 (
    .in0({32{1'b0}}), .in1({32{1'b0}}), .in2({32{1'b0}}), .in3(multiplier_1_cout), .in4(divider_1_rem),
    .in5({32{1'b0}}), .in6({32{1'b0}}), .in7({32{1'b0}}), .in8({32{1'b0}}), .in9({32{1'b0}}),
    .in10({32{1'b0}}), .in11({32{1'b0}}), .in12({32{1'b0}}), .in13({32{1'b0}}), .in14({32{1'b0}}),
    .in15({32{1'b0}}), .out(Result_2), .sel(AluOP));
  Multiplexer #(.select(4), .width(1), .disabled("Z"), .enable("false")) multiplexer_3 (
    .in0(1'b0), .in1(1'b0), .in2(1'b0), .in3(1'b0), .in4(1'b0), .in5(1'b0), .in6(1'b0), .in7(1'b0),
    .in8(1'b0), .in9(1'b0), .in10(1'b0), .in11(comparator_1_lt[0]), .in12(comparator_2_lt[0]), .in13(1'b0),
    .in14(1'b0), .in15(1'b0), .out(out_6), .sel(AluOP));
  not not_1 (out_4, out_6);

  // Other names for the same wires on the sheet: Result2[31:0] = Result_2; S[3:0] = AluOP; tunnel = out_6;
  //   tunnel_t = out_4

  // Notes on the sheet:
  //   不要改变此引脚区域内容，也不要改变ALU封装形式
  //   输入引脚
  //   输出引脚
endmodule

module Regifile (
  input  [31:0] Din,
  input  Clk,
  input  WE,
  input  [4:0] R1_num,
  input  [4:0] W_num,
  input  [4:0] R2_num,
  output [31:0] R1,
  output [31:0] R2
);

  // RegisterFile registerfile_1: pin names not known; wires that end beside it: Din, Clk, WE, W_num, R1_num, R2_num, R1, R2
endmodule

module \理想流水线  (
  output RegWrite,
  output MemWrite,
  output [31:0] IF_PC,
  output [31:0] ID_PC,
  output [31:0] EX_PC,
  output [31:0] M_PC,
  output [31:0] WB_PC,
  output [31:0] RDin,
  output [31:0] MDin,
  output [31:0] LedData
);

  wire ALT, alu_1_equal, alu_1_out_4, and_1_out, and_2_out, and_3_out, and_4_out, and_5_out, and_6_out, Bge,
       clock_1_out, comparator_1_eq, comparator_2_eq, comparator_2_lt, controlled_buffer_1_out, d_ff_1_q,
       ecall, EX_MEM_out3, EX_MEM_out5, EX_MEM_out7, flow_register_bit_1_out1, flow_register_bit_1_out2,
       flow_register_bit_1_out3, flow_register_bit_1_out4, flow_register_bit_1_out5,
       flow_register_bit_1_out7, Flush, Go, go_halt, halt, IR1, IR2, IR3, JAL, JALR, MTR, nand_1_out,
       not_1_out, not_2_out, not_3_out, not_4_out, not_5_out, not_6_out, not_7_out, or_3_out, RST, sb, SType,
       W1, W2, W3, \单周期硬布线控制器_1_alt , \单周期硬布线控制器_1_alu_src , \单周期硬布线控制器_1_beq , \单周期硬布线控制器_1_bge ,
       \单周期硬布线控制器_1_bne , \单周期硬布线控制器_1_ecall , \单周期硬布线控制器_1_jal , \单周期硬布线控制器_1_jalr , \单周期硬布线控制器_1_memtoreg ,
       \单周期硬布线控制器_1_memwrite , \单周期硬布线控制器_1_regwrite , \单周期硬布线控制器_1_sb , \单周期硬布线控制器_1_uret ;
  wire [1:0] flow_register_2_outcor;
  wire [3:0] flow_register_bit_1_aluopout, MemSel, shifter_3_out, \单周期硬布线控制器_1_alu_op ;
  wire [4:0] flow_register_1_outrd, flow_register_2_outrd, multiplexer_3_out, multiplexer_4_out,
       multiplexer_8_out, WBAddr;
  wire [11:0] multiplexer_5_out;
  wire [12:0] CNT_num;
  wire [15:0] adder_1_out, \LoadUse次数 , \总周期数 , \插入气泡数 , \无条件分支数 , \条件分支成功数 ;
  wire [19:0] bit_extender_2_out, bit_extender_5_out, multiplexer_6_out;
  wire [31:0] adder_2_out, adder_3_out, adder_4_out, alu_1_result, alu_1_result_2, ALUO, bit_extender_1_out,
       bit_extender_3_out, bit_extender_4_out, CLK, EX_IR, flow_register_1_out1, flow_register_1_out2,
       flow_register_1_out3, flow_register_1_out4, flow_register_2_out1, flow_register_2_out4,
       flow_register_3_out3, ID_IR, IF_IR, MEM_IR, mips_ram_1_p7, multiplexer_1_out, multiplexer_2_out,
       multiplexer_7_out, multiplexer_9_out, PCOffset, regifile_1_r1, regifile_1_r2, shifter_2_out, WB_IR;

  Button \u_总复位  (.out(RST));
  Button _1 (.out(IR1));
  Button _2 (.out(IR2));
  Button _3 (.out(IR3));
  Button \u_继续运行  (.out(Go));
  LED #(.active("true")) led_1 (.in(W1));
  LED #(.active("true")) led_2 (.in(W2));
  LED #(.active("true")) led_3 (.in(W3));
  not not_1 (not_1_out, halt);
  Hex_Digit_Display hex_digit_display_1 (.value(LedData[31:28]));  // open: dp
  Register #(.width(16), .trigger("rising"), .Select("low")) \u_周期  (
    .D(adder_1_out), .en(not_1_out), .Q(\总周期数 ), .clk(CLK[0]), .clr(RST));
  not not_2 (not_2_out, go_halt);
  Hex_Digit_Display hex_digit_display_2 (.value(LedData[27:24]));  // open: dp
  Hex_Digit_Display hex_digit_display_3 (.value(LedData[23:20]));  // open: dp
  // OR_Gate or_1 has open pins: in0=Go, in1=and_1_out, out=open
  and and_1 (and_1_out, not_2_out, not_3_out);
  not not_3 (not_3_out, halt);
  Hex_Digit_Display hex_digit_display_4 (.value(LedData[15:12]));  // open: dp
  Hex_Digit_Display hex_digit_display_5 (.value(LedData[19:16]));  // open: dp
  Adder #(.width(16)) adder_1 (.a(\总周期数 ), .b(16'h1), .out(adder_1_out));  // open: cin, cout
  Register #(.width(32), .trigger("rising"), .Select("low")) PC (
    .D(multiplexer_2_out), .Q(IF_PC), .clk(CLK[0]), .clr(RST));  // open: en
  Hex_Digit_Display hex_digit_display_6 (.value(LedData[7:4]));  // open: dp
  Hex_Digit_Display hex_digit_display_7 (.value(LedData[11:8]));  // open: dp
  not not_4 (not_4_out, halt);
  Adder #(.width(32)) adder_2 (.a(EX_PC), .b(PCOffset), .out(adder_2_out));  // open: cin, cout
  Hex_Digit_Display hex_digit_display_8 (.value(LedData[3:0]));  // open: dp
  Register #(.width(1), .trigger("rising"), .Select("low")) u_Halt (
    .D(go_halt), .en(not_4_out), .Q(halt), .clk(CLK[0]), .clr(Go));
  Adder #(.width(32)) adder_3 (.a(IF_PC), .b(32'h4), .out(adder_3_out));  // open: cin, cout
  Multiplexer #(.select(1), .width(32), .disabled("Z"), .enable("false")) multiplexer_1 (
    .in0(adder_2_out), .in1(ALUO), .out(multiplexer_1_out), .sel(JALR));
  Multiplexer #(.select(1), .width(32), .disabled("Z"), .enable("false")) multiplexer_2 (
    .in0(adder_3_out), .in1(multiplexer_1_out), .out(multiplexer_2_out), .sel(Flush));
  // Probe on \总周期数 
  ROM #(.addrWidth(10), .dataWidth(32), .Select("high")) rom_1 (.addr(IF_PC[11:2]), .data(IF_IR));
  // Probe on \总周期数 
  // Probe on \无条件分支数 
  // Probe on \条件分支成功数 
  // Probe on \插入气泡数 
  // Probe on \LoadUse次数 
  Flow_Register IF_ID (
    .IN1(IF_IR), .Flush(Flush), .CLK(CLK[0]), .OUT1(ID_IR), .PC2(IF_PC), .PC2_2(ID_PC), .RST(RST));  // open: PC, PC_2, IN2, OUT2, IN3, OUT3, IN4, OUT4, INrd, OUTrd, INcor, OUTcor, EN, INForA, OUTForA
  // Probe on IF_PC[11:0]
  // Probe on ID_PC[11:0]
  // Probe on EX_PC[11:0]
  // Probe on M_PC[11:0]
  \单周期硬布线控制器  \u_单周期硬布线控制器_1  (
    .Funct({ID_IR[30], ID_IR[25], ID_IR[14:12]}), .OP(ID_IR[6:2]), .ALU_OP(\单周期硬布线控制器_1_alu_op ),
    .MemToReg(\单周期硬布线控制器_1_memtoreg ), .MemWrite(\单周期硬布线控制器_1_memwrite ), .ALU_SRC(\单周期硬布线控制器_1_alu_src ),
    .RegWrite(\单周期硬布线控制器_1_regwrite ), .ecall(\单周期硬布线控制器_1_ecall ), .S_type(SType),
    .Jalr(\单周期硬布线控制器_1_jalr ), .Beq(\单周期硬布线控制器_1_beq ), .JAL(\单周期硬布线控制器_1_jal ), .Bne(\单周期硬布线控制器_1_bne ),
    .IR(ID_IR[21]), .uret(\单周期硬布线控制器_1_uret ), .Bge(\单周期硬布线控制器_1_bge ), .sb(\单周期硬布线控制器_1_sb ),
    .ALT(\单周期硬布线控制器_1_alt ));  // open: RsUsed, RtUsed, IRE, IRD, LUI, BLT
  Multiplexer #(.select(1), .width(5), .disabled("Z"), .enable("false")) multiplexer_3 (
    .in0(ID_IR[19:15]), .in1(5'b01010), .out(multiplexer_3_out), .sel(\单周期硬布线控制器_1_ecall ));
  Multiplexer #(.select(1), .width(5), .disabled("Z"), .enable("false")) multiplexer_4 (
    .in0(ID_IR[24:20]), .in1(5'b10001), .out(multiplexer_4_out), .sel(\单周期硬布线控制器_1_ecall ));
  Multiplexer #(.select(1), .width(12), .disabled("Z"), .enable("false")) multiplexer_5 (
    .in0(ID_IR[31:20]), .in1({ID_IR[31:25], ID_IR[11:7]}), .out(multiplexer_5_out), .sel(SType));
  // Probe on WB_PC[11:0]
  assign bit_extender_1_out = {{20{multiplexer_5_out[11]}}, multiplexer_5_out};  // Bit_Extender bit_extender_1
  assign bit_extender_2_out = {{8{ID_IR[31]}}, {ID_IR[31], ID_IR[7], ID_IR[30:25], ID_IR[11:8]}};  // Bit_Extender bit_extender_2
  Multiplexer #(.select(1), .width(20), .disabled("Z"), .enable("false")) multiplexer_6 (
    .in0(bit_extender_2_out), .in1({ID_IR[31], ID_IR[19:12], ID_IR[20], ID_IR[30:21]}),
    .out(multiplexer_6_out), .sel(\单周期硬布线控制器_1_jal ));
  Regifile regifile_1 (
    .Din(RDin), .Clk(CLK[0]), .R1(regifile_1_r1), .R2(regifile_1_r2), .WE(RegWrite), .W_num(WBAddr),
    .R1_num(multiplexer_3_out), .R2_num(multiplexer_4_out));
  assign bit_extender_3_out = {{12{multiplexer_6_out[19]}}, multiplexer_6_out};  // Bit_Extender bit_extender_3
  Flow_Register_Bit ID_EX (
    .IN4(\单周期硬布线控制器_1_alt ), .IN3(\单周期硬布线控制器_1_jal ), .IN2(\单周期硬布线控制器_1_jalr ), .IN5(\单周期硬布线控制器_1_bge ),
    .IN6(\单周期硬布线控制器_1_sb ), .IN1(\单周期硬布线控制器_1_ecall ), .OUT4(ALT), .OUT3(JAL), .OUT2(JALR), .OUT5(Bge),
    .OUT6(sb), .OUT1(ecall), .Flush(Flush), .CLK(CLK[0]), .RST(RST));  // open: IN7, OUT7, ALUOPIN, ALUOPOut, EN
  Flow_Register_Bit flow_register_bit_1 (
    .IN4(\单周期硬布线控制器_1_beq ), .IN3(\单周期硬布线控制器_1_bne ), .IN2(\单周期硬布线控制器_1_memtoreg ),
    .IN5(\单周期硬布线控制器_1_memwrite ), .IN1(\单周期硬布线控制器_1_alu_src ), .OUT4(flow_register_bit_1_out4),
    .OUT3(flow_register_bit_1_out3), .OUT2(flow_register_bit_1_out2), .OUT5(flow_register_bit_1_out5),
    .OUT1(flow_register_bit_1_out1), .Flush(Flush), .CLK(CLK[0]), .RST(RST), .IN7(\单周期硬布线控制器_1_regwrite ),
    .OUT7(flow_register_bit_1_out7), .ALUOPIN(\单周期硬布线控制器_1_alu_op ), .ALUOPOut(flow_register_bit_1_aluopout));  // open: IN6, OUT6, EN
  Flow_Register flow_register_1 (
    .IN1(regifile_1_r1), .Flush(Flush), .CLK(CLK[0]), .OUT1(flow_register_1_out1), .PC2(ID_PC),
    .PC2_2(EX_PC), .RST(RST), .IN2(regifile_1_r2), .OUT2(flow_register_1_out2), .IN3(bit_extender_3_out),
    .OUT3(flow_register_1_out3), .IN4(bit_extender_1_out), .OUT4(flow_register_1_out4), .INrd(ID_IR[11:7]),
    .OUTrd(flow_register_1_outrd));  // open: PC, PC_2, INcor, OUTcor, EN, INForA, OUTForA
  Multiplexer #(.select(1), .width(32), .disabled("Z"), .enable("false")) multiplexer_7 (
    .in0(flow_register_1_out2), .in1(flow_register_1_out4), .out(multiplexer_7_out),
    .sel(flow_register_bit_1_out1));
  // Probe on \总周期数 
  // Probe on \总周期数 
  ALU alu_1 (
    .X(flow_register_1_out1), .Y(multiplexer_7_out), .AluOP(flow_register_bit_1_aluopout),
    .Equal(alu_1_equal), .Result(alu_1_result), .Result_2(alu_1_result_2), .out_4(alu_1_out_4));  // open: out_6
  Shifter #(.width(32), .shift("ll")) shifter_1 (.in(flow_register_1_out3), .\dist (5'b00001), .out(PCOffset));
  // Probe on IF_PC[19:0]
  // RiscV_Probe riscv_probe_1: pin names not known; wires that end beside it: IF_IR
  not not_5 (not_5_out, alu_1_equal);
  Multiplexer #(.select(2), .width(5), .disabled("Z"), .enable("false")) multiplexer_8 (
    .in0({5{1'b0}}), .in1(5'b01000), .in2(5'b10000), .in3(5'b11000), .out(multiplexer_8_out),
    .sel(alu_1_result[1:0]));
  and and_2 (and_2_out, alu_1_out_4, Bge);
  and and_3 (and_3_out, flow_register_bit_1_out3, not_5_out);
  Comparator #(.width(32), .mode("twosComplement")) comparator_1 (
    .a(flow_register_1_out2), .b(32'h22), .eq(comparator_1_eq));  // open: gt, lt
  not not_6 (not_6_out, comparator_1_eq);
  Shifter #(.width(32), .shift("ll")) shifter_2 (
    .in(flow_register_1_out2), .\dist (multiplexer_8_out), .out(shifter_2_out));
  // Probe on ID_PC[19:0]
  // RiscV_Probe riscv_probe_2: pin names not known; wires that end beside it: ID_IR
  and and_4 (and_4_out, flow_register_bit_1_out4, alu_1_equal);
  Register #(.width(32), .trigger("rising"), .Select("low")) LED_Register (
    .D(flow_register_1_out1), .en(and_5_out), .Q(LedData), .clk(CLK[0]), .clr(RST));
  and and_5 (and_5_out, ecall, comparator_1_eq);
  and and_6 (and_6_out, ecall, not_6_out);
  Multiplexer #(.select(1), .width(32), .disabled("Z"), .enable("false")) multiplexer_9 (
    .in0(alu_1_result), .in1(alu_1_result_2), .out(multiplexer_9_out), .sel(ALT));
  or or_2 (Flush, and_3_out, and_4_out, and_2_out, JAL, JALR);
  Adder #(.width(32)) adder_4 (.a(32'h4), .b(EX_PC), .out(adder_4_out));  // open: cin, cout
  // Probe on EX_PC[19:0]
  // RiscV_Probe riscv_probe_3: pin names not known; wires that end beside it: EX_IR
  or or_3 (or_3_out, JALR, JAL);
  assign bit_extender_4_out = {{2{1'b0}}, alu_1_result[31:2]};  // Bit_Extender bit_extender_4
  Multiplexer #(.select(1), .width(32), .disabled("Z"), .enable("false")) multiplexer_10 (
    .in0(multiplexer_9_out), .in1(adder_4_out), .out(CLK), .sel(or_3_out));
  // Probe on M_PC[19:0]
  // RiscV_Probe riscv_probe_4: pin names not known; wires that end beside it: MEM_IR
  Flow_Register_Bit EX_MEM (
    .IN3(flow_register_bit_1_out7), .IN5(flow_register_bit_1_out2), .IN1(flow_register_bit_1_out5),
    .OUT3(EX_MEM_out3), .OUT5(EX_MEM_out5), .OUT1(MemWrite), .Flush(Flush), .CLK(CLK[0]), .RST(RST),
    .IN7(and_6_out), .OUT7(EX_MEM_out7));  // open: IN4, IN2, IN6, OUT4, OUT2, OUT6, ALUOPIN, ALUOPOut, EN
  Flow_Register flow_register_2 (
    .Flush(Flush), .CLK(CLK[0]), .OUT1(flow_register_2_out1), .PC2(EX_PC), .PC2_2(M_PC), .RST(RST),
    .IN3(shifter_2_out), .OUT3(MDin), .IN4(bit_extender_4_out), .OUT4(flow_register_2_out4),
    .INrd(flow_register_1_outrd), .OUTrd(flow_register_2_outrd), .INcor(alu_1_result[1:0]),
    .OUTcor(flow_register_2_outcor));  // open: IN1, PC, PC_2, IN2, OUT2, EN, INForA, OUTForA
  // RiscV_Probe riscv_probe_5: pin names not known; wires that end beside it: WB_IR
  // Probe on WB_PC[19:0]
  Bit_Extender #(.in_width(32), .out_width(20), .\type ("zero")) bit_extender_5 (
    .in(flow_register_2_out4), .out(bit_extender_5_out));
  Shifter #(.width(4), .shift("ll")) shifter_3 (.in(4'b0001), .\dist (flow_register_2_outcor), .out(shifter_3_out));
  Multiplexer #(.select(1), .width(4), .disabled("Z"), .enable("false")) multiplexer_11 (
    .in0(4'b1111), .in1(shifter_3_out), .out(MemSel), .sel(sb));
  D_Flip_Flop #(.trigger("high"), .Pre_Clr_Positions("LEGACY"), .NegatePresetClear("false"), .enable("true"), .NewFFLayout("false")) d_ff_1 (.Q(d_ff_1_q));  // open: clk, D, Qn, preset, en, reset
  // Probe on 13'h12
  // MIPS_RAM mips_ram_1: pin names not known; wires that end beside it: bit_extender_5_out, MDin, MemWrite, MemSel, CLK, RST, mips_ram_1_p7, flow_register_2_out1, mips_ram_1_p7, flow_register_2_outrd, M_PC
  Comparator #(.width(13), .mode("twosComplement")) comparator_2 (
    .a(CNT_num), .b(13'h12), .eq(comparator_2_eq), .lt(comparator_2_lt));  // open: gt
  Clock #(.highDuration(1), .lowDuration(1)) clock_1 (.out(clock_1_out));
  nand nand_1 (nand_1_out, d_ff_1_q, comparator_2_eq);
  Counter #(.width(13), .max('h1fff), .ongoal("stay"), .trigger("rising"), .behavior("old")) counter_1 (
    .count(comparator_2_lt), .Q(CNT_num), .clk(clock_1_out));  // open: load, D, carry, clr, preset
  Flow_Register_Bit MEM_WB (
    .IN3(EX_MEM_out3), .IN5(EX_MEM_out5), .OUT3(RegWrite), .OUT5(MTR), .Flush(Flush), .CLK(CLK[0]),
    .RST(RST), .IN7(EX_MEM_out7), .OUT7(go_halt));  // open: IN4, IN2, IN6, IN1, OUT4, OUT2, OUT6, OUT1, ALUOPIN, ALUOPOut, EN
  Flow_Register flow_register_3 (
    .IN1(flow_register_2_out1), .Flush(Flush), .CLK(CLK[0]), .OUT1(ALUO), .PC2(M_PC), .PC2_2(WB_PC),
    .RST(RST), .IN3(mips_ram_1_p7), .OUT3(flow_register_3_out3), .INrd(flow_register_2_outrd), .OUTrd(WBAddr));  // open: PC, PC_2, IN2, OUT2, IN4, OUT4, INcor, OUTcor, EN, INForA, OUTForA
  assign controlled_buffer_1_out = nand_1_out ? clock_1_out : 1'bz;  // Controlled_Buffer controlled_buffer_1
  Pull_Resistor #(.pull(1)) pull_resistor_1 (.node(controlled_buffer_1_out));
  Multiplexer #(.select(1), .width(32), .disabled("Z"), .enable("false")) multiplexer_12 (
    .in0(ALUO), .in1(flow_register_3_out3), .out(RDin), .sel(MTR));
  not not_7 (not_7_out, halt);
  and and_7 (CLK[0], controlled_buffer_1_out, not_7_out);
  // Pins of 1 and 32 bits meet at CLK

  // Other names for the same wires on the sheet: IR[31:0] = ID_IR; MEM_PC[31:0] = M_PC; PCSig[31:0] = EX_PC;
  //   PCSrc = Flush

  // Notes on the sheet:
  //   中断源
  //   中断等待指示
  //   数码管输出
  //   指令存储器
  //   contents of rom_1 (hex, n*v repeats v):
  //   413 493 913 993 46413 14e493 296913 39e993 842023 942223 1242423 1342623 a00893 493 913 993 73
  //   指令字
  //   JAL
  //   JALR
  //   URET
  //   Bge
  //   BEQ offset
  //   JAL offset
  //   流水调试日志用
  //   Beq
  //   Bne
  //   MemToReg
  //   MemWrite
  //   AluOP
  //   AluSrcB
  //   RegWrite
  //   S_Type
  //   ecall
  //   rd
  //   时空图监测，可删除
  //   为方便自动评测，需要输出流水线各段保存的PC值，注意是PC不是PC+4，另外ID段寄存器写入信息，Mem段内存写入信息也要输出
  //   Bne Judge
  //   Beq Judge
  //   rd
  //   Bge Judge
  //   rd
  //   控制位
  //   暂停节拍，不能为0
  //   戳工具置1进入计数暂停模式，ctrl+k时钟自动运行到对应节拍暂停
  //   ctrl+k关闭时钟连续运行，将控制位置零，进入单步调试模式调试
  //   用这个时钟源需要去掉电路中的其他时钟源
  //   可计数暂停的时钟源
endmodule

module \气泡流水线  (
  output RegWrite,
  output MemWrite,
  output [31:0] IF_PC,
  output [31:0] ID_PC,
  output [31:0] EX_PC,
  output [31:0] M_PC,
  output [31:0] WB_PC,
  output [31:0] RDin,
  output [31:0] MDin,
  output [31:0] LedData
);

  wire ALT, alu_1_equal, alu_1_out_4, and_1_out, and_3_out, and_4_out, and_5_out, and_6_out, and_7_out, Bge,
       CLK, clock_1_out, comparator_1_eq, comparator_1_lt, comparator_2_eq, controlled_buffer_1_out,
       d_ff_1_q, ecall, EX_MEM_out3, EX_MEM_out5, EX_MEM_out7, flow_register_bit_1_out1,
       flow_register_bit_1_out2, flow_register_bit_1_out3, flow_register_bit_1_out4,
       flow_register_bit_1_out5, flow_register_bit_1_out7, Flush, Go, go_halt, halt, ID_EX_out6, IR1, IR2,
       IR3, JAL, JALR, MTR, nand_1_out, not_1_out, not_2_out, not_3_out, not_4_out, not_5_out, not_6_out,
       not_7_out, or_3_out, PCSrc, RST, RsUsed, RtUsed, sb, Stall, SType, W1, W2, W3, \单周期硬布线控制器_1_alt ,
       \单周期硬布线控制器_1_alu_src , \单周期硬布线控制器_1_beq , \单周期硬布线控制器_1_bge , \单周期硬布线控制器_1_bne , \单周期硬布线控制器_1_ecall ,
       \单周期硬布线控制器_1_jal , \单周期硬布线控制器_1_jalr , \单周期硬布线控制器_1_memtoreg , \单周期硬布线控制器_1_memwrite ,
       \单周期硬布线控制器_1_regwrite , \单周期硬布线控制器_1_sb , \单周期硬布线控制器_1_uret ;
  wire [1:0] flow_register_2_outcor;
  wire [3:0] flow_register_bit_1_aluopout, MemSel, shifter_3_out, \单周期硬布线控制器_1_alu_op ;
  wire [4:0] flow_register_1_outrd, flow_register_2_outrd, multiplexer_8_out, Rs, Rt, WBAddr;
  wire [11:0] multiplexer_5_out;
  wire [12:0] CNT_num;
  wire [15:0] adder_1_out, \LoadUse次数 , \总周期数 , \插入气泡数 , \无条件分支数 , \条件分支成功数 ;
  wire [19:0] bit_extender_2_out, bit_extender_5_out, multiplexer_6_out;
  wire [31:0] adder_2_out, adder_3_out, adder_4_out, alu_1_result_2, ALUO, bit_extender_1_out,
       bit_extender_3_out, bit_extender_4_out, EX_IR, flow_register_1_out1, flow_register_1_out2,
       flow_register_1_out3, flow_register_1_out4, flow_register_2_out1, flow_register_2_out4,
       flow_register_3_out1, flow_register_3_out3, ID_IR, IF_IR, MEM_IR, mips_ram_1_p7, multiplexer_1_out,
       multiplexer_2_out, multiplexer_7_out, multiplexer_9_out, multiplexer_10_out, PCOffset, regifile_1_r1,
       regifile_1_r2, shifter_2_out, WB_IR;

  Button \u_总复位  (.out(RST));
  Button _1 (.out(IR1));
  Button _2 (.out(IR2));
  Button _3 (.out(IR3));
  // Probe on \总周期数 
  // Probe on \总周期数 
  Button \u_继续运行  (.out(Go));
  LED #(.active("true")) led_1 (.in(W1));
  LED #(.active("true")) led_2 (.in(W2));
  LED #(.active("true")) led_3 (.in(W3));
  Hex_Digit_Display hex_digit_display_1 (.value(LedData[31:28]));  // open: dp
  // Probe on IF_PC[19:0]
  // RiscV_Probe riscv_probe_1: pin names not known; wires that end beside it: IF_IR
  Hex_Digit_Display hex_digit_display_2 (.value(LedData[23:20]));  // open: dp
  Hex_Digit_Display hex_digit_display_3 (.value(LedData[27:24]));  // open: dp
  // Probe on ID_PC[19:0]
  // RiscV_Probe riscv_probe_2: pin names not known; wires that end beside it: ID_IR
  Register #(.width(16), .trigger("rising"), .Select("low")) \u_周期  (
    .D(adder_1_out), .en(not_1_out), .Q(\总周期数 ), .clk(CLK), .clr(RST));
  not not_1 (not_1_out, halt);
  not not_2 (not_2_out, go_halt);
  Hex_Digit_Display hex_digit_display_4 (.value(LedData[19:16]));  // open: dp
  Hex_Digit_Display hex_digit_display_5 (.value(LedData[15:12]));  // open: dp
  // OR_Gate or_1 has open pins: in0=Go, in1=and_1_out, out=open
  and and_1 (and_1_out, not_2_out, not_3_out);
  not not_3 (not_3_out, halt);
  Hex_Digit_Display hex_digit_display_6 (.value(LedData[7:4]));  // open: dp
  Hex_Digit_Display hex_digit_display_7 (.value(LedData[11:8]));  // open: dp
  // Probe on EX_PC[19:0]
  // RiscV_Probe riscv_probe_3: pin names not known; wires that end beside it: EX_IR
  Adder #(.width(16)) adder_1 (.a(\总周期数 ), .b(16'h1), .out(adder_1_out));  // open: cin, cout
  Register #(.width(32), .trigger("rising"), .Select("low")) PC (
    .D(multiplexer_2_out), .en(Stall), .Q(IF_PC), .clk(CLK), .clr(RST));
  Hex_Digit_Display hex_digit_display_8 (.value(LedData[3:0]));  // open: dp
  not not_4 (not_4_out, halt);
  Adder #(.width(32)) adder_2 (.a(EX_PC), .b(PCOffset), .out(adder_2_out));  // open: cin, cout
  // Probe on \总周期数 
  // Probe on M_PC[19:0]
  // RiscV_Probe riscv_probe_4: pin names not known; wires that end beside it: MEM_IR
  Register #(.width(1), .trigger("falling"), .Select("low")) u_Halt (
    .D(go_halt), .en(not_4_out), .Q(halt), .clk(CLK), .clr(Go));
  Adder #(.width(32)) adder_3 (.a(IF_PC), .b(32'h4), .out(adder_3_out));  // open: cin, cout
  Multiplexer #(.select(1), .width(32), .disabled("Z"), .enable("false")) multiplexer_1 (
    .in0(adder_2_out), .in1(ALUO), .out(multiplexer_1_out), .sel(JALR));
  Multiplexer #(.select(1), .width(32), .disabled("Z"), .enable("false")) multiplexer_2 (
    .in0(adder_3_out), .in1(multiplexer_1_out), .out(multiplexer_2_out), .sel(PCSrc));
  // Probe on \总周期数 
  // Probe on \无条件分支数 
  // Probe on \条件分支成功数 
  // Probe on \插入气泡数 
  // Probe on \LoadUse次数 
  ROM #(.addrWidth(10), .dataWidth(32), .Select("high")) rom_1 (.addr(IF_PC[11:2]), .data(IF_IR));
  Fowarding_Logic fowarding_logic_1 (
    .Ex_RegWrite(flow_register_bit_1_out7), .PCSrc(PCSrc), .Stall(Stall), .Flush(Flush),
    .MEM_RegWrite(EX_MEM_out3), .Rs(Rs), .Rt(Rt), .ExAddr(flow_register_1_outrd),
    .MEMAddr(flow_register_2_outrd), .RsUsed(RsUsed), .RtUsed(RtUsed));  // open: RsForward, RtForward, Ex_MemRead
  // Probe on IF_PC[11:0]
  // Probe on WB_PC[19:0]
  // RiscV_Probe riscv_probe_5: pin names not known; wires that end beside it: WB_IR
  // Probe on EX_PC[11:0]
  // Probe on ID_PC[11:0]
  Flow_Register IF_ID (
    .IN1(IF_IR), .Flush(Flush), .CLK(CLK), .OUT1(ID_IR), .PC2(IF_PC), .PC2_2(ID_PC), .RST(RST), .EN(Stall));  // open: PC, PC_2, IN2, OUT2, IN3, OUT3, IN4, OUT4, INrd, OUTrd, INcor, OUTcor, INForA, OUTForA
  // Probe on M_PC[11:0]
  D_Flip_Flop #(.trigger("high"), .Pre_Clr_Positions("LEGACY"), .NegatePresetClear("false"), .enable("true"), .NewFFLayout("false")) d_ff_1 (.Q(d_ff_1_q));  // open: clk, D, Qn, preset, en, reset
  // Probe on 13'h12
  // Probe on WB_PC[11:0]
  Comparator #(.width(13), .mode("twosComplement")) comparator_1 (
    .a(CNT_num), .b(13'h12), .eq(comparator_1_eq), .lt(comparator_1_lt));  // open: gt
  Clock #(.highDuration(1), .lowDuration(1)) clock_1 (.out(clock_1_out));
  \单周期硬布线控制器  \u_单周期硬布线控制器_1  (
    .Funct({ID_IR[30], ID_IR[25], ID_IR[14:12]}), .OP(ID_IR[6:2]), .ALU_OP(\单周期硬布线控制器_1_alu_op ),
    .MemToReg(\单周期硬布线控制器_1_memtoreg ), .MemWrite(\单周期硬布线控制器_1_memwrite ), .ALU_SRC(\单周期硬布线控制器_1_alu_src ),
    .RegWrite(\单周期硬布线控制器_1_regwrite ), .ecall(\单周期硬布线控制器_1_ecall ), .S_type(SType),
    .Jalr(\单周期硬布线控制器_1_jalr ), .Beq(\单周期硬布线控制器_1_beq ), .JAL(\单周期硬布线控制器_1_jal ), .Bne(\单周期硬布线控制器_1_bne ),
    .IR(ID_IR[21]), .uret(\单周期硬布线控制器_1_uret ), .Bge(\单周期硬布线控制器_1_bge ), .sb(\单周期硬布线控制器_1_sb ),
    .ALT(\单周期硬布线控制器_1_alt ), .RsUsed(RsUsed), .RtUsed(RtUsed));  // open: IRE, IRD, LUI, BLT
  Multiplexer #(.select(1), .width(5), .disabled("Z"), .enable("false")) multiplexer_3 (
    .in0(ID_IR[19:15]), .in1(5'b01010), .out(Rs), .sel(\单周期硬布线控制器_1_ecall ));
  Multiplexer #(.select(1), .width(5), .disabled("Z"), .enable("false")) multiplexer_4 (
    .in0(ID_IR[24:20]), .in1(5'b10001), .out(Rt), .sel(\单周期硬布线控制器_1_ecall ));
  Multiplexer #(.select(1), .width(12), .disabled("Z"), .enable("false")) multiplexer_5 (
    .in0(ID_IR[31:20]), .in1({ID_IR[31:25], ID_IR[11:7]}), .out(multiplexer_5_out), .sel(SType));
  nand nand_1 (nand_1_out, d_ff_1_q, comparator_1_eq);
  Counter #(.width(13), .max('h1fff), .ongoal("stay"), .trigger("rising"), .behavior("old")) counter_1 (
    .count(comparator_1_lt), .Q(CNT_num), .clk(clock_1_out));  // open: load, D, carry, clr, preset
  assign bit_extender_1_out = {{20{multiplexer_5_out[11]}}, multiplexer_5_out};  // Bit_Extender bit_extender_1
  assign bit_extender_2_out = {{8{ID_IR[31]}}, {ID_IR[31], ID_IR[7], ID_IR[30:25], ID_IR[11:8]}};  // Bit_Extender bit_extender_2
  Multiplexer #(.select(1), .width(20), .disabled("Z"), .enable("false")) multiplexer_6 (
    .in0(bit_extender_2_out), .in1({ID_IR[31], ID_IR[19:12], ID_IR[20], ID_IR[30:21]}),
    .out(multiplexer_6_out), .sel(\单周期硬布线控制器_1_jal ));
  assign controlled_buffer_1_out = nand_1_out ? clock_1_out : 1'bz;  // Controlled_Buffer controlled_buffer_1
  Regifile regifile_1 (
    .Din(RDin), .Clk(CLK), .R1(regifile_1_r1), .R2(regifile_1_r2), .WE(RegWrite), .W_num(WBAddr),
    .R1_num(Rs), .R2_num(Rt));
  Pull_Resistor #(.pull(1)) pull_resistor_1 (.node(controlled_buffer_1_out));
  assign bit_extender_3_out = {{12{multiplexer_6_out[19]}}, multiplexer_6_out};  // Bit_Extender bit_extender_3
  not not_5 (not_5_out, halt);
  Flow_Register_Bit ID_EX (
    .IN4(\单周期硬布线控制器_1_alt ), .IN3(\单周期硬布线控制器_1_jal ), .IN2(\单周期硬布线控制器_1_jalr ), .IN5(\单周期硬布线控制器_1_bge ),
    .IN6(\单周期硬布线控制器_1_sb ), .IN1(\单周期硬布线控制器_1_ecall ), .OUT4(ALT), .OUT3(JAL), .OUT2(JALR), .OUT5(Bge),
    .OUT6(ID_EX_out6), .OUT1(ecall), .Flush(Flush), .CLK(CLK), .RST(RST));  // open: IN7, OUT7, ALUOPIN, ALUOPOut, EN
  Flow_Register_Bit flow_register_bit_1 (
    .IN4(\单周期硬布线控制器_1_beq ), .IN3(\单周期硬布线控制器_1_bne ), .IN2(\单周期硬布线控制器_1_memtoreg ),
    .IN5(\单周期硬布线控制器_1_memwrite ), .IN1(\单周期硬布线控制器_1_alu_src ), .OUT4(flow_register_bit_1_out4),
    .OUT3(flow_register_bit_1_out3), .OUT2(flow_register_bit_1_out2), .OUT5(flow_register_bit_1_out5),
    .OUT1(flow_register_bit_1_out1), .Flush(Flush), .CLK(CLK), .RST(RST), .IN7(\单周期硬布线控制器_1_regwrite ),
    .OUT7(flow_register_bit_1_out7), .ALUOPIN(\单周期硬布线控制器_1_alu_op ), .ALUOPOut(flow_register_bit_1_aluopout));  // open: IN6, OUT6, EN
  Flow_Register flow_register_1 (
    .IN1(regifile_1_r1), .Flush(Flush), .CLK(CLK), .OUT1(flow_register_1_out1), .PC(ID_IR), .PC_2(EX_IR),
    .PC2(ID_PC), .PC2_2(EX_PC), .RST(RST), .IN2(regifile_1_r2), .OUT2(flow_register_1_out2),
    .IN3(bit_extender_3_out), .OUT3(flow_register_1_out3), .IN4(bit_extender_1_out),
    .OUT4(flow_register_1_out4), .INrd(ID_IR[11:7]), .OUTrd(flow_register_1_outrd));  // open: INcor, OUTcor, EN, INForA, OUTForA
  and and_2 (CLK, controlled_buffer_1_out, not_5_out);
  Multiplexer #(.select(1), .width(32), .disabled("Z"), .enable("false")) multiplexer_7 (
    .in0(flow_register_1_out2), .in1(flow_register_1_out4), .out(multiplexer_7_out),
    .sel(flow_register_bit_1_out1));
  ALU alu_1 (
    .X(flow_register_1_out1), .Y(multiplexer_7_out), .AluOP(flow_register_bit_1_aluopout),
    .Equal(alu_1_equal), .Result(ALUO), .Result_2(alu_1_result_2), .out_4(alu_1_out_4));  // open: out_6
  Shifter #(.width(32), .shift("ll")) shifter_1 (.in(flow_register_1_out3), .\dist (5'b00001), .out(PCOffset));
  and and_3 (and_3_out, flow_register_bit_1_out3, not_6_out);
  not not_6 (not_6_out, alu_1_equal);
  Comparator #(.width(32), .mode("twosComplement")) comparator_2 (
    .a(flow_register_1_out2), .b(32'h22), .eq(comparator_2_eq));  // open: gt, lt
  not not_7 (not_7_out, comparator_2_eq);
  Multiplexer #(.select(2), .width(5), .disabled("Z"), .enable("false")) multiplexer_8 (
    .in0({5{1'b0}}), .in1(5'b01000), .in2(5'b10000), .in3(5'b11000), .out(multiplexer_8_out), .sel(ALUO[1:0]));
  and and_4 (and_4_out, alu_1_out_4, Bge);
  and and_5 (and_5_out, flow_register_bit_1_out4, alu_1_equal);
  and and_6 (and_6_out, ecall, comparator_2_eq);
  and and_7 (and_7_out, ecall, not_7_out);
  Multiplexer #(.select(1), .width(32), .disabled("Z"), .enable("false")) multiplexer_9 (
    .in0(ALUO), .in1(alu_1_result_2), .out(multiplexer_9_out), .sel(ALT));
  Shifter #(.width(32), .shift("ll")) shifter_2 (
    .in(flow_register_1_out2), .\dist (multiplexer_8_out), .out(shifter_2_out));
  or or_2 (PCSrc, and_3_out, and_5_out, and_4_out, JAL, JALR);
  Register #(.width(32), .trigger("rising"), .Select("low")) LED_Register (
    .D(flow_register_1_out1), .en(and_6_out), .Q(LedData), .clk(CLK), .clr(RST));
  or or_3 (or_3_out, JALR, JAL);
  assign bit_extender_4_out = {{2{1'b0}}, ALUO[31:2]};  // Bit_Extender bit_extender_4
  Adder #(.width(32)) adder_4 (.a(32'h4), .b(EX_PC), .out(adder_4_out));  // open: cin, cout
  Multiplexer #(.select(1), .width(32), .disabled("Z"), .enable("false")) multiplexer_10 (
    .in0(multiplexer_9_out), .in1(adder_4_out), .out(multiplexer_10_out), .sel(or_3_out));
  Flow_Register_Bit EX_MEM (
    .IN3(flow_register_bit_1_out7), .IN2(ID_EX_out6), .IN5(flow_register_bit_1_out2),
    .IN1(flow_register_bit_1_out5), .OUT3(EX_MEM_out3), .OUT2(sb), .OUT5(EX_MEM_out5), .OUT1(MemWrite),
    .Flush(1'b0), .CLK(CLK), .RST(RST), .IN7(and_7_out), .OUT7(EX_MEM_out7));  // open: IN4, IN6, OUT4, OUT6, ALUOPIN, ALUOPOut, EN
  Flow_Register flow_register_2 (
    .IN1(multiplexer_10_out), .Flush(1'b0), .CLK(CLK), .OUT1(flow_register_2_out1), .PC(EX_IR),
    .PC_2(MEM_IR), .PC2(EX_PC), .PC2_2(M_PC), .RST(RST), .IN3(shifter_2_out), .OUT3(MDin),
    .IN4(bit_extender_4_out), .OUT4(flow_register_2_out4), .INrd(flow_register_1_outrd),
    .OUTrd(flow_register_2_outrd), .INcor(ALUO[1:0]), .OUTcor(flow_register_2_outcor));  // open: IN2, OUT2, EN, INForA, OUTForA
  Bit_Extender #(.in_width(32), .out_width(20), .\type ("zero")) bit_extender_5 (
    .in(flow_register_2_out4), .out(bit_extender_5_out));
  Shifter #(.width(4), .shift("ll")) shifter_3 (.in(4'b0001), .\dist (flow_register_2_outcor), .out(shifter_3_out));
  // MIPS_RAM mips_ram_1: pin names not known; wires that end beside it: bit_extender_5_out, MDin, MemWrite, MemSel, CLK, RST, mips_ram_1_p7, MEM_IR
  Multiplexer #(.select(1), .width(4), .disabled("Z"), .enable("false")) multiplexer_11 (
    .in0(4'b1111), .in1(shifter_3_out), .out(MemSel), .sel(sb));
  Flow_Register_Bit MEM_WB (
    .IN3(EX_MEM_out3), .IN5(EX_MEM_out5), .OUT3(RegWrite), .OUT5(MTR), .Flush(1'b0), .CLK(CLK), .RST(RST),
    .IN7(EX_MEM_out7), .OUT7(go_halt));  // open: IN4, IN2, IN6, IN1, OUT4, OUT2, OUT6, OUT1, ALUOPIN, ALUOPOut, EN
  Flow_Register flow_register_3 (
    .IN1(flow_register_2_out1), .Flush(1'b0), .CLK(CLK), .OUT1(flow_register_3_out1), .PC(MEM_IR),
    .PC_2(WB_IR), .PC2(M_PC), .PC2_2(WB_PC), .RST(RST), .IN3(mips_ram_1_p7), .OUT3(flow_register_3_out3),
    .INrd(flow_register_2_outrd), .OUTrd(WBAddr));  // open: IN2, OUT2, IN4, OUT4, INcor, OUTcor, EN, INForA, OUTForA
  Multiplexer #(.select(1), .width(32), .disabled("Z"), .enable("false")) multiplexer_12 (
    .in0(flow_register_3_out1), .in1(flow_register_3_out3), .out(RDin), .sel(MTR));

  // Other names for the same wires on the sheet: MEM_PC[31:0] = M_PC; PCSig[31:0] = EX_PC

  // Notes on the sheet:
  //   中断源
  //   时空图监测，可删除
  //   中断等待指示
  //   数码管输出
  //   指令存储器
  //   contents of rom_1 (hex, n*v repeats v):
  //   100493 100006f 100493 200913 300993 100006f 100493 200913 300993 100006f 100493 200913 300993
  //   100006f 100493 200913 300993 29c000ef 100413 100493 1f49493 900533 2200893 73 24d493 48463 fedff06f
  //   900533 2200893 73 100493 249493 900533 2200893 73 48463 fedff06f 100493 1f49493 900533 2200893 73
  //   4034d493 900533 2200893 73 4044d493 900533 2200893 73 4044d493 900533 2200893 73 4044d493 900533
  //   2200893 73 4044d493 900533 2200893 73 4044d493 900533 2200893 73 4044d493 900533 2200893 73 4044d493
  //   900533 2200893 73 100413 1f41993 41f9d993 433 c00913 300b13 140413 f47413 800293 100313 499993
  //   89e9b3 1300533 2200893 73 406282b3 fe0294e3 140413 f00f93 1f47433 1c41413 800293 100313 49d993
  //   89e9b3 1300533 2200893 73 406282b3 fe0294e3 1c45413 406b0b33 b0463 f95ff06f 2b3 fff2c293 829293
  //   ff2e293 500533 2200893 73 fff00413 493 84a023 140413 448493 84a023 140413 448493 84a023 140413
  //   448493 84a023 140413 448493 84a023 140413 448493 84a023 140413 448493 84a023 140413 448493 84a023
  //   140413 448493 84a023 140413 448493 84a023 140413 448493 84a023 140413 448493 84a023 140413 448493
  //   84a023 140413 448493 84a023 140413 448493 84a023 140413 448493 84a023 140413 448493 140413 433
  //   3c00493 42983 4aa03 149a2b3 28663 134a023 1442023 ffc48493 fe9412e3 800533 2200893 73 440413 3c00493
  //   fc9416e3 a00893 73 413 140413 800533 2200893 73 240413 800533 2200893 73 340413 800533 2200893 73
  //   440413 800533 2200893 73 540413 800533 2200893 73 640413 800533 2200893 73 740413 800533 2200893 73
  //   840413 800533 2200893 2200893 73 8067
  //   控制位
  //   指令字
  //   流水调试日志用
  //   暂停节拍，不能为0
  //   JAL
  //   JALR
  //   URET
  //   Bge
  //   BEQ offset
  //   JAL offset
  //   用这个时钟源需要去掉电路中的其他时钟源
  //   Beq
  //   Bne
  //   MemToReg
  //   MemWrite
  //   AluOP
  //   AluSrcB
  //   RegWrite
  //   S_Type
  //   ecall
  //   可计数暂停的时钟源
  //   rd
  //   为方便自动评测，需要输出流水线各段保存的PC值，注意是PC不是PC+4，另外ID段寄存器写入信息，Mem段内存写入信息也要输出
  //   Beq Judge
  //   Bne Judge
  //   Bge Judge
  //   rd
  //   rd
endmodule
module \重定向流水线  (
  output RegWrite,
  output MemWrite,
  output [31:0] IF_PC,
  output [31:0] ID_PC,
  output [31:0] EX_PC,
  output [31:0] M_PC,
  output [31:0] WB_PC,
  output [31:0] RDin,
  output [31:0] MDin,
  output [31:0] LedData
);

  wire ALT, alu_1_equal, alu_1_out_4, and_1_out, and_3_out, and_4_out, and_5_out, and_6_out, and_7_out,
       and_8_out, Bge, CLK, clock_1_out, comparator_1_eq, comparator_1_lt, comparator_2_eq, comparator_3_eq,
       controlled_buffer_1_out, d_ff_1_q, demultiplexer_1_out1, demultiplexer_1_out2, demultiplexer_1_out3,
       ecall, EX_MEM_out3, EX_MEM_out5, EX_MEM_out7, flow_register_bit_1_out1, flow_register_bit_1_out3,
       flow_register_bit_1_out4, flow_register_bit_1_out5, flow_register_bit_1_out7, Flush, Go, go_halt,
       halt, ID_EX_out6, IE, IR1, IR2, IR3, IRespond, JAL, JALR, MEMRead, MTR, nand_1_out, not_1_out,
       not_2_out, not_3_out, not_4_out, not_5_out, not_6_out, not_7_out, not_8_out, not_9_out, or_1_out,
       or_2_out, or_4_out, or_5_out, PCSrc, priority_encoder_1_gs, RST, RsUsed, RtUsed, sb, Stall, SType,
       URET, W1, W2, W3, \中断按键参考电路_1_iro , \中断按键参考电路_2_iro , \中断按键参考电路_3_iro , \单周期硬布线控制器_1_alt ,
       \单周期硬布线控制器_1_alu_src , \单周期硬布线控制器_1_beq , \单周期硬布线控制器_1_bge , \单周期硬布线控制器_1_bne , \单周期硬布线控制器_1_ecall ,
       \单周期硬布线控制器_1_jal , \单周期硬布线控制器_1_jalr , \单周期硬布线控制器_1_memtoreg , \单周期硬布线控制器_1_memwrite ,
       \单周期硬布线控制器_1_regwrite , \单周期硬布线控制器_1_sb ;
  wire [1:0] flow_register_1_outcor, flow_register_1_outfora, flow_register_2_outcor,
       fowarding_logic_1_rsforward, fowarding_logic_1_rtforward, IREncode, register_1_q;
  wire [3:0] flow_register_bit_1_aluopout, MemSel, shifter_3_out, \单周期硬布线控制器_1_alu_op ;
  wire [4:0] flow_register_1_outrd, flow_register_2_outrd, multiplexer_13_out, Rs, Rt, WBAddr;
  wire [11:0] multiplexer_8_out;
  wire [12:0] CNT_num;
  wire [15:0] adder_1_out, adder_4_out, adder_5_out, adder_6_out, adder_7_out, adder_8_out,
       bit_extender_1_out, bit_extender_5_out, bit_extender_6_out, bit_extender_7_out, bit_extender_8_out,
       \LoadUse次数 , \总周期数 , \插入气泡数 , \无条件分支数 , \条件分支成功数 ;
  wire [19:0] bit_extender_3_out, bit_extender_10_out, multiplexer_9_out;
  wire [31:0] adder_2_out, adder_3_out, adder_9_out, alu_1_result_2, ALUO, bit_extender_2_out,
       bit_extender_4_out, bit_extender_9_out, EX_IR, flow_register_1_out1, flow_register_1_out2,
       flow_register_1_out3, flow_register_1_out4, flow_register_2_out4, flow_register_3_out1,
       flow_register_3_out3, ForEX, IAddr, ID_IR, IF_IR, MEM_IR, mEPC_q, mips_ram_1_p7, multiplexer_1_out,
       multiplexer_2_out, multiplexer_4_out, multiplexer_5_out, multiplexer_10_out, multiplexer_11_out,
       multiplexer_12_out, multiplexer_14_out, multiplexer_15_out, PCOffset, regifile_1_r1, regifile_1_r2,
       shifter_2_out, WB_IR;

  Button \u_总复位  (.out(RST));
  Button _1 (.out(IR1));
  Button _2 (.out(IR2));
  Button _3 (.out(IR3));
  // Probe on \总周期数 
  // Probe on \总周期数 
  Button \u_继续运行  (.out(Go));
  LED #(.active("true")) led_1 (.in(W1));
  LED #(.active("true")) led_2 (.in(W2));
  LED #(.active("true")) led_3 (.in(W3));
  Hex_Digit_Display hex_digit_display_1 (.value(LedData[31:28]));  // open: dp
  // Probe on IF_PC[19:0]
  // RiscV_Probe riscv_probe_1: pin names not known; wires that end beside it: IF_IR
  Hex_Digit_Display hex_digit_display_2 (.value(LedData[23:20]));  // open: dp
  Hex_Digit_Display hex_digit_display_3 (.value(LedData[27:24]));  // open: dp
  // Probe on ID_PC[19:0]
  // RiscV_Probe riscv_probe_2: pin names not known; wires that end beside it: ID_IR
  Register #(.width(16), .trigger("rising"), .Select("low")) \u_周期  (
    .D(adder_1_out), .en(not_1_out), .Q(\总周期数 ), .clk(CLK), .clr(RST));
  not not_1 (not_1_out, halt);
  Multiplexer #(.select(1), .width(32), .disabled("Z"), .enable("false")) multiplexer_1 (
    .in0(multiplexer_5_out), .in1(IAddr), .out(multiplexer_1_out), .sel(or_1_out));
  or or_1 (or_1_out, URET, IRespond);
  Hex_Digit_Display hex_digit_display_4 (.value(LedData[15:12]));  // open: dp
  Hex_Digit_Display hex_digit_display_5 (.value(LedData[19:16]));  // open: dp
  Hex_Digit_Display hex_digit_display_6 (.value(LedData[11:8]));  // open: dp
  Hex_Digit_Display hex_digit_display_7 (.value(LedData[7:4]));  // open: dp
  // Probe on EX_PC[19:0]
  // RiscV_Probe riscv_probe_3: pin names not known; wires that end beside it: EX_IR
  Adder #(.width(16)) adder_1 (.a(\总周期数 ), .b(16'h1), .out(adder_1_out));  // open: cin, cout
  Register #(.width(32), .trigger("rising"), .Select("low")) PC (
    .D(multiplexer_1_out), .en(Stall), .Q(IF_PC), .clk(CLK), .clr(RST));
  Multiplexer #(.select(2), .width(32), .disabled("Z"), .enable("false")) multiplexer_2 (
    .in1(32'h30ac), .in2(32'h3150), .in3(32'h31f4), .out(multiplexer_2_out), .sel(IREncode));  // open: in0
  Hex_Digit_Display hex_digit_display_8 (.value(LedData[3:0]));  // open: dp
  not not_2 (not_2_out, halt);
  Adder #(.width(32)) adder_2 (.a(EX_PC), .b(PCOffset), .out(adder_2_out));  // open: cin, cout
  Register #(.width(32), .trigger("rising"), .Select("low")) mEPC (
    .D(multiplexer_5_out), .en(IRespond), .Q(mEPC_q), .clk(CLK));  // open: clr
  Multiplexer #(.select(1), .width(32), .disabled("Z"), .enable("false")) multiplexer_3 (
    .in0(multiplexer_2_out), .in1(mEPC_q), .out(IAddr), .sel(URET));
  // Probe on \总周期数 
  // Probe on M_PC[19:0]
  // RiscV_Probe riscv_probe_4: pin names not known; wires that end beside it: MEM_IR
  Register #(.width(1), .trigger("falling"), .Select("low")) u_Halt (
    .D(go_halt), .en(not_2_out), .Q(halt), .clk(CLK), .clr(Go));
  Adder #(.width(32)) adder_3 (.a(IF_PC), .b(32'h4), .out(adder_3_out));  // open: cin, cout
  Multiplexer #(.select(1), .width(32), .disabled("Z"), .enable("false")) multiplexer_4 (
    .in0(adder_2_out), .in1(ALUO), .out(multiplexer_4_out), .sel(JALR));
  Multiplexer #(.select(1), .width(32), .disabled("Z"), .enable("false")) multiplexer_5 (
    .in0(adder_3_out), .in1(multiplexer_4_out), .out(multiplexer_5_out), .sel(PCSrc));
  // Probe on \总周期数 
  // Probe on \无条件分支数 
  // Probe on \条件分支成功数 
  // Probe on \插入气泡数 
  // Probe on \LoadUse次数 
  ROM #(.addrWidth(10), .dataWidth(32), .Select("high")) rom_1 (.addr(IF_PC[11:2]), .data(IF_IR));
  Fowarding_Logic fowarding_logic_1 (
    .Ex_RegWrite(flow_register_bit_1_out7), .PCSrc(PCSrc), .Stall(Stall), .Flush(Flush),
    .MEM_RegWrite(EX_MEM_out3), .Rs(Rs), .Rt(Rt), .ExAddr(flow_register_1_outrd),
    .MEMAddr(flow_register_2_outrd), .RsUsed(RsUsed), .RtUsed(RtUsed),
    .RsForward(fowarding_logic_1_rsforward), .RtForward(fowarding_logic_1_rtforward), .Ex_MemRead(MEMRead));
  // Probe on IF_PC[11:0]
  // Probe on WB_PC[19:0]
  // RiscV_Probe riscv_probe_5: pin names not known; wires that end beside it: WB_IR
  Register #(.width(16), .trigger("rising"), .Select("low")) \u_无条件分支数  (
    .D(adder_4_out), .Q(\无条件分支数 ), .clk(CLK), .clr(RST));  // open: en
  or or_2 (or_2_out, JAL, JALR);
  // Probe on EX_PC[11:0]
  // Probe on ID_PC[11:0]
  Flow_Register IF_ID (
    .IN1(IF_IR), .Flush(PCSrc), .CLK(CLK), .OUT1(ID_IR), .PC2(IF_PC), .PC2_2(ID_PC), .RST(RST), .EN(Stall));  // open: PC, PC_2, IN2, OUT2, IN3, OUT3, IN4, OUT4, INrd, OUTrd, INcor, OUTcor, INForA, OUTForA
  assign bit_extender_1_out = {{15{1'b0}}, or_2_out};  // Bit_Extender bit_extender_1
  // Probe on M_PC[11:0]
  D_Flip_Flop #(.trigger("high"), .Pre_Clr_Positions("LEGACY"), .NegatePresetClear("false"), .enable("true"), .NewFFLayout("false")) d_ff_1 (.Q(d_ff_1_q));  // open: clk, D, Qn, preset, en, reset
  // Probe on 13'h377
  Adder #(.width(16)) adder_4 (.a(\无条件分支数 ), .b(bit_extender_1_out), .out(adder_4_out));  // open: cin, cout
  // Probe on WB_PC[11:0]
  Comparator #(.width(13), .mode("twosComplement")) comparator_1 (
    .a(CNT_num), .b(13'h377), .eq(comparator_1_eq), .lt(comparator_1_lt));  // open: gt
  Clock #(.highDuration(1), .lowDuration(1)) clock_1 (.out(clock_1_out));
  \单周期硬布线控制器  \u_单周期硬布线控制器_1  (
    .Funct({ID_IR[30], ID_IR[25], ID_IR[14:12]}), .OP(ID_IR[6:2]), .ALU_OP(\单周期硬布线控制器_1_alu_op ),
    .MemToReg(\单周期硬布线控制器_1_memtoreg ), .MemWrite(\单周期硬布线控制器_1_memwrite ), .ALU_SRC(\单周期硬布线控制器_1_alu_src ),
    .RegWrite(\单周期硬布线控制器_1_regwrite ), .ecall(\单周期硬布线控制器_1_ecall ), .S_type(SType),
    .Jalr(\单周期硬布线控制器_1_jalr ), .Beq(\单周期硬布线控制器_1_beq ), .JAL(\单周期硬布线控制器_1_jal ), .Bne(\单周期硬布线控制器_1_bne ),
    .IR(ID_IR[21]), .uret(URET), .Bge(\单周期硬布线控制器_1_bge ), .sb(\单周期硬布线控制器_1_sb ), .ALT(\单周期硬布线控制器_1_alt ),
    .RsUsed(RsUsed), .RtUsed(RtUsed));  // open: IRE, IRD, LUI, BLT
  Multiplexer #(.select(1), .width(5), .disabled("Z"), .enable("false")) multiplexer_6 (
    .in0(ID_IR[19:15]), .in1(5'b01010), .out(Rs), .sel(\单周期硬布线控制器_1_ecall ));
  Multiplexer #(.select(1), .width(5), .disabled("Z"), .enable("false")) multiplexer_7 (
    .in0(ID_IR[24:20]), .in1(5'b10001), .out(Rt), .sel(\单周期硬布线控制器_1_ecall ));
  Multiplexer #(.select(1), .width(12), .disabled("Z"), .enable("false")) multiplexer_8 (
    .in0(ID_IR[31:20]), .in1({ID_IR[31:25], ID_IR[11:7]}), .out(multiplexer_8_out), .sel(SType));
  nand nand_1 (nand_1_out, d_ff_1_q, comparator_1_eq);
  Counter #(.width(13), .max('h1fff), .ongoal("stay"), .trigger("rising"), .behavior("old")) counter_1 (
    .count(comparator_1_lt), .Q(CNT_num), .clk(clock_1_out));  // open: load, D, carry, clr, preset
  assign bit_extender_2_out = {{20{multiplexer_8_out[11]}}, multiplexer_8_out};  // Bit_Extender bit_extender_2
  assign bit_extender_3_out = {{8{ID_IR[31]}}, {ID_IR[31], ID_IR[7], ID_IR[30:25], ID_IR[11:8]}};  // Bit_Extender bit_extender_3
  Multiplexer #(.select(1), .width(20), .disabled("Z"), .enable("false")) multiplexer_9 (
    .in0(bit_extender_3_out), .in1({ID_IR[31], ID_IR[19:12], ID_IR[20], ID_IR[30:21]}),
    .out(multiplexer_9_out), .sel(\单周期硬布线控制器_1_jal ));
  assign controlled_buffer_1_out = nand_1_out ? clock_1_out : 1'bz;  // Controlled_Buffer controlled_buffer_1
  Regifile regifile_1 (
    .Din(RDin), .Clk(CLK), .R1(regifile_1_r1), .R2(regifile_1_r2), .WE(RegWrite), .W_num(WBAddr),
    .R1_num(Rs), .R2_num(Rt));
  not not_3 (not_3_out, JAL);
  not not_4 (not_4_out, JALR);
  Pull_Resistor #(.pull(1)) pull_resistor_1 (.node(controlled_buffer_1_out));
  assign bit_extender_4_out = {{12{multiplexer_9_out[19]}}, multiplexer_9_out};  // Bit_Extender bit_extender_4
  Register #(.width(16), .trigger("rising"), .Select("low")) \u_条件分支成功数  (
    .D(adder_5_out), .Q(\条件分支成功数 ), .clk(CLK), .clr(RST));  // open: en
  and and_1 (and_1_out, not_3_out, PCSrc, not_4_out);
  not not_5 (not_5_out, halt);
  Flow_Register_Bit ID_EX (
    .IN4(\单周期硬布线控制器_1_alt ), .IN3(\单周期硬布线控制器_1_jal ), .IN2(\单周期硬布线控制器_1_jalr ), .IN5(\单周期硬布线控制器_1_bge ),
    .IN6(\单周期硬布线控制器_1_sb ), .IN1(\单周期硬布线控制器_1_ecall ), .OUT4(ALT), .OUT3(JAL), .OUT2(JALR), .OUT5(Bge),
    .OUT6(ID_EX_out6), .OUT1(ecall), .Flush(Flush), .CLK(CLK), .RST(RST));  // open: IN7, OUT7, ALUOPIN, ALUOPOut, EN
  Flow_Register_Bit flow_register_bit_1 (
    .IN4(\单周期硬布线控制器_1_beq ), .IN3(\单周期硬布线控制器_1_bne ), .IN2(\单周期硬布线控制器_1_memtoreg ),
    .IN5(\单周期硬布线控制器_1_memwrite ), .IN1(\单周期硬布线控制器_1_alu_src ), .OUT4(flow_register_bit_1_out4),
    .OUT3(flow_register_bit_1_out3), .OUT2(MEMRead), .OUT5(flow_register_bit_1_out5),
    .OUT1(flow_register_bit_1_out1), .Flush(Flush), .CLK(CLK), .RST(RST), .IN7(\单周期硬布线控制器_1_regwrite ),
    .OUT7(flow_register_bit_1_out7), .ALUOPIN(\单周期硬布线控制器_1_alu_op ), .ALUOPOut(flow_register_bit_1_aluopout));  // open: IN6, OUT6, EN
  Flow_Register flow_register_1 (
    .IN1(regifile_1_r1), .Flush(Flush), .CLK(CLK), .OUT1(flow_register_1_out1), .PC(ID_IR), .PC_2(EX_IR),
    .PC2(ID_PC), .PC2_2(EX_PC), .RST(RST), .IN2(regifile_1_r2), .OUT2(flow_register_1_out2),
    .IN3(bit_extender_4_out), .OUT3(flow_register_1_out3), .IN4(bit_extender_2_out),
    .OUT4(flow_register_1_out4), .INrd(ID_IR[11:7]), .OUTrd(flow_register_1_outrd),
    .INcor(fowarding_logic_1_rsforward), .OUTcor(flow_register_1_outcor),
    .INForA(fowarding_logic_1_rtforward), .OUTForA(flow_register_1_outfora));  // open: EN
  assign bit_extender_5_out = {{15{1'b0}}, and_1_out};  // Bit_Extender bit_extender_5
  and and_2 (CLK, controlled_buffer_1_out, not_5_out);
  Multiplexer #(.select(2), .width(32), .disabled("Z"), .enable("false")) multiplexer_10 (
    .in0(flow_register_1_out1), .in1(RDin), .in2(ForEX), .out(multiplexer_10_out),
    .sel(flow_register_1_outcor));  // open: in3
  Multiplexer #(.select(2), .width(32), .disabled("Z"), .enable("false")) multiplexer_11 (
    .in0(flow_register_1_out2), .in1(RDin), .in2(ForEX), .out(multiplexer_11_out),
    .sel(flow_register_1_outfora));  // open: in3
  Adder #(.width(16)) adder_5 (.a(\条件分支成功数 ), .b(bit_extender_5_out), .out(adder_5_out));  // open: cin, cout
  Multiplexer #(.select(1), .width(32), .disabled("Z"), .enable("false")) multiplexer_12 (
    .in0(multiplexer_11_out), .in1(flow_register_1_out4), .out(multiplexer_12_out),
    .sel(flow_register_bit_1_out1));
  ALU alu_1 (
    .X(multiplexer_10_out), .Y(multiplexer_12_out), .AluOP(flow_register_bit_1_aluopout),
    .Equal(alu_1_equal), .Result(ALUO), .Result_2(alu_1_result_2), .out_4(alu_1_out_4));  // open: out_6
  Register #(.width(2), .trigger("rising"), .Select("low")) register_1 (
    .D(IREncode), .en(IRespond), .Q(register_1_q), .clk(CLK));  // open: clr
  Shifter #(.width(32), .shift("ll")) shifter_1 (.in(flow_register_1_out3), .\dist (5'b00001), .out(PCOffset));
  assign bit_extender_6_out = {{15{1'b0}}, PCSrc};  // Bit_Extender bit_extender_6
  assign bit_extender_7_out = {{15{1'b0}}, Flush};  // Bit_Extender bit_extender_7
  not not_6 (not_6_out, PCSrc);
  and and_3 (and_3_out, flow_register_bit_1_out3, not_7_out);
  not not_7 (not_7_out, alu_1_equal);
  Comparator #(.width(32), .mode("twosComplement")) comparator_2 (
    .a(multiplexer_11_out), .b(32'h22), .eq(comparator_2_eq));  // open: gt, lt
  not not_8 (not_8_out, comparator_2_eq);
  Multiplexer #(.select(2), .width(5), .disabled("Z"), .enable("false")) multiplexer_13 (
    .in0({5{1'b0}}), .in1(5'b01000), .in2(5'b10000), .in3(5'b11000), .out(multiplexer_13_out), .sel(ALUO[1:0]));
  Register #(.width(16), .trigger("rising"), .Select("low")) \u_气泡数  (
    .D(adder_7_out), .Q(\插入气泡数 ), .clk(CLK), .clr(RST));  // open: en
  Register #(.width(16), .trigger("rising"), .Select("low")) \LoadUse数  (
    .D(adder_8_out), .Q(\LoadUse次数 ), .clk(CLK), .clr(RST));  // open: en
  and and_4 (and_4_out, not_6_out, Flush);
  Demultiplexer #(.select(2), .width(1), .tristate("false"), .disabled("Z"), .enable("false")) demultiplexer_1 (
    .out1(demultiplexer_1_out1), .out2(demultiplexer_1_out2), .out3(demultiplexer_1_out3), .in(URET),
    .sel(register_1_q));  // open: out0
  and and_5 (and_5_out, alu_1_out_4, Bge);
  and and_6 (and_6_out, flow_register_bit_1_out4, alu_1_equal);
  and and_7 (and_7_out, ecall, comparator_2_eq);
  and and_8 (and_8_out, ecall, not_8_out);
  Multiplexer #(.select(1), .width(32), .disabled("Z"), .enable("false")) multiplexer_14 (
    .in0(ALUO), .in1(alu_1_result_2), .out(multiplexer_14_out), .sel(ALT));
  Shifter #(.width(32), .shift("ll")) shifter_2 (
    .in(multiplexer_11_out), .\dist (multiplexer_13_out), .out(shifter_2_out));
  Adder #(.width(16)) adder_6 (.a(bit_extender_6_out), .b(bit_extender_7_out), .out(adder_6_out));  // open: cin, cout
  assign bit_extender_8_out = {{15{1'b0}}, and_4_out};  // Bit_Extender bit_extender_8
  or or_3 (PCSrc, and_3_out, and_6_out, and_5_out, JAL, JALR);
  Register #(.width(32), .trigger("rising"), .Select("low")) LED_Register (
    .D(multiplexer_10_out), .en(and_7_out), .Q(LedData), .clk(CLK), .clr(RST));
  Adder #(.width(16)) adder_7 (.a(\插入气泡数 ), .b(adder_6_out), .out(adder_7_out));  // open: cin, cout
  Adder #(.width(16)) adder_8 (.a(\LoadUse次数 ), .b(bit_extender_8_out), .out(adder_8_out));  // open: cin, cout
  \中断按键参考电路  \u_中断按键参考电路_1  (
    .IRO(\中断按键参考电路_1_iro ), .\同步清零信号 (demultiplexer_1_out1), .IR(IR1), .IR_Light(W1), .CLK(CLK));  // open: IROI, IROI_CLR, IROR
  \中断按键参考电路  \u_中断按键参考电路_2  (
    .IRO(\中断按键参考电路_2_iro ), .\同步清零信号 (demultiplexer_1_out2), .IR(IR2), .IR_Light(W2), .CLK(CLK));  // open: IROI, IROI_CLR, IROR
  \中断按键参考电路  \u_中断按键参考电路_3  (
    .IRO(\中断按键参考电路_3_iro ), .\同步清零信号 (demultiplexer_1_out3), .IR(IR3), .IR_Light(W3), .CLK(CLK));  // open: IROI, IROI_CLR, IROR
  or or_4 (or_4_out, JALR, JAL);
  assign bit_extender_9_out = {{2{1'b0}}, ALUO[31:2]};  // Bit_Extender bit_extender_9
  Adder #(.width(32)) adder_9 (.a(32'h4), .b(EX_PC), .out(adder_9_out));  // open: cin, cout
  Multiplexer #(.select(1), .width(32), .disabled("Z"), .enable("false")) multiplexer_15 (
    .in0(multiplexer_14_out), .in1(adder_9_out), .out(multiplexer_15_out), .sel(or_4_out));
  Priority_Encoder #(.select(2), .disabled("Z")) priority_encoder_1 (
    .in1(\中断按键参考电路_1_iro ), .in2(\中断按键参考电路_2_iro ), .in3(\中断按键参考电路_3_iro ), .out(IREncode),
    .gs(priority_encoder_1_gs));  // open: in0, en_out, en_in
  Flow_Register_Bit EX_MEM (
    .IN3(flow_register_bit_1_out7), .IN2(ID_EX_out6), .IN5(MEMRead), .IN1(flow_register_bit_1_out5),
    .OUT3(EX_MEM_out3), .OUT2(sb), .OUT5(EX_MEM_out5), .OUT1(MemWrite), .Flush(1'b0), .CLK(CLK), .RST(RST),
    .IN7(and_8_out), .OUT7(EX_MEM_out7));  // open: IN4, IN6, OUT4, OUT6, ALUOPIN, ALUOPOut, EN
  Flow_Register flow_register_2 (
    .IN1(multiplexer_15_out), .Flush(1'b0), .CLK(CLK), .OUT1(ForEX), .PC(EX_IR), .PC_2(MEM_IR), .PC2(EX_PC),
    .PC2_2(M_PC), .RST(RST), .IN3(shifter_2_out), .OUT3(MDin), .IN4(bit_extender_9_out),
    .OUT4(flow_register_2_out4), .INrd(flow_register_1_outrd), .OUTrd(flow_register_2_outrd),
    .INcor(ALUO[1:0]), .OUTcor(flow_register_2_outcor));  // open: IN2, OUT2, EN, INForA, OUTForA
  and and_9 (IRespond, priority_encoder_1_gs, IE);
  Bit_Extender #(.in_width(32), .out_width(20), .\type ("zero")) bit_extender_10 (
    .in(flow_register_2_out4), .out(bit_extender_10_out));
  Shifter #(.width(4), .shift("ll")) shifter_3 (.in(4'b0001), .\dist (flow_register_2_outcor), .out(shifter_3_out));
  not not_9 (not_9_out, IRespond);
  Comparator #(.width(16), .mode("twosComplement")) comparator_3 (
    .a(\总周期数 ), .b({16{1'b0}}), .eq(comparator_3_eq));  // open: gt, lt
  // MIPS_RAM mips_ram_1: pin names not known; wires that end beside it: bit_extender_10_out, MDin, MemWrite, MemSel, CLK, RST, mips_ram_1_p7, MEM_IR
  Multiplexer #(.select(1), .width(4), .disabled("Z"), .enable("false")) multiplexer_16 (
    .in0(4'b1111), .in1(shifter_3_out), .out(MemSel), .sel(sb));
  or or_5 (or_5_out, IRespond, URET);
  Register #(.width(1), .trigger("rising"), .Select("low")) u_IE (
    .D(not_9_out), .en(or_5_out), .Q(IE), .clk(CLK), .preset(comparator_3_eq));  // open: clr, cs
  Flow_Register_Bit MEM_WB (
    .IN3(EX_MEM_out3), .IN5(EX_MEM_out5), .OUT3(RegWrite), .OUT5(MTR), .Flush(1'b0), .CLK(CLK), .RST(RST),
    .IN7(EX_MEM_out7), .OUT7(go_halt));  // open: IN4, IN2, IN6, IN1, OUT4, OUT2, OUT6, OUT1, ALUOPIN, ALUOPOut, EN
  Flow_Register flow_register_3 (
    .IN1(ForEX), .Flush(1'b0), .CLK(CLK), .OUT1(flow_register_3_out1), .PC(MEM_IR), .PC_2(WB_IR), .PC2(M_PC),
    .PC2_2(WB_PC), .RST(RST), .IN3(mips_ram_1_p7), .OUT3(flow_register_3_out3), .INrd(flow_register_2_outrd),
    .OUTrd(WBAddr));  // open: IN2, OUT2, IN4, OUT4, INcor, OUTcor, EN, INForA, OUTForA
  Multiplexer #(.select(1), .width(32), .disabled("Z"), .enable("false")) multiplexer_17 (
    .in0(flow_register_3_out1), .in1(flow_register_3_out3), .out(RDin), .sel(MTR));

  // Other names for the same wires on the sheet: ForMEM[31:0] = RDin; MEM_PC[31:0] = M_PC; PCSig[31:0] = EX_PC

  // Notes on the sheet:
  //   中断源
  //   时空图监测，可删除
  //   中断等待指示
  //   数码管输出
  //   指令存储器
  //   contents of rom_1 (hex, n*v repeats v):
  //   100493 100006f 100493 200913 300993 100006f 100493 200913 300993 100006f 100493 200913 300993
  //   100006f 100493 200913 300993 394000ef 100413 100493 1f49493 900533 2200893 73 24d493 48463 fedff06f
  //   900533 2200893 73 100493 249493 900533 2200893 73 48463 fedff06f 100493 1f49493 900533 2200893 73
  //   4034d493 900533 2200893 73 4044d493 900533 2200893 73 4044d493 900533 2200893 73 4044d493 900533
  //   2200893 73 4044d493 900533 2200893 73 4044d493 900533 2200893 73 4044d493 900533 2200893 73 4044d493
  //   900533 2200893 73 100413 1f41993 41f9d993 433 c00913 300b13 140413 f47413 800293 100313 499993
  //   89e9b3 1300533 2200893 73 406282b3 fe0294e3 140413 f00f93 1f47433 1c41413 800293 100313 49d993
  //   89e9b3 1300533 2200893 73 406282b3 fe0294e3 1c45413 406b0b33 b0463 f95ff06f 2b3 fff2c293 829293
  //   ff2e293 500533 2200893 73 fff00413 493 84a023 140413 448493 84a023 140413 448493 84a023 140413
  //   448493 84a023 140413 448493 84a023 140413 448493 84a023 140413 448493 84a023 140413 448493 84a023
  //   140413 448493 84a023 140413 448493 84a023 140413 448493 84a023 140413 448493 84a023 140413 448493
  //   84a023 140413 448493 84a023 140413 448493 84a023 140413 448493 84a023 140413 448493 140413 433
  //   3c00493 42983 4aa03 149a2b3 28663 134a023 1442023 ffc48493 fe9412e3 800533 2200893 73 440413 3c00493
  //   fc9416e3 200293 1100493 849493 1148493 1049493 900533 2200893 73 1c00e13 254d4b3 900533 2200893 73
  //   fffe0e13 fe0e16e3 a00893 73 8800493 849493 4848493 8700913 891913 5490913 2997933 1091913 11096913
  //   1200533 2200893 73 a00893 73 313 2000e13 493 100913 930023 900533 2200893 73 12484b3 130313 fffe0e13
  //   fe0e12e3 800e13 313 32483 900533 2200893 73 430313 fffe0e13 fe0e14e3 a00893 73 f00493 900533 2200893
  //   73 fff48493 fe04d8e3 a00893 73 a00893 73 413 140413 800533 2200893 73 240413 800533 2200893 73
  //   340413 800533 2200893 73 440413 800533 2200893 73 540413 800533 2200893 73 640413 800533 2200893 73
  //   740413 800533 2200893 73 840413 800533 2200893 2200893 73 8067
  //   控制位
  //   指令字
  //   流水调试日志用
  //   暂停节拍，不能为0
  //   JAL
  //   JALR
  //   URET
  //   Bge
  //   BEQ offset
  //   JAL offset
  //   戳工具置1进入计数暂停模式，ctrl+k时钟自动运行到对应节拍暂停
  //   ctrl+k关闭时钟连续运行，将控制位置零，进入单步调试模式调试
  //   用这个时钟源需要去掉电路中的其他时钟源
  //   Beq
  //   Bne
  //   MemToReg
  //   MemWrite
  //   AluOP
  //   AluSrcB
  //   RegWrite
  //   S_Type
  //   ecall
  //   可计数暂停的时钟源
  //   rd
  //   为方便自动评测，需要输出流水线各段保存的PC值，注意是PC不是PC+4，另外ID段寄存器写入信息，Mem段内存写入信息也要输出
  //   Beq Judge
  //   Bne Judge
  //   Bge Judge
  //   rd
  //   rd
endmodule

module \中断按键参考电路  (
  input  IROI_CLR,
  input  CLK,
  input  IR,
  input  \同步清零信号 ,
  output IROI,
  output IRO,
  output IROR,
  output IR_Light
);

  wire and_1_out, and_2_out, d_ff_1_q, IRRunning_qn, or_2_out, or_3_out, or_4_out;

  or or_1 (IR_Light, IRO, d_ff_1_q);
  D_Flip_Flop #(.trigger("rising"), .Pre_Clr_Positions("LEGACY"), .NegatePresetClear("false"), .enable("true"), .NewFFLayout("false")) d_ff_1 (
    .clk(IR), .D(1'b1), .Q(d_ff_1_q), .reset(IRO));  // open: Qn, preset, en
  or or_2 (or_2_out, d_ff_1_q, IRO);
  and and_1 (and_1_out, or_2_out, ~\同步清零信号 );  // AND_Gate
  D_Flip_Flop #(.trigger("rising"), .Pre_Clr_Positions("LEGACY"), .NegatePresetClear("false"), .enable("true"), .NewFFLayout("false")) IR1 (
    .clk(CLK), .D(and_1_out), .Q(IRO));  // open: Qn, preset, en, reset
  and and_2 (and_2_out, and_1_out, IRRunning_qn);
  or or_3 (or_3_out, IROI_CLR, IROR);
  D_Flip_Flop #(.trigger("falling"), .Pre_Clr_Positions("LEGACY"), .NegatePresetClear("false"), .enable("true"), .NewFFLayout("false")) IR2 (
    .clk(CLK), .D(and_2_out), .Q(IROI), .en(or_3_out));  // open: Qn, preset, reset
  D_Flip_Flop #(.trigger("rising"), .Pre_Clr_Positions("LEGACY"), .NegatePresetClear("false"), .enable("true"), .NewFFLayout("false")) IRRunning (
    .clk(CLK), .D(and_1_out), .Q(IROR), .Qn(IRRunning_qn), .en(or_4_out));  // open: preset, reset
  or or_4 (or_4_out, IROI_CLR, \同步清零信号 );

  // Notes on the sheet:
  //   中断信号采样参考电路
  //   Reset 
endmodule

module \单周期_单级中断  (
  input  IR1,
  input  IR2,
  input  IR3,
  input  [31:0] Dir,
  output CLK,
  output [31:0] LedData,
  output LEDGO,
  output [31:0] LEDOUT
);

  wire ALT, alu_1_equal, alu_1_out_4, and_1_out, and_3_out, and_4_out, and_5_out, and_6_out, and_7_out,
       and_9_out, Bge, BLT, clock_1_out, comparator_1_eq, comparator_1_lt, comparator_2_eq, comparator_3_eq,
       comparator_4_eq, d_ff_1_q, demultiplexer_1_out1, demultiplexer_1_out2, demultiplexer_1_out3, ecall,
       Go, go_halt, halt, IE, IR1_t, IR2_t, IR3_t, IRA, IRB, IRC, IRespond, JAL, JALR, LUI, MemWrite, MTR,
       nand_1_out, not_1_out, not_2_out, not_3_out, not_4_out, not_5_out, not_6_out, or_2_out, or_4_out,
       or_6_out, or_7_out, PCSrc, priority_encoder_1_gs, RegWrite, RST, sb, Smaller, SPEC, SType, URET, W1,
       W2, W3, \中断按键参考电路_1_iro , \中断按键参考电路_2_iro , \中断按键参考电路_3_iro , \单周期硬布线控制器_1_alu_src ,
       \单周期硬布线控制器_1_beq , \单周期硬布线控制器_1_bne ;
  wire [1:0] IREncode, register_1_q;
  wire [3:0] MemSel, shifter_4_out, \单周期硬布线控制器_1_alu_op ;
  wire [4:0] multiplexer_6_out, multiplexer_7_out, multiplexer_13_out;
  wire [11:0] multiplexer_8_out;
  wire [12:0] CNT_num;
  wire [15:0] adder_1_out, \总周期数 ;
  wire [19:0] bit_extender_1_out, multiplexer_9_out, shifter_2_out;
  wire [23:0] bit_extender_5_out;
  wire [31:0] adder_2_out, adder_3_out, alu_1_result, alu_1_result_2, ALUO, bit_extender_2_out,
       bit_extender_3_out, IAddr, IR, MDin, mEPC_q, mips_ram_1_p7, multiplexer_1_out, multiplexer_2_out,
       multiplexer_3_out, multiplexer_4_out, multiplexer_11_out, multiplexer_12_out, multiplexer_16_out,
       multiplexer_18_out, PC, PCOffset, RDin, regifile_1_r2, shifter_1_out, shifter_3_out;

  Button \u_继续运行  (.out(Go));
  Button _1 ();  // open: out
  Button _2 ();  // open: out
  Button _3 ();  // open: out
  LED #(.active("true")) led_1 (.in(W1));
  LED #(.active("true")) led_2 (.in(W2));
  LED #(.active("true")) led_3 (.in(W3));
  Pull_Resistor #(.pull(0)) pull_resistor_1 (.node(IRA));
  Pull_Resistor #(.pull(0)) pull_resistor_2 (.node(IRB));
  Pull_Resistor #(.pull(0)) pull_resistor_3 (.node(IRC));
  not not_1 (not_1_out, halt);
  or or_1 (IR1_t, IR1, IRA);
  Register #(.width(16), .trigger("rising"), .Select("low")) \u_周期  (
    .D(adder_1_out), .en(not_1_out), .Q(\总周期数 ), .clk(CLK), .clr(RST));
  or or_2 (or_2_out, Go, and_1_out);
  not not_2 (not_2_out, go_halt);
  or or_3 (IR2_t, IR2, IRB);
  and and_1 (and_1_out, not_2_out, not_3_out);
  not not_3 (not_3_out, halt);
  Multiplexer #(.select(1), .width(32), .disabled("Z"), .enable("false")) multiplexer_1 (
    .in0(multiplexer_3_out), .in1(IAddr), .out(multiplexer_1_out), .sel(or_4_out));
  or or_4 (or_4_out, URET, IRespond);
  Adder #(.width(16)) adder_1 (.a(\总周期数 ), .b(16'h1), .out(adder_1_out));  // open: cin, cout
  Register #(.width(32), .trigger("rising"), .Select("low")) u_PC (
    .D(multiplexer_1_out), .en(or_2_out), .Q(PC), .clk(CLK), .clr(RST));
  or or_5 (IR3_t, IR3, IRC);
  Adder #(.width(32)) adder_2 (.a(PC), .b(PCOffset), .out(adder_2_out));  // open: cin, cout
  Register #(.width(1), .trigger("rising"), .Select("low")) u_Halt (.D(go_halt), .Q(halt), .clk(CLK));  // open: en, clr
  Adder #(.width(32)) adder_3 (.a(PC), .b(32'h4), .out(adder_3_out));  // open: cin, cout
  Multiplexer #(.select(1), .width(32), .disabled("Z"), .enable("false")) multiplexer_2 (
    .in0(adder_2_out), .in1(ALUO), .out(multiplexer_2_out), .sel(JALR));
  Multiplexer #(.select(1), .width(32), .disabled("Z"), .enable("false")) multiplexer_3 (
    .in0(adder_3_out), .in1(multiplexer_2_out), .out(multiplexer_3_out), .sel(PCSrc));
  ROM #(.addrWidth(10), .dataWidth(32), .Select("high")) rom_1 (.addr(PC[11:2]), .data(IR));
  Register #(.width(32), .trigger("rising"), .Select("low")) mEPC (
    .D(multiplexer_3_out), .en(IRespond), .Q(mEPC_q), .clk(CLK));  // open: clr
  // RiscV_Probe riscv_probe_1: pin names not known; wires that end beside it: IR
  Multiplexer #(.select(2), .width(32), .disabled("Z"), .enable("false")) multiplexer_4 (
    .in1(32'h7b8), .in2(32'h3150), .in3(32'h31f4), .out(multiplexer_4_out), .sel(IREncode));  // open: in0
  Multiplexer #(.select(1), .width(32), .disabled("Z"), .enable("false")) multiplexer_5 (
    .in0(multiplexer_4_out), .in1(mEPC_q), .out(IAddr), .sel(URET));
  Register #(.width(2), .trigger("rising"), .Select("low")) register_1 (
    .D(IREncode), .en(IRespond), .Q(register_1_q), .clk(CLK));  // open: clr
  \单周期硬布线控制器  \u_单周期硬布线控制器_1  (
    .Funct({IR[30], IR[25], IR[14:12]}), .OP(IR[6:2]), .ALU_OP(\单周期硬布线控制器_1_alu_op ), .MemToReg(MTR),
    .MemWrite(MemWrite), .ALU_SRC(\单周期硬布线控制器_1_alu_src ), .RegWrite(RegWrite), .ecall(ecall), .S_type(SType),
    .Jalr(JALR), .Beq(\单周期硬布线控制器_1_beq ), .JAL(JAL), .Bne(\单周期硬布线控制器_1_bne ), .IR(IR[21]), .uret(URET),
    .Bge(Bge), .sb(sb), .ALT(ALT), .LUI(LUI), .BLT(BLT));  // open: RsUsed, RtUsed, IRE, IRD
  Multiplexer #(.select(1), .width(5), .disabled("Z"), .enable("false")) multiplexer_6 (
    .in0(IR[19:15]), .in1(5'b01010), .out(multiplexer_6_out), .sel(ecall));
  Multiplexer #(.select(1), .width(5), .disabled("Z"), .enable("false")) multiplexer_7 (
    .in0(IR[24:20]), .in1(5'b10001), .out(multiplexer_7_out), .sel(ecall));
  Multiplexer #(.select(1), .width(12), .disabled("Z"), .enable("false")) multiplexer_8 (
    .in0(IR[31:20]), .in1({IR[31:25], IR[11:7]}), .out(multiplexer_8_out), .sel(SType));
  assign bit_extender_1_out = {{8{IR[31]}}, {IR[31], IR[7], IR[30:25], IR[11:8]}};  // Bit_Extender bit_extender_1
  assign bit_extender_2_out = {{12{IR[31]}}, IR[31:12]};  // Bit_Extender bit_extender_2
  Shifter #(.width(32), .shift("ll")) shifter_1 (.in(bit_extender_2_out), .\dist (5'b01100), .out(shifter_1_out));
  D_Flip_Flop #(.trigger("high"), .Pre_Clr_Positions("LEGACY"), .NegatePresetClear("false"), .enable("true"), .NewFFLayout("false")) d_ff_1 (.Q(d_ff_1_q));  // open: clk, D, Qn, preset, en, reset
  // Probe on 13'hbb
  Demultiplexer #(.select(2), .width(1), .tristate("false"), .disabled("Z"), .enable("false")) demultiplexer_1 (
    .out1(demultiplexer_1_out1), .out2(demultiplexer_1_out2), .out3(demultiplexer_1_out3), .in(URET),
    .sel(register_1_q));  // open: out0
  assign bit_extender_3_out = {{20{multiplexer_8_out[11]}}, multiplexer_8_out};  // Bit_Extender bit_extender_3
  Multiplexer #(.select(1), .width(20), .disabled("Z"), .enable("false")) multiplexer_9 (
    .in0(bit_extender_1_out), .in1({IR[31], IR[19:12], IR[20], IR[30:21]}), .out(multiplexer_9_out), .sel(JAL));
  Comparator #(.width(13), .mode("twosComplement")) comparator_1 (
    .a(CNT_num), .b(13'hbb), .eq(comparator_1_eq), .lt(comparator_1_lt));  // open: gt
  Clock #(.highDuration(1), .lowDuration(1)) clock_1 (.out(clock_1_out));
  Regifile regifile_1 (
    .Din(RDin), .Clk(CLK), .R1(LEDOUT), .R2({regifile_1_r2[31:7], SPEC, regifile_1_r2[5:0]}), .WE(RegWrite),
    .W_num(IR[11:7]), .R1_num(multiplexer_6_out), .R2_num(multiplexer_7_out));
  Multiplexer #(.select(1), .width(32), .disabled("Z"), .enable("false")) multiplexer_10 (
    .in0(multiplexer_12_out), .in1(shifter_1_out), .out(RDin), .sel(LUI));
  or or_6 (or_6_out, JALR, JAL);
  Counter #(.width(13), .max('h1fff), .ongoal("stay"), .trigger("rising"), .behavior("old")) counter_1 (
    .count(comparator_1_lt), .Q(CNT_num), .clk(clock_1_out));  // open: load, D, carry, clr, preset
  \中断按键参考电路  \u_中断按键参考电路_1  (
    .IRO(\中断按键参考电路_1_iro ), .\同步清零信号 (demultiplexer_1_out1), .IR(IR1_t), .IR_Light(W1), .CLK(CLK));  // open: IROI, IROI_CLR, IROR
  \中断按键参考电路  \u_中断按键参考电路_2  (
    .IRO(\中断按键参考电路_2_iro ), .\同步清零信号 (demultiplexer_1_out2), .IR(IR2_t), .IR_Light(W2), .CLK(CLK));  // open: IROI, IROI_CLR, IROR
  \中断按键参考电路  \u_中断按键参考电路_3  (
    .IRO(\中断按键参考电路_3_iro ), .\同步清零信号 (demultiplexer_1_out3), .IR(IR3_t), .IR_Light(W3), .CLK(CLK));  // open: IROI, IROI_CLR, IROR
  Multiplexer #(.select(1), .width(32), .disabled("Z"), .enable("false")) multiplexer_11 (
    .in0({regifile_1_r2[31:7], SPEC, regifile_1_r2[5:0]}), .in1(bit_extender_3_out),
    .out(multiplexer_11_out), .sel(\单周期硬布线控制器_1_alu_src ));
  Multiplexer #(.select(1), .width(32), .disabled("Z"), .enable("false")) multiplexer_12 (
    .in0(multiplexer_18_out), .in1(adder_3_out), .out(multiplexer_12_out), .sel(or_6_out));
  nand nand_1 (nand_1_out, d_ff_1_q, comparator_1_eq);
  ALU alu_1 (
    .X(LEDOUT), .Y(multiplexer_11_out), .AluOP(\单周期硬布线控制器_1_alu_op ), .Equal(alu_1_equal),
    .Result(alu_1_result), .Result_2(alu_1_result_2), .out_4(alu_1_out_4), .out_6(Smaller));
  Shifter #(.width(20), .shift("ll")) shifter_2 (.in(multiplexer_9_out), .\dist (5'b00001), .out(shifter_2_out));
  assign CLK = nand_1_out ? clock_1_out : 1'bz;  // Controlled_Buffer controlled_buffer_1
  Pull_Resistor #(.pull(1)) pull_resistor_4 (.node(CLK));
  Priority_Encoder #(.select(2), .disabled("Z")) priority_encoder_1 (
    .in1(\中断按键参考电路_1_iro ), .in2(\中断按键参考电路_2_iro ), .in3(\中断按键参考电路_3_iro ), .out(IREncode),
    .gs(priority_encoder_1_gs));  // open: in0, en_out, en_in
  Multiplexer #(.select(2), .width(5), .disabled("Z"), .enable("false")) multiplexer_13 (
    .in0({5{1'b0}}), .in1(5'b01000), .in2(5'b10000), .in3(5'b11000), .out(multiplexer_13_out),
    .sel(alu_1_result[1:0]));
  assign PCOffset = {{12{shifter_2_out[19]}}, shifter_2_out};  // Bit_Extender bit_extender_4
  and and_2 (IRespond, priority_encoder_1_gs, IE);
  Shifter #(.width(32), .shift("ll")) shifter_3 (
    .in({regifile_1_r2[31:7], SPEC, regifile_1_r2[5:0]}), .\dist (multiplexer_13_out), .out(shifter_3_out));
  not not_4 (not_4_out, alu_1_equal);
  Multiplexer #(.select(1), .width(32), .disabled("Z"), .enable("false")) multiplexer_14 (
    .in0(alu_1_result), .in1(alu_1_result_2), .out(ALUO), .sel(ALT));
  and and_3 (and_3_out, alu_1_out_4, Bge);
  and and_4 (and_4_out, \单周期硬布线控制器_1_bne , not_4_out);
  not not_5 (not_5_out, IRespond);
  or or_7 (or_7_out, IRespond, URET);
  Comparator #(.width(16), .mode("twosComplement")) comparator_2 (
    .a(\总周期数 ), .b({16{1'b0}}), .eq(comparator_2_eq));  // open: gt, lt
  and and_5 (and_5_out, \单周期硬布线控制器_1_beq , alu_1_equal);
  Comparator #(.width(6), .mode("twosComplement")) comparator_3 (
    .a(regifile_1_r2[5:0]), .b(6'b100010), .eq(comparator_3_eq));  // open: gt, lt
  Comparator #(.width(32), .mode("twosComplement")) comparator_4 (
    .a(shifter_3_out), .b(32'h1bf52), .eq(comparator_4_eq));  // open: gt, lt
  Shifter #(.width(4), .shift("ll")) shifter_4 (.in(4'b0001), .\dist (alu_1_result[1:0]), .out(shifter_4_out));
  Register #(.width(1), .trigger("rising"), .Select("low")) u_IE (
    .D(not_5_out), .en(or_7_out), .Q(IE), .clk(CLK), .preset(comparator_2_eq));  // open: clr, cs
  or or_8 (PCSrc, and_3_out, and_4_out, and_5_out, JAL, JALR, and_7_out);
  and and_6 (and_6_out, ecall, comparator_3_eq);
  not not_6 (not_6_out, comparator_3_eq);
  Multiplexer #(.select(1), .width(32), .disabled("Z"), .enable("false")) multiplexer_15 (
    .in0(shifter_3_out), .in1(multiplexer_16_out), .out(MDin), .sel(W1));
  Multiplexer #(.select(1), .width(32), .disabled("Z"), .enable("false")) multiplexer_16 (
    .in0(shifter_3_out), .in1(Dir), .out(multiplexer_16_out), .sel(comparator_4_eq));
  Multiplexer #(.select(1), .width(4), .disabled("Z"), .enable("false")) multiplexer_17 (
    .in0(4'b1111), .in1(shifter_4_out), .out(MemSel), .sel(sb));
  and and_7 (and_7_out, Smaller, BLT);
  and and_8 (go_halt, ecall, not_6_out);
  Bit_Extender #(.in_width(30), .out_width(24), .\type ("zero")) bit_extender_5 (
    .in(alu_1_result[31:2]), .out(bit_extender_5_out));
  Register #(.width(32), .trigger("rising"), .Select("low")) LED_Register (
    .D(LEDOUT), .en(and_9_out), .Q(LedData), .clk(CLK), .clr(RST));
  and and_9 (and_9_out, and_6_out, SPEC);
  and and_10 (LEDGO, and_6_out, ~SPEC);  // AND_Gate
  // MIPS_RAM mips_ram_1: pin names not known; wires that end beside it: bit_extender_5_out, MDin, MemWrite, MemSel, CLK, RST, mips_ram_1_p7
  Multiplexer #(.select(1), .width(32), .disabled("Z"), .enable("false")) multiplexer_18 (
    .in0(ALUO), .in1(mips_ram_1_p7), .out(multiplexer_18_out), .sel(MTR));

  // Notes on the sheet:
  //   中断源
  //   中断等待指示
  //   总复位信号应将除ROM以外所有存储组件全部清零
  //   数码管输出应该用寄存器锁存，否则显示数据只能一闪而过
  //   指令存储器
  //   contents of rom_1 (hex, n*v repeats v):
  //   1e137 fd810113 7b7 78793 7a023 7b7 78793 100713 e7a223 7b7 78793 100713 e7a423 7b7 78793 7a623 7b7
  //   78793 fff00713 e7a823 7b7 78793 7aa23 7b7 78793 7ac23 7b7 78793 fff00713 e7ae23 27b7 bc78793 50737
  //   70713 2e7a423 27b7 bc78793 57737 70713 50070713 2e7a623 27b7 bc78793 25737 70713 50070713 2e7a823
  //   27b7 bc78793 27737 70713 70070713 2e7aa23 27b7 bc78793 20737 70713 2e7ac23 27b7 bc78793 400737 70713
  //   2070713 4e7a023 27b7 bc78793 473737 70713 72070713 4e7a223 27b7 bc78793 452737 70713 62070713
  //   4e7a423 27b7 bc78793 476737 70713 70070713 4e7a623 27b7 bc78793 700737 2070713 4e7a823 27b7 a00713
  //   2c78793 e7a023 27b7 500713 3078793 e7a023 27b7 3878793 7a023 17b7 1000713 2c78793 e7a023 17b7
  //   2c7a703 7b7 2c78793 e7a023 27b7 3c78793 10737 70713 4e7a023 7b7 247a783 178713 41f75793 167d793
  //   f70733 3ff77713 40f707b3 fef42023 7b7 247a703 7b7 271713 2c78793 f707b3 7a703 7b7 207a683 7b7 369693
  //   78793 f687b3 7a783 f70733 7b7 fe042683 269693 2c78793 f687b3 e7a023 7b7 247a703 17b7 271713 2c78793
  //   f707b3 7a703 7b7 207a683 7b7 369693 78793 f687b3 47a783 f70733 17b7 fe042683 269693 2c78793 f687b3
  //   e7a023 7b7 fe042703 2478793 e7a023 7b7 247a703 7b7 271713 2c78793 f707b3 7a783 4a07c463 7b7 247a703
  //   7b7 271713 2c78793 f707b3 7a703 1f00793 48e7c263 7b7 247a703 17b7 271713 2c78793 f707b3 7a783
  //   4607c263 7b7 247a703 17b7 271713 2c78793 f707b3 7a703 1f00793 44e7c063 7b7 247a703 7b7 271713
  //   2c78793 f707b3 7a703 27b7 2c7a783 1af71c63 7b7 247a703 17b7 271713 2c78793 f707b3 7a703 27b7 307a783
  //   18f71863 7b7 247a703 7b7 271713 2c78793 f707b3 7a703 27b7 271713 3c78793 f707b3 7a703 7b7 247a683
  //   17b7 269693 2c78793 f687b3 7a783 f757b3 17f793 fcf42e23 fdc42783 38079263 7b7 247a703 7b7 271713
  //   2c78793 f707b3 7a703 27b7 271713 3c78793 f707b3 7a703 7b7 247a683 17b7 269693 2c78793 f687b3 7a783
  //   100693 f697b3 6b7 246a603 6b7 261613 2c68693 d606b3 6a683 f76733 27b7 269693 3c78793 f687b3 e7a023
  //   27b7 2c7a703 e007b3 479793 e787b3 d78713 41f75793 1b7d793 f70733 1f77713 40f707b3 f00733 27b7
  //   2c78793 e7a023 27b7 307a703 e007b3 479793 e787b3 d78713 41f75793 1b7d793 f70733 1f77713 40f707b3
  //   f00733 27b7 3078793 e7a023 27b7 347a783 178713 27b7 3478793 e7a023 27b7 100713 3878793 e7a023
  //   1bc0006f 7b7 287a703 7b7 271713 2c78793 f707b3 7a703 27b7 271713 3c78793 f707b3 7a703 7b7 287a683
  //   17b7 269693 2c78793 f687b3 7a783 100693 f697b3 6b7 286a603 6b7 261613 2c68693 d606b3 6a683 f74733
  //   27b7 269693 3c78793 f687b3 e7a023 7b7 287a783 178713 41f75793 167d793 f70733 3ff77713 40f707b3
  //   f00733 7b7 2878793 e7a023 7b7 247a703 7b7 271713 2c78793 f707b3 7a703 27b7 271713 3c78793 f707b3
  //   7a703 7b7 247a683 17b7 269693 2c78793 f687b3 7a783 f757b3 17f793 fcf42c23 fd842783 14079463 7b7
  //   247a703 7b7 271713 2c78793 f707b3 7a703 27b7 271713 3c78793 f707b3 7a703 7b7 247a683 17b7 269693
  //   2c78793 f687b3 7a783 100693 f697b3 6b7 246a603 6b7 261613 2c68693 d606b3 6a683 f76733 27b7 269693
  //   3c78793 f687b3 e7a023 27b7 387a783 17c713 27b7 3878793 e7a023 fe042623 880006f 27b7 fec42703 271713
  //   3c78793 f707b3 7a783 fef42423 27b7 2c7a783 fec42703 4f71063 27b7 307a783 fe842703 f757b3 17f793 2737
  //   3872703 2e78063 27b7 307a783 100713 f717b3 fe842703 f747b3 fef42423 fe842783 f00533 2200893 73
  //   fec42783 178793 fef42623 fec42703 1f00793 f6e7dae3 a71ff06f 13 80006f 13 fe042223 380006f 27b7
  //   fe442703 271713 bc78793 f707b3 7a783 fcf42a23 f00533 2200893 73 fe442783 178793 fef42223 fe442703
  //   1f00793 fce7d2e3 793 f00533 a00893 73 d12023 410113 e12023 410113 f12023 410113 7b7 1c737 f5270713
  //   2078693 e6a023 ffc10113 12783 ffc10113 12703 ffc10113 12683 200073
  //   为方便自动评测，需要输出PC，IR，寄存器堆写如数据RDin
  //   指令探针
  //   RAM写使能MemWrite、RAM写入数据MDin等信号
  //   指令字
  //   JAL
  //   JALR
  //   URET
  //   Bge
  //   BEQ offset
  //   JAL offset
  //   Beq
  //   Bne
  //   MemToReg
  //   MemWrite
  //   AluOP
  //   AluSrcB
  //   RegWrite
  //   S_Type
  //   ecall
  //   rd
  //   控制位
  //   暂停节拍，不能为0
  //   可计数暂停的时钟源
  //   Bne Judge
  //   Beq Judge
  //   Bge Judge
endmodule

module \单周期_多级中断  (
  input  IR1,
  input  IR2,
  input  IR3,
  output RegWrite,
  output MemWrite,
  output CLK,
  output [31:0] PC,
  output [31:0] IR,
  output [31:0] RDin,
  output [31:0] MDin,
  output [31:0] LedData
);

  wire ALT, alu_1_equal, alu_1_out_4, and_1_out, and_2_out, and_3_out, and_4_out, and_6_out, and_8_out, Bge,
       clock_1_out, comparator_1_eq, comparator_2_eq, comparator_3_eq, comparator_4_eq, comparator_5_eq,
       comparator_6_eq, comparator_6_lt, comparator_7_eq, comparator_8_eq, d_ff_1_q, demultiplexer_1_out1,
       demultiplexer_1_out2, demultiplexer_1_out3, demultiplexer_2_out1, demultiplexer_2_out2,
       demultiplexer_2_out3, ecall, Go, go_halt, halt, IE, IR1_t, IR2_t, IR3_t, IRA, IRB, IRC, IRD, IRE,
       IRespond, JAL, JALR, MTR, nand_1_out, not_1_out, not_2_out, not_3_out, not_4_out, not_5_out,
       not_6_out, or_1_out, or_2_out, or_4_out, or_6_out, or_8_out, or_9_out, or_10_out, or_11_out,
       or_13_out, or_14_out, PCSrc, RST, sb, SType, URET, W1, W2, W3, \中断按键参考电路_1_iro , \中断按键参考电路_1_iroi ,
       \中断按键参考电路_1_iror , \中断按键参考电路_2_iro , \中断按键参考电路_2_iroi , \中断按键参考电路_2_iror , \中断按键参考电路_3_iro ,
       \中断按键参考电路_3_iroi , \中断按键参考电路_3_iror , \单周期硬布线控制器_1_alu_src , \单周期硬布线控制器_1_beq , \单周期硬布线控制器_1_bne ;
  wire [1:0] adder_4_out, IREncode, multiplexer_5_out, multiplexer_6_out, priority_encoder_1_out,
       Stack_Pointer_q;
  wire [3:0] MemSel, shifter_3_out, \单周期硬布线控制器_1_alu_op ;
  wire [4:0] multiplexer_8_out, multiplexer_9_out, multiplexer_15_out;
  wire [11:0] multiplexer_10_out;
  wire [12:0] CNT_num;
  wire [15:0] adder_1_out, \总周期数 ;
  wire [19:0] bit_extender_1_out, bit_extender_4_out, multiplexer_12_out, shifter_1_out;
  wire [31:0] adder_2_out, adder_3_out, alu_1_result, alu_1_result_2, ALUO, bit_extender_2_out, IAddr,
       mEPC_q, mEPC_Ret, mips_ram_1_p7, multiplexer_1_out, multiplexer_2_out, multiplexer_3_out,
       multiplexer_4_out, multiplexer_7_out, multiplexer_13_out, multiplexer_18_out, PCOffset, regifile_1_r1,
       regifile_1_r2;

  Button \u_继续运行  (.out(Go));
  Button _1 ();  // open: out
  Button _2 ();  // open: out
  Button _3 ();  // open: out
  LED #(.active("true")) led_1 (.in(W1));
  LED #(.active("true")) led_2 (.in(W2));
  LED #(.active("true")) led_3 (.in(W3));
  Hex_Digit_Display hex_digit_display_1 (.value(LedData[31:28]));  // open: dp
  Comparator #(.width(16), .mode("twosComplement")) comparator_1 (
    .a(\总周期数 ), .b(16'h7), .eq(comparator_1_eq));  // open: gt, lt
  Comparator #(.width(16), .mode("twosComplement")) comparator_2 (
    .a(\总周期数 ), .b(16'h241), .eq(comparator_2_eq));  // open: gt, lt
  Hex_Digit_Display hex_digit_display_2 (.value(LedData[27:24]));  // open: dp
  Hex_Digit_Display hex_digit_display_3 (.value(LedData[23:20]));  // open: dp
  Comparator #(.width(16), .mode("twosComplement")) comparator_3 (
    .a(16'h258), .b(\总周期数 ), .eq(comparator_3_eq));  // open: gt, lt
  or or_1 (or_1_out, comparator_3_eq, comparator_4_eq);
  Comparator #(.width(16), .mode("twosComplement")) comparator_4 (
    .a(\总周期数 ), .b(16'h1), .eq(comparator_4_eq));  // open: gt, lt
  Comparator #(.width(16), .mode("twosComplement")) comparator_5 (
    .a(\总周期数 ), .b(16'h4), .eq(comparator_5_eq));  // open: gt, lt
  or or_2 (or_2_out, comparator_1_eq, comparator_2_eq);
  Hex_Digit_Display hex_digit_display_4 (.value(LedData[19:16]));  // open: dp
  Hex_Digit_Display hex_digit_display_5 (.value(LedData[15:12]));  // open: dp
  Pull_Resistor #(.pull(0)) pull_resistor_1 (.node(IRA));
  assign IRA = or_1_out ? ~CLK : 1'bz;  // Controlled_Inverter controlled_inverter_1
  Pull_Resistor #(.pull(0)) pull_resistor_2 (.node(IRB));
  assign IRB = comparator_5_eq ? ~CLK : 1'bz;  // Controlled_Inverter controlled_inverter_2
  Pull_Resistor #(.pull(0)) pull_resistor_3 (.node(IRC));
  assign IRC = or_2_out ? ~CLK : 1'bz;  // Controlled_Inverter controlled_inverter_3
  Hex_Digit_Display hex_digit_display_6 (.value(LedData[11:8]));  // open: dp
  Hex_Digit_Display hex_digit_display_7 (.value(LedData[7:4]));  // open: dp
  // Probe on \总周期数 
  Hex_Digit_Display hex_digit_display_8 (.value(LedData[3:0]));  // open: dp
  not not_1 (not_1_out, halt);
  or or_3 (IR1_t, IR1, IRA);
  Register #(.width(16), .trigger("rising"), .Select("low")) \u_周期  (
    .D(adder_1_out), .en(not_1_out), .Q(\总周期数 ), .clk(CLK), .clr(RST));
  or or_4 (or_4_out, Go, and_1_out);
  not not_2 (not_2_out, go_halt);
  or or_5 (IR2_t, IR2, IRB);
  and and_1 (and_1_out, not_2_out, not_3_out);
  not not_3 (not_3_out, halt);
  Multiplexer #(.select(1), .width(32), .disabled("Z"), .enable("false")) multiplexer_1 (
    .in0(multiplexer_3_out), .in1(IAddr), .out(multiplexer_1_out), .sel(or_6_out));
  or or_6 (or_6_out, URET, IRespond);
  Adder #(.width(16)) adder_1 (.a(\总周期数 ), .b(16'h1), .out(adder_1_out));  // open: cin, cout
  Register #(.width(32), .trigger("rising"), .Select("low")) u_PC (
    .D(multiplexer_1_out), .en(or_4_out), .Q(PC), .clk(CLK), .clr(RST));
  or or_7 (IR3_t, IR3, IRC);
  Adder #(.width(32)) adder_2 (.a(PC), .b(PCOffset), .out(adder_2_out));  // open: cin, cout
  Register #(.width(1), .trigger("rising"), .Select("low")) u_Halt (.D(go_halt), .Q(halt), .clk(CLK));  // open: en, clr
  Adder #(.width(32)) adder_3 (.a(PC), .b(32'h4), .out(adder_3_out));  // open: cin, cout
  Multiplexer #(.select(1), .width(32), .disabled("Z"), .enable("false")) multiplexer_2 (
    .in0(adder_2_out), .in1(ALUO), .out(multiplexer_2_out), .sel(JALR));
  Multiplexer #(.select(1), .width(32), .disabled("Z"), .enable("false")) multiplexer_3 (
    .in0(adder_3_out), .in1(multiplexer_2_out), .out(multiplexer_3_out), .sel(PCSrc));
  or or_8 (or_8_out, IRespond, URET);
  ROM #(.addrWidth(10), .dataWidth(32), .Select("high")) rom_1 (.addr(PC[11:2]), .data(IR));
  Register #(.width(2), .trigger("rising"), .Select("low")) Stack_Pointer (
    .D(adder_4_out), .en(or_8_out), .Q(Stack_Pointer_q), .clk(CLK));  // open: clr
  // RiscV_Probe riscv_probe_1: pin names not known; wires that end beside it: IR
  Multiplexer #(.select(1), .width(32), .disabled("Z"), .enable("false")) multiplexer_4 (
    .in0(multiplexer_3_out), .in1(mEPC_Ret), .out(multiplexer_4_out), .sel(URET));
  or or_9 (or_9_out, IRespond, URET);
  Multiplexer #(.select(1), .width(2), .disabled("Z"), .enable("false")) multiplexer_5 (
    .in0(2'b01), .in1(2'b11), .out(multiplexer_5_out), .sel(URET));
  Register #(.width(32), .trigger("rising"), .Select("low")) mEPC (
    .D(multiplexer_4_out), .en(or_9_out), .Q(mEPC_q), .clk(CLK));  // open: clr
  Multiplexer #(.select(1), .width(2), .disabled("Z"), .enable("false")) multiplexer_6 (
    .in0(Stack_Pointer_q), .in1(adder_4_out), .out(multiplexer_6_out), .sel(URET));
  Adder #(.width(2)) adder_4 (.a(Stack_Pointer_q), .b(multiplexer_5_out), .out(adder_4_out));  // open: cin, cout
  Priority_Encoder #(.select(2), .disabled("Z")) priority_encoder_1 (
    .in0(1'b1), .in1(\中断按键参考电路_1_iror ), .in2(\中断按键参考电路_2_iror ), .in3(\中断按键参考电路_3_iror ),
    .out(priority_encoder_1_out));  // open: gs, en_out, en_in
  Multiplexer #(.select(2), .width(32), .disabled("Z"), .enable("false")) multiplexer_7 (
    .in1(32'h30ac), .in2(32'h3158), .in3(32'h3204), .out(multiplexer_7_out), .sel(IREncode));  // open: in0
  \单周期硬布线控制器  \u_单周期硬布线控制器_1  (
    .Funct({IR[30], IR[25], IR[14:12]}), .OP(IR[6:2]), .ALU_OP(\单周期硬布线控制器_1_alu_op ), .MemToReg(MTR),
    .MemWrite(MemWrite), .ALU_SRC(\单周期硬布线控制器_1_alu_src ), .RegWrite(RegWrite), .ecall(ecall), .S_type(SType),
    .Jalr(JALR), .Beq(\单周期硬布线控制器_1_beq ), .JAL(JAL), .Bne(\单周期硬布线控制器_1_bne ), .IR(IR[21]), .uret(URET),
    .Bge(Bge), .sb(sb), .ALT(ALT), .IRE(IRE), .IRD(IRD));  // open: RsUsed, RtUsed, LUI, BLT
  Multiplexer #(.select(1), .width(5), .disabled("Z"), .enable("false")) multiplexer_8 (
    .in0(IR[19:15]), .in1(5'b01010), .out(multiplexer_8_out), .sel(ecall));
  Multiplexer #(.select(1), .width(5), .disabled("Z"), .enable("false")) multiplexer_9 (
    .in0(IR[24:20]), .in1(5'b10001), .out(multiplexer_9_out), .sel(ecall));
  Multiplexer #(.select(1), .width(12), .disabled("Z"), .enable("false")) multiplexer_10 (
    .in0(IR[31:20]), .in1({IR[31:25], IR[11:7]}), .out(multiplexer_10_out), .sel(SType));
  assign bit_extender_1_out = {{8{IR[31]}}, {IR[31], IR[7], IR[30:25], IR[11:8]}};  // Bit_Extender bit_extender_1
  Multiplexer #(.select(1), .width(32), .disabled("Z"), .enable("false")) multiplexer_11 (
    .in0(multiplexer_7_out), .in1(mEPC_q), .out(IAddr), .sel(URET));
  D_Flip_Flop #(.trigger("high"), .Pre_Clr_Positions("LEGACY"), .NegatePresetClear("false"), .enable("true"), .NewFFLayout("false")) d_ff_1 (.Q(d_ff_1_q));  // open: clk, D, Qn, preset, en, reset
  // Probe on 13'h11
  Demultiplexer #(.select(2), .width(1), .tristate("false"), .disabled("Z"), .enable("false")) demultiplexer_1 (
    .out1(demultiplexer_1_out1), .out2(demultiplexer_1_out2), .out3(demultiplexer_1_out3), .in(URET),
    .sel(priority_encoder_1_out));  // open: out0
  assign bit_extender_2_out = {{20{multiplexer_10_out[11]}}, multiplexer_10_out};  // Bit_Extender bit_extender_2
  Multiplexer #(.select(1), .width(20), .disabled("Z"), .enable("false")) multiplexer_12 (
    .in0(bit_extender_1_out), .in1({IR[31], IR[19:12], IR[20], IR[30:21]}), .out(multiplexer_12_out),
    .sel(JAL));
  RAM #(.addrWidth(2), .dataWidth(32), .bus("separate"), .Select("low")) ram_1 (
    .addr(multiplexer_6_out), .din(mEPC_q), .data(mEPC_Ret), .str(IRespond), .clk(CLK), .ld(URET), .clr(RST));  // open: sel
  Comparator #(.width(13), .mode("twosComplement")) comparator_6 (
    .a(CNT_num), .b(13'h11), .eq(comparator_6_eq), .lt(comparator_6_lt));  // open: gt
  Clock #(.highDuration(1), .lowDuration(1)) clock_1 (.out(clock_1_out));
  Regifile regifile_1 (
    .Din(RDin), .Clk(CLK), .R1(regifile_1_r1), .R2(regifile_1_r2), .WE(RegWrite), .W_num(IR[11:7]),
    .R1_num(multiplexer_8_out), .R2_num(multiplexer_9_out));
  or or_10 (or_10_out, JALR, JAL);
  Counter #(.width(13), .max('h1fff), .ongoal("stay"), .trigger("rising"), .behavior("old")) counter_1 (
    .count(comparator_6_lt), .Q(CNT_num), .clk(clock_1_out));  // open: load, D, carry, clr, preset
  \中断按键参考电路  \u_中断按键参考电路_1  (
    .IRO(\中断按键参考电路_1_iro ), .\同步清零信号 (demultiplexer_1_out1), .IR(IR1_t), .IR_Light(W1), .CLK(CLK),
    .IROI(\中断按键参考电路_1_iroi ), .IROI_CLR(demultiplexer_2_out1), .IROR(\中断按键参考电路_1_iror ));
  \中断按键参考电路  \u_中断按键参考电路_2  (
    .IRO(\中断按键参考电路_2_iro ), .\同步清零信号 (demultiplexer_1_out2), .IR(IR2_t), .IR_Light(W2), .CLK(CLK),
    .IROI(\中断按键参考电路_2_iroi ), .IROI_CLR(demultiplexer_2_out2), .IROR(\中断按键参考电路_2_iror ));
  \中断按键参考电路  \u_中断按键参考电路_3  (
    .IRO(\中断按键参考电路_3_iro ), .\同步清零信号 (demultiplexer_1_out3), .IR(IR3_t), .IR_Light(W3), .CLK(CLK),
    .IROI(\中断按键参考电路_3_iroi ), .IROI_CLR(demultiplexer_2_out3), .IROR(\中断按键参考电路_3_iror ));
  Multiplexer #(.select(1), .width(32), .disabled("Z"), .enable("false")) multiplexer_13 (
    .in0(regifile_1_r2), .in1(bit_extender_2_out), .out(multiplexer_13_out), .sel(\单周期硬布线控制器_1_alu_src ));
  Multiplexer #(.select(1), .width(32), .disabled("Z"), .enable("false")) multiplexer_14 (
    .in0(multiplexer_18_out), .in1(adder_3_out), .out(RDin), .sel(or_10_out));
  nand nand_1 (nand_1_out, d_ff_1_q, comparator_6_eq);
  ALU alu_1 (
    .X(regifile_1_r1), .Y(multiplexer_13_out), .AluOP(\单周期硬布线控制器_1_alu_op ), .Equal(alu_1_equal),
    .Result(alu_1_result), .Result_2(alu_1_result_2), .out_4(alu_1_out_4));  // open: out_6
  Shifter #(.width(20), .shift("ll")) shifter_1 (.in(multiplexer_12_out), .\dist (5'b00001), .out(shifter_1_out));
  assign CLK = nand_1_out ? clock_1_out : 1'bz;  // Controlled_Buffer controlled_buffer_1
  Pull_Resistor #(.pull(1)) pull_resistor_4 (.node(CLK));
  Priority_Encoder #(.select(2), .disabled("Z")) priority_encoder_2 (
    .in0(1'b1), .in1(\中断按键参考电路_1_iro ), .in2(\中断按键参考电路_2_iro ), .in3(\中断按键参考电路_3_iro ), .out(IREncode));  // open: gs, en_out, en_in
  not not_4 (not_4_out, alu_1_equal);
  Multiplexer #(.select(2), .width(5), .disabled("Z"), .enable("false")) multiplexer_15 (
    .in0({5{1'b0}}), .in1(5'b01000), .in2(5'b10000), .in3(5'b11000), .out(multiplexer_15_out),
    .sel(alu_1_result[1:0]));
  assign PCOffset = {{12{shifter_1_out[19]}}, shifter_1_out};  // Bit_Extender bit_extender_3
  Demultiplexer #(.select(2), .width(1), .tristate("false"), .disabled(0), .enable("false")) demultiplexer_2 (
    .out1(demultiplexer_2_out1), .out2(demultiplexer_2_out2), .out3(demultiplexer_2_out3), .in(IE),
    .sel(IREncode));  // open: out0
  and and_2 (and_2_out, alu_1_out_4, Bge);
  and and_3 (and_3_out, \单周期硬布线控制器_1_bne , not_4_out);
  Shifter #(.width(32), .shift("ll")) shifter_2 (.in(regifile_1_r2), .\dist (multiplexer_15_out), .out(MDin));
  or or_11 (or_11_out, \中断按键参考电路_1_iroi , \中断按键参考电路_2_iroi , \中断按键参考电路_3_iroi );
  and and_4 (and_4_out, \单周期硬布线控制器_1_beq , alu_1_equal);
  Comparator #(.width(6), .mode("twosComplement")) comparator_7 (
    .a(regifile_1_r2[5:0]), .b(6'b100010), .eq(comparator_7_eq));  // open: gt, lt
  Multiplexer #(.select(1), .width(32), .disabled("Z"), .enable("false")) multiplexer_16 (
    .in0(alu_1_result), .in1(alu_1_result_2), .out(ALUO), .sel(ALT));
  and and_5 (IRespond, or_11_out, IE);
  or or_12 (PCSrc, and_3_out, and_4_out, and_2_out, JAL, JALR);
  Shifter #(.width(4), .shift("ll")) shifter_3 (.in(4'b0001), .\dist (alu_1_result[1:0]), .out(shifter_3_out));
  and and_6 (and_6_out, ecall, comparator_7_eq);
  and and_7 (go_halt, ecall, not_5_out);
  not not_5 (not_5_out, comparator_7_eq);
  Multiplexer #(.select(1), .width(4), .disabled("Z"), .enable("false")) multiplexer_17 (
    .in0(4'b1111), .in1(shifter_3_out), .out(MemSel), .sel(sb));
  not not_6 (not_6_out, IRespond);
  or or_13 (or_13_out, IRD, IRespond, URET, IRE);
  Register #(.width(32), .trigger("rising"), .Select("low")) LED_Register (
    .D(regifile_1_r1), .en(and_6_out), .Q(LedData), .clk(CLK), .clr(RST));
  and and_8 (and_8_out, ~IRD, not_6_out);  // AND_Gate
  Comparator #(.width(16), .mode("twosComplement")) comparator_8 (
    .a(\总周期数 ), .b({16{1'b0}}), .eq(comparator_8_eq));  // open: gt, lt
  Bit_Extender #(.in_width(30), .out_width(20), .\type ("zero")) bit_extender_4 (
    .in(alu_1_result[31:2]), .out(bit_extender_4_out));
  or or_14 (or_14_out, IRE, and_8_out);
  Register #(.width(1), .trigger("rising"), .Select("low")) u_IE (
    .D(or_14_out), .en(or_13_out), .Q(IE), .clk(CLK), .preset(comparator_8_eq));  // open: clr, cs
  // MIPS_RAM mips_ram_1: pin names not known; wires that end beside it: bit_extender_4_out, MDin, MemWrite, MemSel, CLK, RST, mips_ram_1_p7
  Multiplexer #(.select(1), .width(32), .disabled("Z"), .enable("false")) multiplexer_18 (
    .in0(ALUO), .in1(mips_ram_1_p7), .out(multiplexer_18_out), .sel(MTR));

  // Notes on the sheet:
  //   中断源
  //   中断等待指示
  //   总复位信号应将除ROM以外所有存储组件全部清零
  //   多级中断测试信号模拟器
  //   数码管输出
  //   数码管输出应该用寄存器锁存，否则显示数据只能一闪而过
  //   指令存储器
  //   contents of rom_1 (hex, n*v repeats v):
  //   7d000113 100413 1f41993 41f9d993 433 c00913 800b13 140413 f47413 800293 100313 499993 89e9b3 1300533
  //   2200893 73 406282b3 fe0294e3 140413 f00f93 1f47433 1c41413 800293 100313 49d993 89e9b3 1300533
  //   2200893 73 406282b3 fe0294e3 1c45413 406b0b33 b0463 f95ff06f 2b3 fff2c293 1029293 fff2e293 500533
  //   2200893 73 f5dff06f 1112023 410113 a12023 410113 812023 410113 1312023 410113 1412023 410113 1512023
  //   410113 1612023 410113 40e073 100b13 300a13 100a93 1600433 441413 14469b3 1300533 2200893 73 fe0416e3
  //   415a0a33 fe0a10e3 40f073 ffc10113 12b03 ffc10113 12a83 ffc10113 12a03 ffc10113 12983 ffc10113 12403
  //   ffc10113 12503 ffc10113 12883 200073 1112023 410113 a12023 410113 812023 410113 1312023 410113
  //   1412023 410113 1512023 410113 1612023 410113 40e073 200b13 300a13 100a93 1600433 441413 14469b3
  //   1300533 2200893 73 fe0416e3 415a0a33 fe0a10e3 40f073 ffc10113 12b03 ffc10113 12a83 ffc10113 12a03
  //   ffc10113 12983 ffc10113 12403 ffc10113 12503 ffc10113 12883 200073 1112023 410113 a12023 410113
  //   812023 410113 1312023 410113 1412023 410113 1512023 410113 1612023 410113 40e073 300b13 300a13
  //   100a93 1600433 441413 14469b3 1300533 2200893 73 fe0416e3 415a0a33 fe0a10e3 40f073 ffc10113 12b03
  //   ffc10113 12a83 ffc10113 12a03 ffc10113 12983 ffc10113 12403 ffc10113 12503 ffc10113 12883 200073
  //   为方便自动评测，需要输出PC，IR，寄存器堆写如数据RDin
  //   指令探针
  //   RAM写使能MemWrite、RAM写入数据MDin等信号
  //   指令字
  //   JAL
  //   JALR
  //   URET
  //   Bge
  //   BEQ offset
  //   JAL offset
  //   Beq
  //   Bne
  //   MemToReg
  //   MemWrite
  //   AluOP
  //   AluSrcB
  //   RegWrite
  //   S_Type
  //   ecall
  //   rd
  //   控制位
  //   暂停节拍，不能为0
  //   戳工具置1进入计数暂停模式，ctrl+k时钟自动运行到对应节拍暂停
  //   ctrl+k关闭时钟连续运行，将控制位置零，进入单步调试模式调试
  //   可计数暂停的时钟源
  //   Bne Judge
  //   Beq Judge
  //   Bge Judge
endmodule

module \封装正确性测试  (
);

  wire IR1, IR2, IR3, MemW, RegW;
  wire [31:0] IR, LED, MDin, PC, RDin;

  \单周期_多级中断  \u_单周期_多级中断_1  (
    .IR1(IR1), .IR2(IR2), .IR3(IR3), .RegWrite(RegW), .MemWrite(MemW), .CLK(PC[0]), .PC(IR), .IR(RDin),
    .RDin(MDin), .MDin(LED));  // open: LedData
  // Pins of 1 and 32 bits meet at PC

  // Notes on the sheet:
  //   请检查上面封装有无位宽不匹配，引脚标签是否和连接的标签相对应，否则无法在educoder平台上正确测试
  //   单周期+多级中断封装测试
endmodule

module Flow_Register (
  input  [1:0] INForA,
  input  [1:0] INcor,
  input  [4:0] INrd,
  input  [31:0] IN4,
  input  [31:0] IN3,
  input  [31:0] IN2,
  input  [31:0] PC2,
  input  [31:0] PC,
  input  [31:0] IN1,
  input  CLK,
  input  RST,
  input  Flush,
  input  EN,
  output [1:0] OUTForA,
  output [1:0] OUTcor,
  output [4:0] OUTrd,
  output [31:0] OUT4,
  output [31:0] OUT3,
  output [31:0] OUT2,
  output [31:0] PC2_2,
  output [31:0] PC_2,
  output [31:0] OUT1
);

  wire [1:0] multiplexer_1_out, multiplexer_2_out;
  wire [4:0] multiplexer_3_out;
  wire [31:0] multiplexer_4_out, multiplexer_5_out, multiplexer_6_out, multiplexer_7_out, multiplexer_8_out,
       multiplexer_9_out;

  Multiplexer #(.select(1), .width(2), .disabled("Z"), .enable("false")) multiplexer_1 (
    .in0(INForA), .in1(2'b00), .out(multiplexer_1_out), .sel(Flush));
  Multiplexer #(.select(1), .width(2), .disabled("Z"), .enable("false")) multiplexer_2 (
    .in0(INcor), .in1(2'b00), .out(multiplexer_2_out), .sel(Flush));
  Multiplexer #(.select(1), .width(5), .disabled("Z"), .enable("false")) multiplexer_3 (
    .in0(INrd), .in1({5{1'b0}}), .out(multiplexer_3_out), .sel(Flush));
  Multiplexer #(.select(1), .width(32), .disabled("Z"), .enable("false")) multiplexer_4 (
    .in0(IN4), .in1({32{1'b0}}), .out(multiplexer_4_out), .sel(Flush));
  Multiplexer #(.select(1), .width(32), .disabled("Z"), .enable("false")) multiplexer_5 (
    .in0(IN3), .in1({32{1'b0}}), .out(multiplexer_5_out), .sel(Flush));
  Multiplexer #(.select(1), .width(32), .disabled("Z"), .enable("false")) multiplexer_6 (
    .in0(IN2), .in1({32{1'b0}}), .out(multiplexer_6_out), .sel(Flush));
  Multiplexer #(.select(1), .width(32), .disabled("Z"), .enable("false")) multiplexer_7 (
    .in0(PC2), .in1({32{1'b0}}), .out(multiplexer_7_out), .sel(Flush));
  Multiplexer #(.select(1), .width(32), .disabled("Z"), .enable("false")) multiplexer_8 (
    .in0(PC), .in1({32{1'b0}}), .out(multiplexer_8_out), .sel(Flush));
  Multiplexer #(.select(1), .width(32), .disabled("Z"), .enable("false")) multiplexer_9 (
    .in0(IN1), .in1({32{1'b0}}), .out(multiplexer_9_out), .sel(Flush));
  Register #(.width(2), .trigger("rising"), .Select("low")) register_1 (
    .D(multiplexer_1_out), .en(EN), .Q(OUTForA), .clk(CLK), .clr(RST));
  Register #(.width(2), .trigger("rising"), .Select("low")) register_2 (
    .D(multiplexer_2_out), .en(EN), .Q(OUTcor), .clk(CLK), .clr(RST));
  Register #(.width(5), .trigger("rising"), .Select("low")) register_3 (
    .D(multiplexer_3_out), .en(EN), .Q(OUTrd), .clk(CLK), .clr(RST));
  Register #(.width(32), .trigger("rising"), .Select("low")) register_4 (
    .D(multiplexer_4_out), .en(EN), .Q(OUT4), .clk(CLK), .clr(RST));
  Register #(.width(32), .trigger("rising"), .Select("low")) register_5 (
    .D(multiplexer_5_out), .en(EN), .Q(OUT3), .clk(CLK), .clr(RST));
  Register #(.width(32), .trigger("rising"), .Select("low")) register_6 (
    .D(multiplexer_6_out), .en(EN), .Q(OUT2), .clk(CLK), .clr(RST));
  Register #(.width(32), .trigger("rising"), .Select("low")) register_7 (
    .D(multiplexer_7_out), .en(EN), .Q(PC2_2), .clk(CLK), .clr(RST));
  Register #(.width(32), .trigger("rising"), .Select("low")) register_8 (
    .D(multiplexer_8_out), .en(EN), .Q(PC_2), .clk(CLK), .clr(RST));
  Register #(.width(32), .trigger("rising"), .Select("low")) register_9 (
    .D(multiplexer_9_out), .en(EN), .Q(OUT1), .clk(CLK), .clr(RST));
endmodule

module Flow_Register_Bit (
  input  [3:0] ALUOPIN,
  input  IN7,
  input  IN4,
  input  IN3,
  input  IN2,
  input  IN5,
  input  IN6,
  input  IN1,
  input  CLK,
  input  RST,
  input  Flush,
  input  EN,
  output [3:0] ALUOPOut,
  output OUT7,
  output OUT4,
  output OUT3,
  output OUT2,
  output OUT5,
  output OUT6,
  output OUT1
);

  wire multiplexer_2_out, multiplexer_3_out, multiplexer_4_out, multiplexer_5_out, multiplexer_6_out,
       multiplexer_7_out, multiplexer_8_out;
  wire [3:0] multiplexer_1_out;

  Multiplexer #(.select(1), .width(4), .disabled("Z"), .enable("false")) multiplexer_1 (
    .in0(ALUOPIN), .in1(4'b0000), .out(multiplexer_1_out), .sel(Flush));
  Multiplexer #(.select(1), .width(1), .disabled("Z"), .enable("false")) multiplexer_2 (
    .in0(IN7), .in1(1'b0), .out(multiplexer_2_out), .sel(Flush));
  Multiplexer #(.select(1), .width(1), .disabled("Z"), .enable("false")) multiplexer_3 (
    .in0(IN4), .in1(1'b0), .out(multiplexer_3_out), .sel(Flush));
  Multiplexer #(.select(1), .width(1), .disabled("Z"), .enable("false")) multiplexer_4 (
    .in0(IN3), .in1(1'b0), .out(multiplexer_4_out), .sel(Flush));
  Multiplexer #(.select(1), .width(1), .disabled("Z"), .enable("false")) multiplexer_5 (
    .in0(IN2), .in1(1'b0), .out(multiplexer_5_out), .sel(Flush));
  Multiplexer #(.select(1), .width(1), .disabled("Z"), .enable("false")) multiplexer_6 (
    .in0(IN5), .in1(1'b0), .out(multiplexer_6_out), .sel(Flush));
  Multiplexer #(.select(1), .width(1), .disabled("Z"), .enable("false")) multiplexer_7 (
    .in0(IN6), .in1(1'b0), .out(multiplexer_7_out), .sel(Flush));
  Multiplexer #(.select(1), .width(1), .disabled("Z"), .enable("false")) multiplexer_8 (
    .in0(IN1), .in1(1'b0), .out(multiplexer_8_out), .sel(Flush));
  Register #(.width(4), .trigger("rising"), .Select("low")) register_1 (
    .D(multiplexer_1_out), .en(EN), .Q(ALUOPOut), .clk(CLK), .clr(RST));
  Register #(.width(1), .trigger("rising"), .Select("low")) register_2 (
    .D(multiplexer_2_out), .en(EN), .Q(OUT7), .clk(CLK), .clr(RST));
  Register #(.width(1), .trigger("rising"), .Select("low")) register_3 (
    .D(multiplexer_3_out), .en(EN), .Q(OUT4), .clk(CLK), .clr(RST));
  Register #(.width(1), .trigger("rising"), .Select("low")) register_4 (
    .D(multiplexer_4_out), .en(EN), .Q(OUT3), .clk(CLK), .clr(RST));
  Register #(.width(1), .trigger("rising"), .Select("low")) register_5 (
    .D(multiplexer_5_out), .en(EN), .Q(OUT2), .clk(CLK), .clr(RST));
  Register #(.width(1), .trigger("rising"), .Select("low")) register_6 (
    .D(multiplexer_6_out), .en(EN), .Q(OUT5), .clk(CLK), .clr(RST));
  Register #(.width(1), .trigger("rising"), .Select("low")) register_7 (
    .D(multiplexer_7_out), .en(EN), .Q(OUT6), .clk(CLK), .clr(RST));
  Register #(.width(1), .trigger("rising"), .Select("low")) register_8 (
    .D(multiplexer_8_out), .en(EN), .Q(OUT1), .clk(CLK), .clr(RST));
endmodule

module Fowarding_Logic (
  input  Ex_MemRead,
  input  PCSrc,
  input  RsUsed,
  input  RtUsed,
  input  [4:0] Rs,
  input  Ex_RegWrite,
  input  [4:0] Rt,
  input  MEM_RegWrite,
  input  [4:0] ExAddr,
  input  [4:0] MEMAddr,
  output Stall,
  output Flush,
  output [1:0] RsForward,
  output [1:0] RtForward
);

  wire and_1_out, and_2_out, and_3_out, and_4_out, and_5_out, and_6_out, comparator_1_eq, comparator_2_eq,
       comparator_3_eq, comparator_4_eq, comparator_5_eq, comparator_6_eq, loaduse_1_datahazzard, not_1_out,
       not_2_out;
  wire [1:0] and_7_out, and_9_out;

  Comparator #(.width(5), .mode("unsigned")) comparator_1 (
    .a(Rs), .b({5{1'b0}}), .eq(comparator_1_eq));  // open: gt, lt
  not not_1 (not_1_out, comparator_1_eq);
  not not_2 (not_2_out, comparator_2_eq);
  Comparator #(.width(5), .mode("unsigned")) comparator_2 (
    .a(Rt), .b({5{1'b0}}), .eq(comparator_2_eq));  // open: gt, lt
  Comparator #(.width(5), .mode("unsigned")) comparator_3 (.a(Rs), .b(ExAddr), .eq(comparator_3_eq));  // open: gt, lt
  Comparator #(.width(5), .mode("unsigned")) comparator_4 (.a(Rt), .b(MEMAddr), .eq(comparator_4_eq));  // open: gt, lt
  Comparator #(.width(5), .mode("unsigned")) comparator_5 (.a(Rs), .b(MEMAddr), .eq(comparator_5_eq));  // open: gt, lt
  Comparator #(.width(5), .mode("unsigned")) comparator_6 (.a(Rt), .b(ExAddr), .eq(comparator_6_eq));  // open: gt, lt
  LoadUse loaduse_1 (
    .RsUsed(RsUsed), .RtUsed(RtUsed), .Rsnz(not_1_out), .Rtnz(not_2_out), .Rseq(comparator_3_eq),
    .Rteq(comparator_6_eq), .ExMemRead(Ex_MemRead), .DataHazzard(loaduse_1_datahazzard));
  and and_1 (and_1_out, RsUsed, not_1_out);
  and and_2 (and_2_out, Ex_RegWrite, comparator_3_eq);
  and and_3 (and_3_out, MEM_RegWrite, comparator_5_eq);
  and and_4 (and_4_out, RtUsed, not_2_out);
  and and_5 (and_5_out, Ex_RegWrite, comparator_6_eq);
  and and_6 (and_6_out, MEM_RegWrite, comparator_4_eq);
  not not_3 (Stall, loaduse_1_datahazzard);
  and and_7 (and_7_out[0], and_1_out, and_2_out);
  and and_8 (and_7_out[1], and_1_out, and_3_out);
  and and_9 (and_9_out[0], and_4_out, and_5_out);
  and and_10 (and_9_out[1], and_4_out, and_6_out);
  or or_1 (Flush, PCSrc, loaduse_1_datahazzard);
  Multiplexer #(.select(2), .width(2), .disabled("Z"), .enable("false")) multiplexer_1 (
    .in0(2'b00), .in1(2'b10), .in2(2'b01), .in3(2'b10), .out(RsForward), .sel(and_7_out));
  Multiplexer #(.select(2), .width(2), .disabled("Z"), .enable("false")) multiplexer_2 (
    .in0(2'b00), .in1(2'b10), .in2(2'b01), .in3(2'b10), .out(RtForward), .sel(and_9_out));

  // Notes on the sheet:
  //   LoadUse
endmodule

module LoadUse (
  input  RsUsed,
  input  RtUsed,
  input  Rsnz,
  input  Rtnz,
  input  Rseq,
  input  Rteq,
  input  ExMemRead,
  output DataHazzard
);

  wire and_1_out, and_2_out;

  and and_1 (and_1_out, RsUsed, Rsnz, ExMemRead, Rseq);
  and and_2 (and_2_out, RtUsed, Rtnz, ExMemRead, Rteq);
  or or_1 (DataHazzard, and_1_out, and_2_out);
endmodule

module LED_Register (
  input  [31:0] IN,
  input  EN,
  input  [4:0] LINE,
  input  CLK,
  output [31:0] o1,
  output [31:0] o2,
  output [31:0] o3,
  output [31:0] o4,
  output [31:0] o5,
  output [31:0] o6,
  output [31:0] o7,
  output [31:0] o8,
  output [31:0] o9,
  output [31:0] o10,
  output [31:0] o11,
  output [31:0] o12,
  output [31:0] o13,
  output [31:0] o14,
  output [31:0] o15,
  output [31:0] o16,
  output [31:0] o17,
  output [31:0] o18,
  output [31:0] o19,
  output [31:0] o20,
  output [31:0] o21,
  output [31:0] o22,
  output [31:0] o23,
  output [31:0] o24,
  output [31:0] o25,
  output [31:0] o26,
  output [31:0] o27,
  output [31:0] o28,
  output [31:0] o29,
  output [31:0] o30,
  output [31:0] o31,
  output [31:0] o32
);

  wire demultiplexer_1_out0, demultiplexer_1_out1, demultiplexer_1_out2, demultiplexer_1_out3,
       demultiplexer_1_out4, demultiplexer_1_out5, demultiplexer_1_out6, demultiplexer_1_out7,
       demultiplexer_1_out8, demultiplexer_1_out9, demultiplexer_1_out10, demultiplexer_1_out11,
       demultiplexer_1_out12, demultiplexer_1_out13, demultiplexer_1_out14, demultiplexer_1_out15,
       demultiplexer_1_out16, demultiplexer_1_out17, demultiplexer_1_out18, demultiplexer_1_out19,
       demultiplexer_1_out20, demultiplexer_1_out21, demultiplexer_1_out22, demultiplexer_1_out23,
       demultiplexer_1_out24, demultiplexer_1_out25, demultiplexer_1_out26, demultiplexer_1_out27,
       demultiplexer_1_out28, demultiplexer_1_out29, demultiplexer_1_out30, demultiplexer_1_out31;

  Demultiplexer #(.select(5), .width(1), .tristate("false"), .disabled("Z"), .enable("false")) demultiplexer_1 (
    .out0(demultiplexer_1_out0), .out1(demultiplexer_1_out1), .out2(demultiplexer_1_out2),
    .out3(demultiplexer_1_out3), .out4(demultiplexer_1_out4), .out5(demultiplexer_1_out5),
    .out6(demultiplexer_1_out6), .out7(demultiplexer_1_out7), .out8(demultiplexer_1_out8),
    .out9(demultiplexer_1_out9), .out10(demultiplexer_1_out10), .out11(demultiplexer_1_out11),
    .out12(demultiplexer_1_out12), .out13(demultiplexer_1_out13), .out14(demultiplexer_1_out14),
    .out15(demultiplexer_1_out15), .out16(demultiplexer_1_out16), .out17(demultiplexer_1_out17),
    .out18(demultiplexer_1_out18), .out19(demultiplexer_1_out19), .out20(demultiplexer_1_out20),
    .out21(demultiplexer_1_out21), .out22(demultiplexer_1_out22), .out23(demultiplexer_1_out23),
    .out24(demultiplexer_1_out24), .out25(demultiplexer_1_out25), .out26(demultiplexer_1_out26),
    .out27(demultiplexer_1_out27), .out28(demultiplexer_1_out28), .out29(demultiplexer_1_out29),
    .out30(demultiplexer_1_out30), .out31(demultiplexer_1_out31), .in(EN), .sel(LINE));
  Register #(.width(32), .trigger("rising"), .Select("low")) register_1 (
    .D(IN), .en(demultiplexer_1_out0), .Q(o1), .clk(CLK));  // open: clr
  Register #(.width(32), .trigger("rising"), .Select("low")) register_2 (
    .D(IN), .en(demultiplexer_1_out1), .Q(o2), .clk(CLK));  // open: clr
  Register #(.width(32), .trigger("rising"), .Select("low")) register_3 (
    .D(IN), .en(demultiplexer_1_out2), .Q(o3), .clk(CLK));  // open: clr
  Register #(.width(32), .trigger("rising"), .Select("low")) register_4 (
    .D(IN), .en(demultiplexer_1_out3), .Q(o4), .clk(CLK));  // open: clr
  Register #(.width(32), .trigger("rising"), .Select("low")) register_5 (
    .D(IN), .en(demultiplexer_1_out4), .Q(o5), .clk(CLK));  // open: clr
  Register #(.width(32), .trigger("rising"), .Select("low")) register_6 (
    .D(IN), .en(demultiplexer_1_out5), .Q(o6), .clk(CLK));  // open: clr
  Register #(.width(32), .trigger("rising"), .Select("low")) register_7 (
    .D(IN), .en(demultiplexer_1_out6), .Q(o7), .clk(CLK));  // open: clr
  Register #(.width(32), .trigger("rising"), .Select("low")) register_8 (
    .D(IN), .en(demultiplexer_1_out7), .Q(o8), .clk(CLK));  // open: clr
  Register #(.width(32), .trigger("rising"), .Select("low")) register_9 (
    .D(IN), .en(demultiplexer_1_out8), .Q(o9), .clk(CLK));  // open: clr
  Register #(.width(32), .trigger("rising"), .Select("low")) register_10 (
    .D(IN), .en(demultiplexer_1_out9), .Q(o10), .clk(CLK));  // open: clr
  Register #(.width(32), .trigger("rising"), .Select("low")) register_11 (
    .D(IN), .en(demultiplexer_1_out10), .Q(o11), .clk(CLK));  // open: clr
  Register #(.width(32), .trigger("rising"), .Select("low")) register_12 (
    .D(IN), .en(demultiplexer_1_out11), .Q(o12), .clk(CLK));  // open: clr
  Register #(.width(32), .trigger("rising"), .Select("low")) register_13 (
    .D(IN), .en(demultiplexer_1_out12), .Q(o13), .clk(CLK));  // open: clr
  Register #(.width(32), .trigger("rising"), .Select("low")) register_14 (
    .D(IN), .en(demultiplexer_1_out13), .Q(o14), .clk(CLK));  // open: clr
  Register #(.width(32), .trigger("rising"), .Select("low")) register_15 (
    .D(IN), .en(demultiplexer_1_out14), .Q(o15), .clk(CLK));  // open: clr
  Register #(.width(32), .trigger("rising"), .Select("low")) register_16 (
    .D(IN), .en(demultiplexer_1_out15), .Q(o16), .clk(CLK));  // open: clr
  Register #(.width(32), .trigger("rising"), .Select("low")) register_17 (
    .D(IN), .en(demultiplexer_1_out16), .Q(o17), .clk(CLK));  // open: clr
  Register #(.width(32), .trigger("rising"), .Select("low")) register_18 (
    .D(IN), .en(demultiplexer_1_out17), .Q(o18), .clk(CLK));  // open: clr
  Register #(.width(32), .trigger("rising"), .Select("low")) register_19 (
    .D(IN), .en(demultiplexer_1_out18), .Q(o19), .clk(CLK));  // open: clr
  Register #(.width(32), .trigger("rising"), .Select("low")) register_20 (
    .D(IN), .en(demultiplexer_1_out19), .Q(o20), .clk(CLK));  // open: clr
  Register #(.width(32), .trigger("rising"), .Select("low")) register_21 (
    .D(IN), .en(demultiplexer_1_out20), .Q(o21), .clk(CLK));  // open: clr
  Register #(.width(32), .trigger("rising"), .Select("low")) register_22 (
    .D(IN), .en(demultiplexer_1_out21), .Q(o22), .clk(CLK));  // open: clr
  Register #(.width(32), .trigger("rising"), .Select("low")) register_23 (
    .D(IN), .en(demultiplexer_1_out22), .Q(o23), .clk(CLK));  // open: clr
  Register #(.width(32), .trigger("rising"), .Select("low")) register_24 (
    .D(IN), .en(demultiplexer_1_out23), .Q(o24), .clk(CLK));  // open: clr
  Register #(.width(32), .trigger("rising"), .Select("low")) register_25 (
    .D(IN), .en(demultiplexer_1_out24), .Q(o25), .clk(CLK));  // open: clr
  Register #(.width(32), .trigger("rising"), .Select("low")) register_26 (
    .D(IN), .en(demultiplexer_1_out25), .Q(o26), .clk(CLK));  // open: clr
  Register #(.width(32), .trigger("rising"), .Select("low")) register_27 (
    .D(IN), .en(demultiplexer_1_out26), .Q(o27), .clk(CLK));  // open: clr
  Register #(.width(32), .trigger("rising"), .Select("low")) register_28 (
    .D(IN), .en(demultiplexer_1_out27), .Q(o28), .clk(CLK));  // open: clr
  Register #(.width(32), .trigger("rising"), .Select("low")) register_29 (
    .D(IN), .en(demultiplexer_1_out28), .Q(o29), .clk(CLK));  // open: clr
  Register #(.width(32), .trigger("rising"), .Select("low")) register_30 (
    .D(IN), .en(demultiplexer_1_out29), .Q(o30), .clk(CLK));  // open: clr
  Register #(.width(32), .trigger("rising"), .Select("low")) register_31 (
    .D(IN), .en(demultiplexer_1_out30), .Q(o31), .clk(CLK));  // open: clr
  Register #(.width(32), .trigger("rising"), .Select("low")) register_32 (
    .D(IN), .en(demultiplexer_1_out31), .Q(o32), .clk(CLK));  // open: clr
endmodule

module Snake_Game (
);

  wire D, L, priority_encoder_1_gs, R, U, \单周期_单级中断_1_clk , \单周期_单级中断_1_ledgo ;
  wire [1:0] priority_encoder_1_out, register_1_q;
  wire [3:0] \单周期_单级中断_1_leddata , \单周期_单级中断_1_leddata_2 , \单周期_单级中断_1_leddata_3 , \单周期_单级中断_1_leddata_4 ,
       \单周期_单级中断_1_leddata_5 , \单周期_单级中断_1_leddata_6 , \单周期_单级中断_1_leddata_7 , \单周期_单级中断_1_leddata_8 ;
  wire [4:0] adder_1_out, register_2_q;
  wire [31:0] bit_extender_1_out, led_register_1_o1, led_register_1_o2, led_register_1_o3, led_register_1_o4,
       led_register_1_o5, led_register_1_o6, led_register_1_o7, led_register_1_o8, led_register_1_o9,
       led_register_1_o10, led_register_1_o11, led_register_1_o12, led_register_1_o13, led_register_1_o14,
       led_register_1_o15, led_register_1_o16, led_register_1_o17, led_register_1_o18, led_register_1_o19,
       led_register_1_o20, led_register_1_o21, led_register_1_o22, led_register_1_o23, led_register_1_o24,
       led_register_1_o25, led_register_1_o26, led_register_1_o27, led_register_1_o28, led_register_1_o29,
       led_register_1_o30, led_register_1_o31, led_register_1_o32, \单周期_单级中断_1_ledout ;

  Priority_Encoder #(.select(2), .disabled("Z")) priority_encoder_1 (
    .in0(L), .in1(D), .in2(U), .in3(R), .out(priority_encoder_1_out), .gs(priority_encoder_1_gs));  // open: en_out, en_in
  Register #(.width(2), .trigger("high"), .Select("low")) register_1 (
    .D(priority_encoder_1_out), .en(priority_encoder_1_gs), .Q(register_1_q), .clk(1'b1));  // open: clr
  assign bit_extender_1_out = {{30{1'b0}}, register_1_q};  // Bit_Extender bit_extender_1
  \单周期_单级中断  \u_单周期_单级中断_1  (
    .IR1(priority_encoder_1_gs), .CLK(\单周期_单级中断_1_clk ), .LEDGO(\单周期_单级中断_1_ledgo ),
    .Dir(bit_extender_1_out), .LEDOUT(\单周期_单级中断_1_ledout ),
    .LedData({\单周期_单级中断_1_leddata_8 , \单周期_单级中断_1_leddata_7 , \单周期_单级中断_1_leddata_6 , \单周期_单级中断_1_leddata_5 , \单周期_单级中断_1_leddata_4 , \单周期_单级中断_1_leddata_3 , \单周期_单级中断_1_leddata_2 , \单周期_单级中断_1_leddata }));  // open: IR3, IR2
  Register #(.width(5), .trigger("rising"), .Select("low")) register_2 (
    .D(adder_1_out), .en(\单周期_单级中断_1_ledgo ), .Q(register_2_q), .clk(\单周期_单级中断_1_clk ));  // open: clr
  Adder #(.width(5)) adder_1 (.a(register_2_q), .b(5'b00001), .out(adder_1_out));  // open: cin, cout
  LED_Register led_register_1 (
    .IN(\单周期_单级中断_1_ledout ), .EN(\单周期_单级中断_1_ledgo ), .LINE(register_2_q), .CLK(\单周期_单级中断_1_clk ),
    .o1(led_register_1_o1), .o2(led_register_1_o2), .o3(led_register_1_o3), .o4(led_register_1_o4),
    .o5(led_register_1_o5), .o6(led_register_1_o6), .o7(led_register_1_o7), .o8(led_register_1_o8),
    .o9(led_register_1_o9), .o10(led_register_1_o10), .o11(led_register_1_o11), .o12(led_register_1_o12),
    .o13(led_register_1_o13), .o14(led_register_1_o14), .o15(led_register_1_o15), .o16(led_register_1_o16),
    .o17(led_register_1_o17), .o18(led_register_1_o18), .o19(led_register_1_o19), .o20(led_register_1_o20),
    .o21(led_register_1_o21), .o22(led_register_1_o22), .o23(led_register_1_o23), .o24(led_register_1_o24),
    .o25(led_register_1_o25), .o26(led_register_1_o26), .o27(led_register_1_o27), .o28(led_register_1_o28),
    .o29(led_register_1_o29), .o30(led_register_1_o30), .o31(led_register_1_o31), .o32(led_register_1_o32));
  Hex_Digit_Display hex_digit_display_1 (.value(\单周期_单级中断_1_leddata_8 ));  // open: dp
  Hex_Digit_Display hex_digit_display_2 (.value(\单周期_单级中断_1_leddata_6 ));  // open: dp
  Hex_Digit_Display hex_digit_display_3 (.value(\单周期_单级中断_1_leddata_7 ));  // open: dp
  DotMatrix #(.inputtype("row"), .matrixcols(32), .matrixrows(32), .persist(0), .dotshape("square")) dotmatrix_1 (
    .row0(led_register_1_o1), .row1(led_register_1_o2), .row2(led_register_1_o3), .row3(led_register_1_o4),
    .row4(led_register_1_o5), .row5(led_register_1_o6), .row6(led_register_1_o7), .row7(led_register_1_o8),
    .row8(led_register_1_o9), .row9(led_register_1_o10), .row10(led_register_1_o11),
    .row11(led_register_1_o12), .row12(led_register_1_o13), .row13(led_register_1_o14),
    .row14(led_register_1_o15), .row15(led_register_1_o16), .row16(led_register_1_o17),
    .row17(led_register_1_o18), .row18(led_register_1_o19), .row19(led_register_1_o20),
    .row20(led_register_1_o21), .row21(led_register_1_o22), .row22(led_register_1_o23),
    .row23(led_register_1_o24), .row24(led_register_1_o25), .row25(led_register_1_o26),
    .row26(led_register_1_o27), .row27(led_register_1_o28), .row28(led_register_1_o29),
    .row29(led_register_1_o30), .row30(led_register_1_o31), .row31(led_register_1_o32));
  Hex_Digit_Display hex_digit_display_4 (.value(\单周期_单级中断_1_leddata_5 ));  // open: dp
  Hex_Digit_Display hex_digit_display_5 (.value(\单周期_单级中断_1_leddata_4 ));  // open: dp
  Hex_Digit_Display hex_digit_display_6 (.value(\单周期_单级中断_1_leddata_2 ));  // open: dp
  Hex_Digit_Display hex_digit_display_7 (.value(\单周期_单级中断_1_leddata_3 ));  // open: dp
  Hex_Digit_Display hex_digit_display_8 (.value(\单周期_单级中断_1_leddata ));  // open: dp
  Button button_1 (.out(L));
  Button button_2 (.out(U));
  Button button_3 (.out(R));
  Button button_4 (.out(D));

  // Notes on the sheet:
  //   数码管输出
endmodule
